// Digital circuit FROMTRUTH4.dig as structural Verilog
module FROMTRUTH4 (
  input  op6,
  input  op5,
  input  op4,
  input  op3,
  input  op2,
  input  f3_2,
  input  f31,
  input  f30,
  input  f730,
  input  inst21,
  input  inst20,
  output RegW,
  output ASel1,
  output ASel0,
  output BSel,
  output MemW,
  output MemR,
  output WBSel1,
  output WBSel0,
  output Br,
  output Jmp,
  output CSRW,
  output CSRS,
  output ALUAdd,
  output immI,
  output immS,
  output immSB,
  output immU,
  output immUJ,
  output ramB,
  output ramH,
  output ld_sext,
  output ecall_sel,
  output mretsel,
  output ebreak_sel,
  output dretsel,
  output CSR_OP_WRITE,
  output CSR_OP_SET,
  output CSR_OP_CLEAR,
  output CSR_USE_IMM
);

  wire and_1_out, and_2_out, and_3_out, and_4_out, and_5_out, and_6_out, and_8_out, and_9_out, and_10_out,
       and_11_out, and_12_out, and_13_out, and_14_out, and_15_out, and_18_out, and_19_out, and_20_out,
       and_21_out, and_22_out, and_23_out, and_24_out, and_25_out, and_28_out, and_29_out, and_30_out,
       and_32_out, and_33_out, and_34_out, and_35_out, and_36_out, and_41_out, and_42_out, and_43_out,
       and_44_out, and_53_out, and_54_out, not_1_out, not_2_out, not_3_out, not_4_out, not_5_out, not_6_out,
       not_7_out, not_8_out, not_9_out, not_10_out, not_11_out;

  not not_1 (not_1_out, op6);
  not not_2 (not_2_out, op5);
  not not_3 (not_3_out, op4);
  not not_4 (not_4_out, op3);
  not not_5 (not_5_out, op2);
  not not_6 (not_6_out, f3_2);
  not not_7 (not_7_out, f31);
  not not_8 (not_8_out, f30);
  not not_9 (not_9_out, f730);
  not not_10 (not_10_out, inst21);
  not not_11 (not_11_out, inst20);
  and and_1 (and_1_out, f30, not_5_out, not_4_out, op4, op5);
  and and_2 (and_2_out, f31, not_5_out, not_4_out, op4, op5);
  and and_3 (and_3_out, f3_2, not_5_out, not_4_out, op4, op5);
  and and_4 (and_4_out, not_5_out, not_4_out, not_2_out, not_1_out);
  and and_5 (and_5_out, op2, not_3_out, op5, op6);
  and and_6 (and_6_out, not_4_out, op4, not_1_out);
  and and_7 (ASel1, op2, not_4_out, op4, op5, not_1_out);
  and and_8 (and_8_out, f30, f31, f3_2, f730, not_5_out, not_4_out, not_3_out, op5, op6);
  and and_9 (and_9_out, op2, not_4_out, op4, not_2_out, not_1_out);
  and and_10 (and_10_out, op2, op3, not_3_out, op5, op6);
  and and_11 (and_11_out, f3_2, not_5_out, not_4_out, op5, op6);
  and and_12 (and_12_out, not_5_out, not_4_out, not_3_out, op5);
  and and_13 (and_13_out, op2, not_4_out, op4, not_1_out);
  and and_14 (and_14_out, not_5_out, not_4_out, not_2_out, not_1_out);
  and and_15 (and_15_out, op2, not_3_out, op5, op6);
  and and_16 (MemW, not_5_out, not_4_out, not_3_out, op5, not_1_out);
  and and_17 (MemR, not_5_out, not_4_out, not_3_out, not_2_out, not_1_out);
  and and_18 (and_18_out, f30, not_5_out, not_4_out, op4, op5, op6);
  and and_19 (and_19_out, f31, not_5_out, not_4_out, op4, op5, op6);
  and and_20 (and_20_out, f3_2, not_5_out, not_4_out, op4, op5, op6);
  and and_21 (and_21_out, not_5_out, not_4_out, not_3_out, not_2_out, not_1_out);
  and and_22 (and_22_out, f30, not_5_out, not_4_out, op4, op5, op6);
  and and_23 (and_23_out, f31, not_5_out, not_4_out, op4, op5, op6);
  and and_24 (and_24_out, f3_2, not_5_out, not_4_out, op4, op5, op6);
  and and_25 (and_25_out, op2, not_3_out, op5, op6);
  and and_26 (Br, not_5_out, not_4_out, not_3_out, op5, op6);
  and and_27 (Jmp, op2, not_3_out, op5, op6);
  and and_28 (and_28_out, f30, not_5_out, not_4_out, op4, op5, op6);
  and and_29 (and_29_out, f31, not_5_out, not_4_out, op4, op5, op6);
  and and_30 (and_30_out, f3_2, not_5_out, not_4_out, op4, op5, op6);
  and and_31 (CSRS, f3_2, not_5_out, not_4_out, op4, op5, op6);
  and and_32 (and_32_out, not_5_out, not_4_out, not_3_out, not_1_out);
  and and_33 (and_33_out, op2, not_4_out, op4, not_1_out);
  and and_34 (and_34_out, op2, not_3_out, op5, op6);
  and and_35 (and_35_out, op2, not_4_out, not_3_out, op5, op6);
  and and_36 (and_36_out, not_5_out, not_4_out, not_2_out, not_1_out);
  and and_37 (immS, not_5_out, not_4_out, not_3_out, op5, not_1_out);
  and and_38 (immSB, not_5_out, not_4_out, not_3_out, op5, op6);
  and and_39 (immU, op2, not_4_out, op4, not_1_out);
  and and_40 (immUJ, op2, op3, not_3_out, op5, op6);
  and and_41 (and_41_out, not_8_out, not_7_out, not_6_out, not_5_out, not_4_out, not_3_out, not_1_out);
  and and_42 (and_42_out, not_8_out, not_7_out, not_5_out, not_4_out, not_3_out, not_2_out, not_1_out);
  and and_43 (and_43_out, f30, not_7_out, not_6_out, not_5_out, not_4_out, not_3_out, not_1_out);
  and and_44 (and_44_out, f30, not_7_out, not_5_out, not_4_out, not_3_out, not_2_out, not_1_out);
  and and_45 (ld_sext, not_6_out, not_5_out, not_4_out, not_3_out, not_2_out, not_1_out);
  and and_46 (ecall_sel, not_8_out, not_7_out, not_6_out, not_9_out, not_11_out, not_10_out, not_5_out, not_4_out, op4, op5, op6);
  and and_47 (mretsel, not_8_out, not_7_out, not_6_out, not_9_out, not_11_out, inst21, not_5_out, not_4_out, op4, op5, op6);
  and and_48 (ebreak_sel, not_8_out, not_7_out, not_6_out, not_9_out, inst20, not_10_out, not_5_out, not_4_out, op4, op5, op6);
  and and_49 (dretsel, not_8_out, not_7_out, not_6_out, f730, not_11_out, inst21, not_5_out, not_4_out, op4, op5, op6);
  and and_50 (CSR_OP_WRITE, f30, not_7_out, not_5_out, not_4_out, op4, op5, op6);
  and and_51 (CSR_OP_SET, not_8_out, f31, not_5_out, not_4_out, op4, op5, op6);
  and and_52 (CSR_OP_CLEAR, f30, f31, not_5_out, not_4_out, op4, op5, op6);
  and and_53 (and_53_out, f30, f3_2, not_5_out, not_4_out, op4, op5, op6);
  and and_54 (and_54_out, f31, f3_2, not_5_out, not_4_out, op4, op5, op6);
  or or_1 (ASel0, and_8_out, and_9_out, and_10_out);
  or or_2 (CSRW, and_28_out, and_29_out, and_30_out);
  or or_3 (ALUAdd, and_32_out, and_33_out, and_34_out);
  or or_4 (immI, and_35_out, and_36_out);
  or or_5 (ramB, and_41_out, and_42_out);
  or or_6 (ramH, and_43_out, and_44_out);
  or or_7 (CSR_USE_IMM, and_53_out, and_54_out);
  or or_8 (RegW, and_1_out, and_2_out, and_3_out, and_4_out, and_5_out, and_6_out);
  or or_9 (BSel, and_11_out, and_12_out, and_13_out, and_14_out, and_15_out);
  or or_10 (WBSel1, and_18_out, and_19_out, and_20_out, and_21_out);
  or or_11 (WBSel0, and_22_out, and_23_out, and_24_out, and_25_out);
endmodule
