// Digital circuit FROMTRUTH5.dig as structural Verilog
module FROMTRUTH5 (
  input  op6,
  input  op5,
  input  op4,
  input  op3,
  input  op2,
  input  f3_2,
  input  f31,
  input  f30,
  input  f730,
  input  inst21,
  input  inst20,
  output wb_sel_1,
  output wb_sel_0,
  output ram_wen,
  output ram_ren,
  output reg_wen,
  output branch_sel,
  output jal_sel,
  output jalr_sel,
  output alu_asel_1,
  output alu_asel_0,
  output alu_bsel,
  output imm_sel_2,
  output imm_sel_1,
  output imm_sel_0,
  output alu_op_class_1,
  output alu_op_class_0,
  output alu_op_2,
  output alu_op_1,
  output alu_op_0,
  output alu_mod,
  output ram_b,
  output ram_h,
  output ld_signext,
  output csr_wen,
  output csr_opset,
  output csr_opclear,
  output csr_useimm,
  output ecall_sel,
  output ebreak_sel,
  output mret_sel
);

  wire and_1_out, and_2_out, and_3_out, and_4_out, and_5_out, and_6_out, and_7_out, and_8_out, and_9_out,
       and_10_out, and_11_out, and_12_out, and_13_out, and_14_out, and_15_out, and_16_out, and_17_out,
       and_18_out, and_19_out, and_20_out, and_21_out, and_22_out, and_23_out, and_24_out, and_25_out,
       and_26_out, and_27_out, and_28_out, and_29_out, and_30_out, and_31_out, and_32_out, and_33_out,
       and_34_out, and_35_out, and_36_out, and_37_out, and_38_out, and_39_out, and_40_out, and_41_out,
       and_42_out, and_43_out, and_44_out, and_45_out, and_46_out, and_47_out, and_48_out, and_49_out,
       and_50_out, and_51_out, and_52_out, and_53_out, and_54_out, and_55_out, and_56_out, and_57_out,
       and_58_out, and_59_out, and_60_out, and_61_out, and_62_out, and_63_out, and_64_out, and_65_out,
       and_66_out, and_67_out, and_68_out, and_69_out, and_70_out, and_71_out, and_72_out, and_73_out,
       and_74_out, and_75_out, and_76_out, and_77_out, and_78_out, and_79_out, and_80_out, and_81_out,
       and_84_out, and_85_out, and_86_out, and_87_out, and_88_out, and_89_out, and_90_out, and_91_out,
       and_92_out, and_95_out, and_96_out, and_97_out, and_98_out, and_99_out, and_100_out, and_101_out,
       and_102_out, and_103_out, and_104_out, and_105_out, and_106_out, and_107_out, and_108_out,
       and_109_out, and_110_out, and_111_out, and_112_out, and_113_out, and_114_out, and_115_out,
       and_116_out, and_117_out, and_118_out, and_119_out, and_120_out, and_121_out, and_122_out,
       and_123_out, and_124_out, and_125_out, and_126_out, and_127_out, and_128_out, and_129_out,
       and_130_out, and_131_out, and_132_out, and_133_out, and_134_out, and_135_out, and_136_out,
       and_138_out, and_139_out, and_140_out, and_141_out, and_142_out, and_143_out, and_144_out,
       and_145_out, and_146_out, and_147_out, and_148_out, and_149_out, and_150_out, and_151_out,
       and_152_out, and_153_out, and_154_out, and_155_out, and_156_out, and_157_out, and_158_out,
       and_159_out, and_160_out, and_161_out, and_162_out, and_165_out, and_166_out, and_167_out,
       and_172_out, and_173_out, and_175_out, and_176_out, and_177_out, and_178_out, and_182_out,
       and_183_out, and_184_out, and_185_out, and_186_out, and_187_out, and_188_out, and_189_out,
       and_190_out, not_1_out, not_2_out, not_3_out, not_4_out, not_5_out, not_7_out, not_8_out, not_9_out,
       not_10_out, or_1_out, or_2_out, or_3_out, or_5_out, or_6_out, or_7_out, or_8_out, or_9_out, or_10_out,
       or_15_out, or_16_out, or_19_out;

  not not_1 (not_1_out, op6);
  not not_2 (not_2_out, op5);
  not not_3 (not_3_out, op4);
  not not_4 (not_4_out, op3);
  not not_5 (not_5_out, op2);
  not not_6 (ld_signext, f3_2);
  not not_7 (not_7_out, f31);
  not not_8 (not_8_out, f30);
  not not_9 (not_9_out, inst21);
  not not_10 (not_10_out, inst20);
  and and_1 (and_1_out, f30, not_5_out);
  and and_2 (and_2_out, not_4_out, op4);
  and and_3 (and_3_out, op5, op6);
  and and_4 (and_4_out, f31, not_5_out);
  and and_5 (and_5_out, not_4_out, op4);
  and and_6 (and_6_out, op5, op6);
  and and_7 (and_7_out, f3_2, not_5_out);
  and and_8 (and_8_out, not_4_out, op4);
  and and_9 (and_9_out, op5, op6);
  and and_10 (and_10_out, not_4_out, not_3_out);
  and and_11 (and_11_out, not_2_out, not_1_out);
  and and_12 (and_12_out, f30, not_5_out);
  and and_13 (and_13_out, not_4_out, op4);
  and and_14 (and_14_out, op5, op6);
  and and_15 (and_15_out, f31, not_5_out);
  and and_16 (and_16_out, not_4_out, op4);
  and and_17 (and_17_out, op5, op6);
  and and_18 (and_18_out, f3_2, not_5_out);
  and and_19 (and_19_out, not_4_out, op4);
  and and_20 (and_20_out, op5, op6);
  and and_21 (and_21_out, op2, not_3_out);
  and and_22 (and_22_out, op5, op6);
  and and_23 (and_23_out, not_4_out, not_3_out);
  and and_24 (and_24_out, op5, not_1_out);
  and and_25 (and_25_out, not_4_out, not_3_out);
  and and_26 (and_26_out, not_2_out, not_1_out);
  and and_27 (and_27_out, not_5_out, not_4_out);
  and and_28 (and_28_out, op4, op5);
  and and_29 (and_29_out, not_5_out, not_4_out);
  and and_30 (and_30_out, op4, op5);
  and and_31 (and_31_out, not_5_out, not_4_out);
  and and_32 (and_32_out, op4, op5);
  and and_33 (and_33_out, not_5_out, not_4_out);
  and and_34 (and_34_out, not_2_out, not_1_out);
  and and_35 (and_35_out, op2, not_3_out);
  and and_36 (and_36_out, op5, op6);
  and and_37 (and_37_out, op4, not_1_out);
  and and_38 (and_38_out, not_4_out, not_3_out);
  and and_39 (and_39_out, op5, op6);
  and and_40 (and_40_out, op3, not_3_out);
  and and_41 (and_41_out, op5, op6);
  and and_42 (and_42_out, not_4_out, not_3_out);
  and and_43 (and_43_out, op5, op6);
  and and_44 (and_44_out, not_4_out, op4);
  and and_45 (and_45_out, op5, not_1_out);
  and and_46 (and_46_out, not_4_out, op4);
  and and_47 (and_47_out, not_2_out, not_1_out);
  and and_48 (and_48_out, op3, not_3_out);
  and and_49 (and_49_out, op5, op6);
  or or_1 (or_1_out, op2, op3);
  and and_50 (and_50_out, not_3_out, not_1_out);
  and and_51 (and_51_out, op3, not_3_out);
  and and_52 (and_52_out, op5, op6);
  and and_53 (and_53_out, not_4_out, not_3_out);
  and and_54 (and_54_out, op5, op6);
  and and_55 (and_55_out, op2, not_4_out);
  and and_56 (and_56_out, op4, not_1_out);
  and and_57 (and_57_out, not_4_out, not_3_out);
  and and_58 (and_58_out, op5, not_1_out);
  and and_59 (and_59_out, op2, not_4_out);
  and and_60 (and_60_out, op4, not_1_out);
  and and_61 (and_61_out, not_5_out, not_4_out);
  and and_62 (and_62_out, op4, not_1_out);
  and and_63 (and_63_out, not_4_out, op4);
  and and_64 (and_64_out, not_2_out, not_1_out);
  and and_65 (and_65_out, not_4_out, not_3_out);
  and and_66 (and_66_out, op5, op6);
  and and_67 (and_67_out, not_5_out, not_4_out);
  and and_68 (and_68_out, op4, not_1_out);
  and and_69 (and_69_out, not_5_out, not_4_out);
  and and_70 (and_70_out, op4, not_1_out);
  and and_71 (and_71_out, not_5_out, not_4_out);
  and and_72 (and_72_out, op4, not_1_out);
  and and_73 (and_73_out, f30, not_7_out);
  and and_74 (and_74_out, f3_2, f730);
  and and_75 (and_75_out, not_5_out, not_4_out);
  and and_76 (and_76_out, op4, not_1_out);
  and and_77 (and_77_out, f730, not_5_out);
  and and_78 (and_78_out, not_4_out, op4);
  and and_79 (and_79_out, op5, not_1_out);
  and and_80 (and_80_out, not_4_out, not_3_out);
  and and_81 (and_81_out, op5, op6);
  and and_82 (ram_b, not_8_out, not_7_out);
  and and_83 (ram_h, f30, not_7_out);
  and and_84 (and_84_out, f30, not_5_out);
  and and_85 (and_85_out, not_4_out, op4);
  and and_86 (and_86_out, op5, op6);
  and and_87 (and_87_out, f31, not_5_out);
  and and_88 (and_88_out, not_4_out, op4);
  and and_89 (and_89_out, op5, op6);
  and and_90 (and_90_out, f3_2, not_5_out);
  and and_91 (and_91_out, not_4_out, op4);
  and and_92 (and_92_out, op5, op6);
  and and_93 (csr_opset, not_8_out, f31);
  and and_94 (csr_opclear, f30, f31);
  and and_95 (and_95_out, not_8_out, not_7_out);
  and and_96 (and_96_out, ld_signext, not_10_out);
  and and_97 (and_97_out, not_9_out, not_5_out);
  and and_98 (and_98_out, not_4_out, op4);
  and and_99 (and_99_out, op5, op6);
  and and_100 (and_100_out, not_8_out, not_7_out);
  and and_101 (and_101_out, ld_signext, inst20);
  and and_102 (and_102_out, not_9_out, not_5_out);
  and and_103 (and_103_out, not_4_out, op4);
  and and_104 (and_104_out, op5, op6);
  and and_105 (and_105_out, not_8_out, not_7_out);
  and and_106 (and_106_out, ld_signext, not_10_out);
  and and_107 (and_107_out, inst21, not_5_out);
  and and_108 (and_108_out, not_4_out, op4);
  and and_109 (and_109_out, op5, op6);
  and and_110 (and_110_out, and_2_out, and_3_out);
  and and_111 (and_111_out, and_5_out, and_6_out);
  and and_112 (and_112_out, and_8_out, and_9_out);
  and and_113 (and_113_out, and_10_out, and_11_out);
  and and_114 (and_114_out, and_13_out, and_14_out);
  and and_115 (and_115_out, and_16_out, and_17_out);
  and and_116 (and_116_out, and_19_out, and_20_out);
  and and_117 (and_117_out, and_21_out, and_22_out);
  and and_118 (and_118_out, and_23_out, and_24_out);
  and and_119 (and_119_out, and_25_out, and_26_out);
  and and_120 (and_120_out, and_27_out, and_28_out);
  and and_121 (and_121_out, and_29_out, and_30_out);
  and and_122 (and_122_out, and_31_out, and_32_out);
  and and_123 (and_123_out, and_33_out, and_34_out);
  and and_124 (and_124_out, and_35_out, and_36_out);
  and and_125 (and_125_out, not_4_out, and_37_out);
  and and_126 (and_126_out, and_38_out, and_39_out);
  and and_127 (and_127_out, and_40_out, and_41_out);
  and and_128 (and_128_out, and_42_out, and_43_out);
  and and_129 (and_129_out, and_44_out, and_45_out);
  and and_130 (and_130_out, and_46_out, and_47_out);
  and and_131 (and_131_out, and_48_out, and_49_out);
  or or_2 (or_2_out, and_50_out, not_2_out);
  and and_132 (and_132_out, and_51_out, and_52_out);
  and and_133 (and_133_out, and_53_out, and_54_out);
  and and_134 (and_134_out, and_55_out, and_56_out);
  and and_135 (and_135_out, and_57_out, and_58_out);
  and and_136 (and_136_out, and_59_out, and_60_out);
  and and_137 (alu_op_class_1, and_61_out, and_62_out);
  and and_138 (and_138_out, and_63_out, and_64_out);
  and and_139 (and_139_out, and_65_out, and_66_out);
  and and_140 (and_140_out, and_67_out, and_68_out);
  and and_141 (and_141_out, and_69_out, and_70_out);
  and and_142 (and_142_out, and_71_out, and_72_out);
  and and_143 (and_143_out, and_73_out, and_74_out);
  and and_144 (and_144_out, and_75_out, and_76_out);
  and and_145 (and_145_out, and_78_out, and_79_out);
  and and_146 (and_146_out, and_80_out, and_81_out);
  and and_147 (and_147_out, and_85_out, and_86_out);
  and and_148 (and_148_out, and_88_out, and_89_out);
  and and_149 (and_149_out, and_91_out, and_92_out);
  and and_150 (and_150_out, and_96_out, and_97_out);
  and and_151 (and_151_out, and_98_out, and_99_out);
  and and_152 (and_152_out, and_101_out, and_102_out);
  and and_153 (and_153_out, and_103_out, and_104_out);
  and and_154 (and_154_out, and_106_out, and_107_out);
  and and_155 (and_155_out, and_108_out, and_109_out);
  and and_156 (and_156_out, and_1_out, and_110_out);
  and and_157 (and_157_out, and_4_out, and_111_out);
  and and_158 (and_158_out, and_7_out, and_112_out);
  and and_159 (and_159_out, not_5_out, and_113_out);
  and and_160 (and_160_out, and_12_out, and_114_out);
  and and_161 (and_161_out, and_15_out, and_115_out);
  and and_162 (and_162_out, and_18_out, and_116_out);
  and and_163 (ram_wen, not_5_out, and_118_out);
  and and_164 (ram_ren, not_5_out, and_119_out);
  and and_165 (and_165_out, f30, and_120_out);
  and and_166 (and_166_out, f31, and_121_out);
  and and_167 (and_167_out, f3_2, and_122_out);
  or or_3 (or_3_out, and_124_out, and_125_out);
  and and_168 (branch_sel, not_5_out, and_126_out);
  and and_169 (jal_sel, op2, and_127_out);
  and and_170 (jalr_sel, op2, and_128_out);
  and and_171 (alu_asel_1, op2, and_129_out);
  and and_172 (and_172_out, op2, and_130_out);
  and and_173 (and_173_out, op2, and_131_out);
  or or_4 (alu_bsel, or_1_out, or_2_out);
  and and_174 (imm_sel_2, op2, and_132_out);
  and and_175 (and_175_out, not_5_out, and_133_out);
  and and_176 (and_176_out, not_5_out, and_135_out);
  and and_177 (and_177_out, not_5_out, and_138_out);
  and and_178 (and_178_out, not_5_out, and_139_out);
  and and_179 (alu_op_2, f3_2, and_140_out);
  and and_180 (alu_op_1, f31, and_141_out);
  and and_181 (alu_op_0, f30, and_142_out);
  and and_182 (and_182_out, and_143_out, and_144_out);
  and and_183 (and_183_out, and_77_out, and_145_out);
  and and_184 (and_184_out, not_5_out, and_146_out);
  and and_185 (and_185_out, and_84_out, and_147_out);
  and and_186 (and_186_out, and_87_out, and_148_out);
  and and_187 (and_187_out, and_90_out, and_149_out);
  and and_188 (and_188_out, and_150_out, and_151_out);
  and and_189 (and_189_out, and_152_out, and_153_out);
  and and_190 (and_190_out, and_154_out, and_155_out);
  or or_5 (or_5_out, and_156_out, and_157_out);
  or or_6 (or_6_out, and_158_out, and_159_out);
  or or_7 (or_7_out, and_160_out, and_161_out);
  or or_8 (or_8_out, and_162_out, and_117_out);
  or or_9 (or_9_out, and_165_out, and_166_out);
  or or_10 (or_10_out, and_167_out, and_123_out);
  or or_11 (alu_asel_0, and_172_out, and_173_out);
  or or_12 (imm_sel_1, and_175_out, and_134_out);
  or or_13 (imm_sel_0, and_176_out, and_136_out);
  or or_14 (alu_op_class_0, and_177_out, and_178_out);
  or or_15 (or_15_out, and_183_out, and_184_out);
  or or_16 (or_16_out, and_186_out, and_187_out);
  and and_191 (ecall_sel, and_95_out, and_188_out);
  and and_192 (ebreak_sel, and_100_out, and_189_out);
  and and_193 (mret_sel, and_105_out, and_190_out);
  or or_17 (wb_sel_1, or_5_out, or_6_out);
  or or_18 (wb_sel_0, or_7_out, or_8_out);
  or or_19 (or_19_out, or_10_out, or_3_out);
  or or_20 (alu_mod, and_182_out, or_15_out);
  or or_21 (csr_wen, and_185_out, or_16_out);
  or or_22 (reg_wen, or_9_out, or_19_out);

  assign csr_useimm = f3_2;
endmodule
