// Digital circuit FROMTRUTH6.dig as structural Verilog
module FROMTRUTH6 (
  input  op6,
  input  op5,
  input  op4,
  input  op3,
  input  op2,
  output wb_sel_1,
  output wb_sel_0,
  output ram_wen,
  output ram_ren,
  output reg_wen,
  output branch_sel,
  output jal_sel,
  output jalr_sel,
  output alu_asel_1,
  output alu_asel_0,
  output alu_bsel,
  output imm_sel_2,
  output imm_sel_1,
  output imm_sel_0,
  output alu_op_class_1,
  output alu_op_class_0
);

  wire and_1_out, and_2_out, and_3_out, and_4_out, and_5_out, and_6_out, and_7_out, and_8_out, and_9_out,
       and_10_out, and_11_out, and_12_out, and_13_out, and_14_out, and_15_out, and_16_out, and_17_out,
       and_18_out, and_19_out, and_20_out, and_21_out, and_22_out, and_23_out, and_24_out, and_25_out,
       and_26_out, and_27_out, and_28_out, and_29_out, and_30_out, and_31_out, and_32_out, and_33_out,
       and_34_out, and_35_out, and_36_out, and_37_out, and_38_out, and_39_out, and_40_out, and_41_out,
       and_42_out, and_43_out, and_45_out, and_46_out, and_47_out, and_48_out, and_49_out, and_50_out,
       and_51_out, and_52_out, and_53_out, and_54_out, and_55_out, and_56_out, and_57_out, and_58_out,
       and_59_out, and_60_out, and_62_out, and_63_out, and_71_out, and_72_out, and_74_out, and_75_out,
       and_76_out, and_77_out, not_1_out, not_2_out, not_3_out, not_4_out, not_5_out, or_1_out, or_2_out,
       or_3_out;

  not not_1 (not_1_out, op6);
  not not_2 (not_2_out, op5);
  not not_3 (not_3_out, op4);
  not not_4 (not_4_out, op3);
  not not_5 (not_5_out, op2);
  and and_1 (and_1_out, not_4_out, not_3_out);
  and and_2 (and_2_out, not_2_out, not_1_out);
  and and_3 (and_3_out, op2, not_3_out);
  and and_4 (and_4_out, op5, op6);
  and and_5 (and_5_out, not_4_out, not_3_out);
  and and_6 (and_6_out, op5, not_1_out);
  and and_7 (and_7_out, not_4_out, not_3_out);
  and and_8 (and_8_out, not_2_out, not_1_out);
  and and_9 (and_9_out, not_5_out, not_4_out);
  and and_10 (and_10_out, not_2_out, not_1_out);
  and and_11 (and_11_out, op2, not_3_out);
  and and_12 (and_12_out, op5, op6);
  and and_13 (and_13_out, op4, not_1_out);
  and and_14 (and_14_out, not_4_out, not_3_out);
  and and_15 (and_15_out, op5, op6);
  and and_16 (and_16_out, op3, not_3_out);
  and and_17 (and_17_out, op5, op6);
  and and_18 (and_18_out, not_4_out, not_3_out);
  and and_19 (and_19_out, op5, op6);
  and and_20 (and_20_out, not_4_out, op4);
  and and_21 (and_21_out, op5, not_1_out);
  and and_22 (and_22_out, not_4_out, op4);
  and and_23 (and_23_out, not_2_out, not_1_out);
  and and_24 (and_24_out, op3, not_3_out);
  and and_25 (and_25_out, op5, op6);
  or or_1 (or_1_out, op2, op3);
  and and_26 (and_26_out, not_3_out, not_1_out);
  and and_27 (and_27_out, op3, not_3_out);
  and and_28 (and_28_out, op5, op6);
  and and_29 (and_29_out, not_4_out, not_3_out);
  and and_30 (and_30_out, op5, op6);
  and and_31 (and_31_out, op2, not_4_out);
  and and_32 (and_32_out, op4, not_1_out);
  and and_33 (and_33_out, not_4_out, not_3_out);
  and and_34 (and_34_out, op5, not_1_out);
  and and_35 (and_35_out, op2, not_4_out);
  and and_36 (and_36_out, op4, not_1_out);
  and and_37 (and_37_out, not_5_out, not_4_out);
  and and_38 (and_38_out, op4, not_1_out);
  and and_39 (and_39_out, not_4_out, op4);
  and and_40 (and_40_out, not_2_out, not_1_out);
  and and_41 (and_41_out, not_4_out, not_3_out);
  and and_42 (and_42_out, op5, op6);
  and and_43 (and_43_out, and_1_out, and_2_out);
  and and_44 (wb_sel_0, and_3_out, and_4_out);
  and and_45 (and_45_out, and_5_out, and_6_out);
  and and_46 (and_46_out, and_7_out, and_8_out);
  and and_47 (and_47_out, and_9_out, and_10_out);
  and and_48 (and_48_out, and_11_out, and_12_out);
  and and_49 (and_49_out, not_4_out, and_13_out);
  and and_50 (and_50_out, and_14_out, and_15_out);
  and and_51 (and_51_out, and_16_out, and_17_out);
  and and_52 (and_52_out, and_18_out, and_19_out);
  and and_53 (and_53_out, and_20_out, and_21_out);
  and and_54 (and_54_out, and_22_out, and_23_out);
  and and_55 (and_55_out, and_24_out, and_25_out);
  or or_2 (or_2_out, and_26_out, not_2_out);
  and and_56 (and_56_out, and_27_out, and_28_out);
  and and_57 (and_57_out, and_29_out, and_30_out);
  and and_58 (and_58_out, and_31_out, and_32_out);
  and and_59 (and_59_out, and_33_out, and_34_out);
  and and_60 (and_60_out, and_35_out, and_36_out);
  and and_61 (alu_op_class_1, and_37_out, and_38_out);
  and and_62 (and_62_out, and_39_out, and_40_out);
  and and_63 (and_63_out, and_41_out, and_42_out);
  and and_64 (wb_sel_1, not_5_out, and_43_out);
  and and_65 (ram_wen, not_5_out, and_45_out);
  and and_66 (ram_ren, not_5_out, and_46_out);
  or or_3 (or_3_out, and_48_out, and_49_out);
  and and_67 (branch_sel, not_5_out, and_50_out);
  and and_68 (jal_sel, op2, and_51_out);
  and and_69 (jalr_sel, op2, and_52_out);
  and and_70 (alu_asel_1, op2, and_53_out);
  and and_71 (and_71_out, op2, and_54_out);
  and and_72 (and_72_out, op2, and_55_out);
  or or_4 (alu_bsel, or_1_out, or_2_out);
  and and_73 (imm_sel_2, op2, and_56_out);
  and and_74 (and_74_out, not_5_out, and_57_out);
  and and_75 (and_75_out, not_5_out, and_59_out);
  and and_76 (and_76_out, not_5_out, and_62_out);
  and and_77 (and_77_out, not_5_out, and_63_out);
  or or_5 (reg_wen, and_47_out, or_3_out);
  or or_6 (alu_asel_0, and_71_out, and_72_out);
  or or_7 (imm_sel_1, and_74_out, and_58_out);
  or or_8 (imm_sel_0, and_75_out, and_60_out);
  or or_9 (alu_op_class_0, and_76_out, and_77_out);
endmodule
