// Digital circuit OTHERFROMTRUTH.dig as structural Verilog
module OTHERFROMTRUTH (
  input  inst31,
  input  inst30,
  input  inst29,
  input  inst28,
  input  inst27,
  input  inst26,
  input  inst25,
  input  inst24,
  input  inst23,
  input  inst22,
  input  inst21,
  input  inst20,
  output ecall_sel,
  output ebreak_sel,
  output mret_sel,
  output dret_sel
);

  wire and_1_out, and_2_out, and_3_out, and_4_out, and_5_out, and_6_out, and_7_out, and_8_out, and_9_out,
       and_10_out, and_11_out, and_12_out, and_13_out, and_14_out, and_15_out, and_16_out, and_17_out,
       and_18_out, and_19_out, and_20_out, and_21_out, and_22_out, and_23_out, and_24_out, and_25_out,
       and_26_out, and_27_out, and_28_out, and_29_out, and_30_out, and_31_out, and_32_out, and_33_out,
       and_34_out, and_35_out, and_36_out, and_37_out, and_38_out, and_39_out, and_40_out, not_1_out,
       not_2_out, not_3_out, not_4_out, not_5_out, not_6_out, not_7_out, not_8_out, not_9_out, not_10_out,
       not_11_out, not_12_out;

  not not_1 (not_1_out, inst31);
  not not_2 (not_2_out, inst30);
  not not_3 (not_3_out, inst29);
  not not_4 (not_4_out, inst28);
  not not_5 (not_5_out, inst27);
  not not_6 (not_6_out, inst26);
  not not_7 (not_7_out, inst25);
  not not_8 (not_8_out, inst24);
  not not_9 (not_9_out, inst23);
  not not_10 (not_10_out, inst22);
  not not_11 (not_11_out, inst21);
  not not_12 (not_12_out, inst20);
  and and_1 (and_1_out, not_12_out, not_11_out);
  and and_2 (and_2_out, not_10_out, not_9_out);
  and and_3 (and_3_out, not_8_out, not_7_out);
  and and_4 (and_4_out, not_6_out, not_5_out);
  and and_5 (and_5_out, not_4_out, not_3_out);
  and and_6 (and_6_out, not_2_out, not_1_out);
  and and_7 (and_7_out, inst20, not_11_out);
  and and_8 (and_8_out, not_10_out, not_9_out);
  and and_9 (and_9_out, not_8_out, not_7_out);
  and and_10 (and_10_out, not_6_out, not_5_out);
  and and_11 (and_11_out, not_4_out, not_3_out);
  and and_12 (and_12_out, not_2_out, not_1_out);
  and and_13 (and_13_out, not_12_out, inst21);
  and and_14 (and_14_out, not_10_out, not_9_out);
  and and_15 (and_15_out, not_8_out, not_7_out);
  and and_16 (and_16_out, not_6_out, not_5_out);
  and and_17 (and_17_out, inst28, inst29);
  and and_18 (and_18_out, not_2_out, not_1_out);
  and and_19 (and_19_out, not_12_out, inst21);
  and and_20 (and_20_out, not_10_out, not_9_out);
  and and_21 (and_21_out, inst24, inst25);
  and and_22 (and_22_out, not_6_out, inst27);
  and and_23 (and_23_out, inst28, inst29);
  and and_24 (and_24_out, inst30, not_1_out);
  and and_25 (and_25_out, and_1_out, and_2_out);
  and and_26 (and_26_out, and_3_out, and_4_out);
  and and_27 (and_27_out, and_5_out, and_6_out);
  and and_28 (and_28_out, and_7_out, and_8_out);
  and and_29 (and_29_out, and_9_out, and_10_out);
  and and_30 (and_30_out, and_11_out, and_12_out);
  and and_31 (and_31_out, and_13_out, and_14_out);
  and and_32 (and_32_out, and_15_out, and_16_out);
  and and_33 (and_33_out, and_17_out, and_18_out);
  and and_34 (and_34_out, and_19_out, and_20_out);
  and and_35 (and_35_out, and_21_out, and_22_out);
  and and_36 (and_36_out, and_23_out, and_24_out);
  and and_37 (and_37_out, and_26_out, and_27_out);
  and and_38 (and_38_out, and_29_out, and_30_out);
  and and_39 (and_39_out, and_32_out, and_33_out);
  and and_40 (and_40_out, and_35_out, and_36_out);
  and and_41 (ecall_sel, and_25_out, and_37_out);
  and and_42 (ebreak_sel, and_28_out, and_38_out);
  and and_43 (mret_sel, and_31_out, and_39_out);
  and and_44 (dret_sel, and_34_out, and_40_out);
endmodule
