// Digital circuit RV5-ALU-CONTROL.dig as structural Verilog
module RV5_ALU_CONTROL (
  input  inst_30,
  input  [1:0] alu_opclass,
  input  [2:0] funct3,
  output [2:0] alu_op,
  output alu_mod
);

  wire and_1_out, and_2_out, and_3_out, and_4_out, and_5_out, and_6_out, not_1_out, not_2_out, not_3_out,
       or_1_out;

  and and_1 (and_1_out, alu_opclass[0], alu_opclass[1]);
  or or_1 (or_1_out, alu_opclass[0], alu_opclass[1]);
  not not_1 (not_1_out, alu_opclass[0]);
  not not_2 (not_2_out, alu_opclass[1]);
  not not_3 (not_3_out, funct3[1]);
  Multiplexer #(.Bits(3)) multiplexer_1 (.sel(or_1_out), .in_0(3'b000), .in_1(funct3), .out(alu_op));
  and and_2 (and_2_out, not_1_out, alu_opclass[1]);
  and and_3 (and_3_out, alu_opclass[0], not_2_out);
  and and_4 (and_4_out, funct3[0], not_3_out, funct3[2]);
  and and_5 (and_5_out, and_3_out, inst_30);
  and and_6 (and_6_out, and_1_out, inst_30, and_4_out);
  or or_2 (alu_mod, and_2_out, and_5_out, and_6_out);

  // Notes on the sheet:
  //   RV5-ALU-CONTROL
endmodule
