// Digital circuit RV5-ALU.dig as structural Verilog
module RV5_ALU (
  input  [2:0] OP,
  input  [31:0] A,
  input  [31:0] B,
  input  MOD,
  output [31:0] Y,
  output BR
);

  wire and_2_out, c, comparator_1_lt, not_3_out, not_4_out, not_5_out, slt, xnor_1_out, xor_2_out, z;
  wire [0:0] not_2_out;
  wire [31:0] \and , multiplexer_1_out, not_1_out, \or , sll, sr, sra_1_out, srl_1_out, sum, \xor ;

  assign \or  = A | B;  // Or or_1, 32 bits wide
  assign \xor  = A ^ B;  // XOr xor_1, 32 bits wide
  assign \and  = A & B;  // And and_1, 32 bits wide
  assign not_1_out = ~B;  // Not not_1, 32 bits wide
  SLL sll_1 (.in(A), .shift(B[4:0]), .out(sll));
  SRL srl_1 (.in(A), .shift(B[4:0]), .out(srl_1_out));
  SRA sra_1 (.in(A), .shift(B[4:0]), .out(sra_1_out));
  Multiplexer #(.Bits(32)) multiplexer_1 (.sel(MOD), .in_0(B), .in_1(not_1_out), .out(multiplexer_1_out));
  Multiplexer #(.Bits(32)) multiplexer_2 (.sel(MOD), .in_0(srl_1_out), .in_1(sra_1_out), .out(sr));
  xnor xnor_1 (xnor_1_out, A[31], multiplexer_1_out[31]);
  not not_2 (not_2_out[0], c);
  Add #(.Bits(32)) add_1 (.a(A), .b(multiplexer_1_out), .c_i(MOD), .s(sum), .c_o(c));
  xor xor_2 (xor_2_out, sum[31], A[31]);
  Multiplexer #(.Selector_Bits(3), .Bits(32)) multiplexer_3 (
    .sel(OP), .in_0(sum), .in_1(sll), .in_2({{31{1'b0}}, slt}), .in_3({{31{1'b0}}, not_2_out[0]}),
    .in_4(\xor ), .in_5(sr), .in_6(\or ), .in_7(\and ), .out(Y));
  Multiplexer #(.Selector_Bits(3)) multiplexer_4 (
    .sel(OP), .in_0(z), .in_1(not_3_out), .in_2(1'b0), .in_3(1'b0), .in_4(slt), .in_5(not_4_out),
    .in_6(not_5_out), .in_7(c), .out(BR));
  not not_3 (not_3_out, z);
  not not_4 (not_4_out, slt);
  not not_5 (not_5_out, c);
  Comparator #(.Signed("true"), .Bits(32)) comparator_1 (
    .a(sum), .b({32{1'b0}}), .eq(z), .lt(comparator_1_lt));  // open: gt
  and and_2 (and_2_out, xor_2_out, xnor_1_out);
  xor xor_3 (slt, comparator_1_lt, and_2_out);

  // Other names for the same wires on the sheet: br_cond = BR

  // Notes on the sheet:
  //   RV-ALU : Combinational
  //   TODO: DOC
endmodule
