// Digital circuit RV5-CSR.dig as structural Verilog
module RV5_CSR (
  input  clk,
  input  [11:0] addr,
  input  [31:0] w_data,
  input  wen,
  input  [31:0] pc_in,
  input  ecall_sel,
  input  mret_sel,
  input  ebreak_sel,
  input  is_debug,
  input  haltreq,
  output [31:0] R_DATA,
  output [31:0] MTVEC_OUT,
  output [31:0] MEPC_OUT,
  output [31:0] DCSR_OUT,
  output [31:0] DPC_OUT
);

  wire and_1_out, and_2_out, and_3_out, and_4_out, and_5_out, and_6_out, and_7_out, and_8_out, and_9_out,
       and_10_out, and_11_out, and_12_out, d_ff_1_nq, dcsr_sel, dpc_sel, dscratch0_sel, dscratch1_sel,
       mcause_sel, mepc_sel, misa_sel, mscratch_sel, mstatus_sel, mtvec_sel, not_1_out, not_2_out, not_3_out,
       or_1_out, or_2_out, or_3_out, or_4_out, or_5_out, or_6_out;
  wire [3:0] priorityencoder_1_num;
  wire [31:0] dscratch0_q, dscratch1_q, mcause_q, mscratch_q, mstatus_q, multiplexer_1_out,
       multiplexer_2_out, multiplexer_3_out, multiplexer_4_out, multiplexer_5_out;

  Comparator #(.Bits(12)) comparator_1 (.a(addr), .b(12'h300), .eq(mstatus_sel));  // open: gt, lt
  Comparator #(.Bits(12)) comparator_2 (.a(addr), .b(12'h301), .eq(misa_sel));  // open: gt, lt
  Comparator #(.Bits(12)) comparator_3 (.a(addr), .b(12'h305), .eq(mtvec_sel));  // open: gt, lt
  Comparator #(.Bits(12)) comparator_4 (.a(addr), .b(12'h340), .eq(mscratch_sel));  // open: gt, lt
  Comparator #(.Bits(12)) comparator_5 (.a(addr), .b(12'h341), .eq(mepc_sel));  // open: gt, lt
  Comparator #(.Bits(12)) comparator_6 (.a(addr), .b(12'h342), .eq(mcause_sel));  // open: gt, lt
  Comparator #(.Bits(12)) comparator_7 (.a(addr), .b(12'h7b0), .eq(dcsr_sel));  // open: gt, lt
  Comparator #(.Bits(12)) comparator_8 (.a(addr), .b(12'h7b1), .eq(dpc_sel));  // open: gt, lt
  Comparator #(.Bits(12)) comparator_9 (.a(addr), .b(12'h7b2), .eq(dscratch0_sel));  // open: gt, lt
  Comparator #(.Bits(12)) comparator_10 (.a(addr), .b(12'h7b3), .eq(dscratch1_sel));  // open: gt, lt
  not not_1 (not_1_out, DCSR_OUT[15]);
  not not_2 (not_2_out, is_debug);
  D_FF d_ff_1 (.D(haltreq), .C(clk), .nQ(d_ff_1_nq));  // open: Q
  and and_1 (and_1_out, not_1_out, ebreak_sel, not_2_out);
  not not_3 (not_3_out, is_debug);
  and and_2 (and_2_out, haltreq, d_ff_1_nq);
  or or_1 (or_1_out, ecall_sel, and_1_out);
  and and_3 (and_3_out, ebreak_sel, not_3_out, DCSR_OUT[15]);
  or or_2 (or_2_out, and_3_out, and_2_out);
  Multiplexer #(.Bits(32)) multiplexer_1 (.sel(or_1_out), .in_0(w_data), .in_1(pc_in), .out(multiplexer_1_out));
  Multiplexer #(.Bits(32)) multiplexer_2 (
    .sel(or_1_out), .in_0(w_data), .in_1(multiplexer_3_out), .out(multiplexer_2_out));
  Multiplexer #(.Bits(32)) multiplexer_3 (.sel(ecall_sel), .in_0(32'h3), .in_1(32'hb), .out(multiplexer_3_out));
  Multiplexer #(.Bits(32)) multiplexer_4 (.sel(or_2_out), .in_0(w_data), .in_1(pc_in), .out(multiplexer_4_out));
  and and_4 (and_4_out, wen, mepc_sel);
  and and_5 (and_5_out, wen, mcause_sel);
  and and_6 (and_6_out, wen, dcsr_sel);
  and and_7 (and_7_out, wen, dpc_sel);
  Multiplexer #(.Bits(32)) multiplexer_5 (
    .sel(haltreq), .in_0(w_data), .in_1({DCSR_OUT[31:9], 3'b011, DCSR_OUT[5:2], 2'b11}),
    .out(multiplexer_5_out));
  or or_3 (or_3_out, and_6_out, haltreq);
  and and_8 (and_8_out, wen, mstatus_sel);
  and and_9 (and_9_out, wen, mtvec_sel);
  and and_10 (and_10_out, wen, mscratch_sel);
  or or_4 (or_4_out, and_4_out, or_1_out);
  or or_5 (or_5_out, and_5_out, or_1_out);
  or or_6 (or_6_out, and_7_out, or_2_out);
  and and_11 (and_11_out, wen, dscratch0_sel);
  and and_12 (and_12_out, wen, dscratch1_sel);
  Register #(.Bits(32)) mstatus (.D(w_data), .C(clk), .en(and_8_out), .Q(mstatus_q));
  Register #(.Bits(32)) mtvec (.D(w_data), .C(clk), .en(and_9_out), .Q(MTVEC_OUT));
  Register #(.Bits(32)) mscratch (.D(w_data), .C(clk), .en(and_10_out), .Q(mscratch_q));
  Register #(.Bits(32)) mepc (.D(multiplexer_1_out), .C(clk), .en(or_4_out), .Q(MEPC_OUT));
  Register #(.Bits(32)) mcause (.D(multiplexer_2_out), .C(clk), .en(or_5_out), .Q(mcause_q));
  Register #(.Bits(32)) dcsr (.D(multiplexer_5_out), .C(clk), .en(or_3_out), .Q(DCSR_OUT));
  Register #(.Bits(32)) dpc (.D(multiplexer_4_out), .C(clk), .en(or_6_out), .Q(DPC_OUT));
  Register #(.Bits(32)) dscratch0 (.D(w_data), .C(clk), .en(and_11_out), .Q(dscratch0_q));
  Register #(.Bits(32)) dscratch1 (.D(w_data), .C(clk), .en(and_12_out), .Q(dscratch1_q));
  PriorityEncoder #(.Selector_Bits(4)) priorityencoder_1 (
    .in0(mstatus_sel), .in1(misa_sel), .in2(mtvec_sel), .in3(mscratch_sel), .in4(mepc_sel), .in5(mcause_sel),
    .in6(dcsr_sel), .in7(dpc_sel), .in8(dscratch0_sel), .in9(dscratch1_sel), .in10(1'b0), .in11(1'b0),
    .in12(1'b0), .in13(1'b0), .in14(1'b0), .in15(1'b0), .num(priorityencoder_1_num));  // open: any
  Multiplexer #(.Selector_Bits(4), .Bits(32)) multiplexer_6 (
    .sel(priorityencoder_1_num), .in_0(mstatus_q), .in_1(32'h40000100), .in_2(MTVEC_OUT), .in_3(mscratch_q),
    .in_4(MEPC_OUT), .in_5(mcause_q), .in_6(DCSR_OUT), .in_7(DPC_OUT), .in_8(dscratch0_q),
    .in_9(dscratch1_q), .in_10({32{1'b0}}), .in_11({32{1'b0}}), .in_12({32{1'b0}}), .in_13({32{1'b0}}),
    .in_14({32{1'b0}}), .in_15({32{1'b0}}), .out(R_DATA));

  // Other names for the same wires on the sheet: dcsr[31:0] = DCSR_OUT

  // Notes on the sheet:
  //   RV5-CSR
endmodule
