// Digital circuit RV5-GPR.dig as structural Verilog
module RV5_GPR (
  input  [4:0] RS1,
  input  [4:0] RS2,
  input  [31:0] D_in,
  input  clk,
  input  WEN,
  input  [4:0] RD,
  output [31:0] RA,
  output [31:0] RB,
  output RD0
);

  wire src1is0, src2is0;
  wire [31:0] REGS_da, REGS_db;

  and and_1 (src1is0, ~RS1[0], ~RS1[1], ~RS1[2], ~RS1[3], ~RS1[4]);  // And
  and and_2 (src2is0, ~RS2[0], ~RS2[1], ~RS2[2], ~RS2[3], ~RS2[4]);  // And
  RegisterFile #(.AddrBits(5), .Bits(32)) REGS (
    .Din(D_in), .we(WEN), .Rw(RD), .C(clk), .Ra(RS1), .Rb(RS2), .Da(REGS_da), .Db(REGS_db));
  Multiplexer #(.Bits(32)) multiplexer_1 (.sel(src1is0), .in_0(REGS_da), .in_1({32{1'b0}}), .out(RA));
  Multiplexer #(.Bits(32)) multiplexer_2 (.sel(src2is0), .in_0(REGS_db), .in_1({32{1'b0}}), .out(RB));
  and and_3 (RD0, ~RD[0], ~RD[1], ~RD[2], ~RD[3], ~RD[4]);  // And

  // Other names for the same wires on the sheet: dst[4:0] = RD; src_1[4:0] = RS1; src_2[4:0] = RS2

  // Notes on the sheet:
  //   RV5-REGS
  //   2-Port Register Bank
  //   Zero Detector
  //   Immediate Selector
  //   /5
  //   /32
  //   Zero Reg Decode
  //   Reg/Reg0
  //   RA-bus
  //   RB-bus
endmodule
