// Digital circuit RV5-IMM.dig as structural Verilog
module RV5_IMM (
  input  UJ_imm_sel,
  input  I_imm_sel,
  input  SB_imm_sel,
  input  S_imm_sel,
  input  U_imm_sel,
  input  [31:0] INSTR_32,
  output [31:0] imm
);

  wire [2:0] priorityencoder_1_num;
  wire [31:0] Iimm32, SBimm32, Simm32, UJimm32;

  BitExtender #(.inputBits(21), .outputBits(32)) bitextender_1 (
    .in({INSTR_32[31], INSTR_32[19:12], INSTR_32[20], INSTR_32[30:21], 1'b0}), .out(UJimm32));
  PriorityEncoder #(.Selector_Bits(3)) priorityencoder_1 (
    .in0(UJ_imm_sel), .in1(U_imm_sel), .in2(SB_imm_sel), .in3(S_imm_sel), .in4(I_imm_sel), .in5(1'b0),
    .in6(1'b0), .in7(1'b0), .num(priorityencoder_1_num));  // open: any
  BitExtender #(.inputBits(12), .outputBits(32)) bitextender_2 (.in({INSTR_32[31:25], INSTR_32[11:7]}), .out(Simm32));
  Multiplexer #(.Selector_Bits(3), .Bits(32)) multiplexer_1 (
    .sel(priorityencoder_1_num), .in_0(UJimm32), .in_1({INSTR_32[31:12], {12{1'b0}}}), .in_2(SBimm32),
    .in_3(Simm32), .in_4(Iimm32), .in_5({32{1'b0}}), .in_6({32{1'b0}}), .in_7({32{1'b0}}), .out(imm));
  BitExtender #(.inputBits(13), .outputBits(32)) bitextender_3 (
    .in({INSTR_32[31], INSTR_32[7], INSTR_32[30:25], INSTR_32[11:8], 1'b0}), .out(SBimm32));
  BitExtender #(.inputBits(12), .outputBits(32)) bitextender_4 (.in(INSTR_32[31:20]), .out(Iimm32));

  // Other names for the same wires on the sheet: Uimm32[31:12] = INSTR_32[31:12]; sgn_ext_imm32[31:0] = imm

  // Notes on the sheet:
  //   INSTR_32: default 33621011
  //   RV5-IMMED-SPLIT-EXTEND-MUX
  //   Immediate extract split sign-extend
  //   Immediate Selector MUX
endmodule
