// Digital circuit RV5-INSTR-DECODE.dig as structural Verilog
module RV5_INSTR_DECODE (
  input  [31:0] instr,
  output [4:0] rs2,
  output [4:0] rs1,
  output [4:0] rd,
  output [6:0] opcode,
  output UJ_imm_sel,
  output U_imm_sel,
  output S_imm_sel,
  output SB_imm_sel,
  output I_imm_sel,
  output alu_mod,
  output ram_wen,
  output [1:0] wb_sel,
  output ram_ren,
  output ecall_sel,
  output [2:0] alu_op,
  output ram_b,
  output ram_h,
  output reg_wen,
  output branch_sel,
  output jal_sel,
  output jalr_sel,
  output [1:0] alu_a_sel,
  output ld_signext,
  output csr_wen,
  output mret_sel,
  output [11:0] system_imm,
  output ebreak_sel,
  output dret_sel,
  output csr_opset,
  output csr_opclear,
  output csr_useimm
);

  wire and_1_out, and_2_out, and_7_out, and_8_out, and_9_out, and_12_out, and_13_out, and_14_out, and_18_out,
       and_19_out, and_24_out, branch_sel_t, comparator_1_eq, comparator_2_eq, comparator_3_eq, csr_opwrite,
       ecall_sel_t, fromtruth4_1_aluadd, fromtruth4_1_bsel, fromtruth4_1_csrs, fromtruth4_1_csrw,
       fromtruth4_1_jmp, funct3_000, funct3_001, funct3_010, funct3_011, funct3_100, funct3_101, funct3_110,
       funct3_111, I_imm_sel_t, L_RPalu_bsel, L_RPbranch_sel, L_RPjal_sel, L_RPjalr_sel, L_RPram_ren,
       L_RPram_wen, L_RPreg_wen, ld_signext_t, mret_sel_t, nor_1_out, not_1_out, not_3_out, not_4_out,
       not_5_out, not_6_out, op42_000, op42_001, op42_010, op42_011, op42_100, op42_101, op42_110, op42_111,
       op65_00, op65_01, op65_10, op65_11, or_2_out, or_3_out, or_4_out, or_5_out, or_6_out, or_12_out,
       ram_b_t, ram_h_t, ram_ren_t, ram_wen_t, reg_wen_t, S_imm_sel_t, SB_imm_sel_t, U_imm_sel_t,
       UJ_imm_sel_t;
  wire [0:0] alu_a_sel_t;
  wire [1:0] L_RPalu_asel, L_RPopclass, L_RPwb_sel, multiplexer_1_out, multiplexer_2_out, wb_sel_t;
  wire [2:0] L_RPimm_sel;

  FROMTRUTH4 fromtruth4_1 (
    .op6(instr[6]), .op5(instr[5]), .op4(instr[4]), .op3(instr[3]), .op2(instr[2]), .f3_2(instr[14]),
    .f31(instr[13]), .f30(instr[12]), .f730(instr[30]), .inst21(instr[21]), .inst20(instr[20]),
    .RegW(reg_wen), .ASel1(alu_a_sel[1]), .ASel0(alu_a_sel[0]), .BSel(fromtruth4_1_bsel), .MemW(ram_wen),
    .MemR(ram_ren), .WBSel1(wb_sel[1]), .WBSel0(wb_sel[0]), .Br(branch_sel), .Jmp(fromtruth4_1_jmp),
    .CSRW(fromtruth4_1_csrw), .CSRS(fromtruth4_1_csrs), .ALUAdd(fromtruth4_1_aluadd), .immI(I_imm_sel),
    .immS(S_imm_sel), .immSB(SB_imm_sel), .immU(U_imm_sel), .immUJ(UJ_imm_sel), .ramB(ram_b), .ramH(ram_h),
    .ld_sext(ld_signext), .ecall_sel(ecall_sel), .mretsel(mret_sel), .ebreak_sel(ebreak_sel),
    .dretsel(dret_sel), .CSR_OP_WRITE(csr_opwrite), .CSR_OP_SET(csr_opset), .CSR_OP_CLEAR(csr_opclear),
    .CSR_USE_IMM(csr_useimm));
  FROMTRUTH6 fromtruth6_1 (
    .op6(instr[6]), .op5(instr[5]), .op4(instr[4]), .op3(instr[3]), .op2(instr[2]), .wb_sel_1(L_RPwb_sel[1]),
    .wb_sel_0(L_RPwb_sel[0]), .ram_wen(L_RPram_wen), .ram_ren(L_RPram_ren), .reg_wen(L_RPreg_wen),
    .branch_sel(L_RPbranch_sel), .jal_sel(L_RPjal_sel), .jalr_sel(L_RPjalr_sel),
    .alu_asel_1(L_RPalu_asel[1]), .alu_asel_0(L_RPalu_asel[0]), .alu_bsel(L_RPalu_bsel),
    .imm_sel_2(L_RPimm_sel[2]), .imm_sel_1(L_RPimm_sel[1]), .imm_sel_0(L_RPimm_sel[0]),
    .alu_op_class_1(L_RPopclass[1]), .alu_op_class_0(L_RPopclass[0]));
  LED led_1 (.in(fromtruth4_1_bsel));
  LED led_2 (.in(fromtruth4_1_jmp));
  LED led_3 (.in(fromtruth4_1_csrw));
  LED led_4 (.in(fromtruth4_1_csrs));
  LED led_5 (.in(fromtruth4_1_aluadd));
  or or_1 (csr_wen, csr_opwrite, csr_opset, csr_opclear);
  and and_1 (and_1_out, op65_01, op42_000);
  and and_2 (and_2_out, op42_000, op65_11);
  or or_2 (or_2_out, op42_000, op42_100, op42_110);
  or or_3 (or_3_out, op42_100, op42_001);
  and and_3 (SB_imm_sel_t, op65_11, op42_000);
  or or_4 (or_4_out, op65_00, op65_01);
  and and_4 (UJ_imm_sel_t, op65_11, op42_011);
  or or_5 (or_5_out, op42_001, op42_011);
  and and_5 (ram_ren_t, op65_00, op42_000);
  and and_6 (ram_wen_t, op42_000, op65_01);
  or or_6 (or_6_out, funct3_101, instr[5]);
  and and_7 (and_7_out, instr[4], instr[30]);
  or or_7 (ram_b_t, funct3_000, funct3_100);
  or or_8 (ram_h_t, funct3_001, funct3_101);
  nor nor_1 (nor_1_out, and_1_out, and_2_out);
  and and_8 (and_8_out, op65_00, or_2_out);
  and and_9 (and_9_out, op65_11, or_3_out);
  and and_10 (S_imm_sel_t, op65_01, op42_000);
  and and_11 (U_imm_sel_t, or_4_out, op42_101);
  and and_12 (and_12_out, op65_11, or_5_out);
  and and_13 (and_13_out, or_6_out, and_7_out);
  Decoder #(.Selector_Bits(3)) decoder_1 (
    .sel(instr[4:2]), .out_0(op42_000), .out_1(op42_001), .out_2(op42_010), .out_3(op42_011),
    .out_4(op42_100), .out_5(op42_101), .out_6(op42_110), .out_7(op42_111));
  or or_9 (I_imm_sel_t, and_8_out, and_9_out);
  Multiplexer #(.Bits(2)) multiplexer_1 (.sel(and_12_out), .in_0(2'b00), .in_1(2'b01), .out(multiplexer_1_out));
  not not_1 (not_1_out, instr[2]);
  or or_10 (reg_wen_t, nor_1_out, csr_wen);
  Comparator #(.Bits(5)) comparator_1 (.a(instr[6:2]), .b(5'b11100), .eq(comparator_1_eq));  // open: gt, lt
  Decoder #(.Selector_Bits(2)) decoder_2 (
    .sel(instr[6:5]), .out_0(op65_00), .out_1(op65_01), .out_2(op65_10), .out_3(op65_11));
  Multiplexer #(.Bits(2)) multiplexer_2 (
    .sel(ram_ren_t), .in_0(multiplexer_1_out), .in_1(2'b10), .out(multiplexer_2_out));
  and and_14 (and_14_out, and_13_out, not_1_out);
  Comparator #(.Bits(12)) comparator_2 (.a(instr[31:20]), .b({12{1'b0}}), .eq(comparator_2_eq));  // open: gt, lt
  Comparator #(.Bits(12)) comparator_3 (.a(instr[31:20]), .b(12'h302), .eq(comparator_3_eq));  // open: gt, lt
  Multiplexer #(.Bits(2)) multiplexer_3 (.sel(csr_wen), .in_0(multiplexer_2_out), .in_1(2'b11), .out(wb_sel_t));
  or or_11 (alu_mod, and_14_out, branch_sel_t);
  not not_2 (ld_signext_t, instr[14]);
  Decoder #(.Selector_Bits(3)) decoder_3 (
    .sel(instr[14:12]), .out_0(funct3_000), .out_1(funct3_001), .out_2(funct3_010), .out_3(funct3_011),
    .out_4(funct3_100), .out_5(funct3_101), .out_6(funct3_110), .out_7(funct3_111));
  and and_15 (branch_sel_t, op65_11, op42_000);
  and and_16 (jal_sel, op65_11, op42_011);
  and and_17 (jalr_sel, op65_11, op42_001);
  not not_3 (not_3_out, funct3_000);
  and and_18 (and_18_out, funct3_000, comparator_2_eq);
  and and_19 (and_19_out, funct3_000, comparator_3_eq);
  // And and_20 has open pins: In_1=not_3_out, In_2=comparator_1_eq, out=open
  and and_21 (ecall_sel_t, comparator_1_eq, and_18_out);
  and and_22 (mret_sel_t, comparator_1_eq, and_19_out);
  not not_4 (not_4_out, instr[5]);
  and and_23 (alu_a_sel_t[0], not_4_out, op42_101);
  Multiplexer #(.Bits(3)) multiplexer_4 (.sel(or_12_out), .in_0(instr[14:12]), .in_1(3'b000), .out(alu_op));
  or or_12 (or_12_out, and_24_out, instr[2]);
  and and_24 (and_24_out, not_5_out, not_6_out);
  not not_5 (not_5_out, instr[4]);
  not not_6 (not_6_out, instr[6]);

  assign opcode = instr[6:0];
  assign rd = instr[11:7];
  assign rs1 = instr[19:15];
  assign rs2 = instr[24:20];
  assign system_imm = instr[31:20];

  // Other names for the same wires on the sheet: nwb_sel[1:0] = wb_sel; nalu_a_sel[1:0] = alu_a_sel;
  //   instr32[31:0] = instr; funct3[2:0] = instr[14:12]; funct7[6:0] = instr[31:25]; nbranch_sel = branch_sel;
  //   necall_sel = ecall_sel; nI_imm_sel = I_imm_sel; nld_signext = ld_signext; nmret_sel = mret_sel; nram_b = ram_b;
  //   nram_h = ram_h; nram_ren = ram_ren; nram_wen = ram_wen; nreg_wen = reg_wen; nS_imm_sel = S_imm_sel;
  //   nSB_imm_sel = SB_imm_sel; nU_imm_sel = U_imm_sel; nUJ_imm_sel = UJ_imm_sel

  // Notes on the sheet:
  //   instr: default 3363864831
  //   This component is in a transitional stage.
  //   Originally, most of what it yielded came from ad-hoc
  //   wirings (that you can see on the right).
  //   However, Digital can autogenerate a circuit from
  //   a truth table, so I'm transitioning over to that to
  //   reduce complexity.
  //   Tunnels starting with the letter 'n' are from the
  //   new autogenerated circuit. Tunnels being outputted
  //   that do not start with 'n' still need to be converted.
  //   RV5-INSTR-SPLIT-IMM-DECODE
  //   Immediate Selector Decode
  //   instruction split
  //   SCUFFED FIX IF USING
endmodule
