// Digital circuit RV5-MAIN-CONTROL.dig as structural Verilog
module RV5_MAIN_CONTROL (
  input  [6:0] opcode,
  output [1:0] wb_sel,
  output ram_wen,
  output ram_ren,
  output reg_wen,
  output branch_sel,
  output jal_sel,
  output jalr_sel,
  output [1:0] alu_asel,
  output alu_bsel,
  output [2:0] imm_sel,
  output [1:0] alu_opclass
);

  wire alu_bsel_t, branch_sel_t, jal_sel_t, jalr_sel_t, ram_ren_t, ram_wen_t, reg_wen_t;
  wire [1:0] alu_asel_t, alu_opclass_t;
  wire [2:0] imm_sel_t;

  FROMTRUTH6 fromtruth6_1 (
    .op6(opcode[6]), .op5(opcode[5]), .op4(opcode[4]), .op3(opcode[3]), .op2(opcode[2]),
    .wb_sel_1(wb_sel[1]), .wb_sel_0(wb_sel[0]), .ram_wen(ram_wen_t), .ram_ren(ram_ren_t),
    .reg_wen(reg_wen_t), .branch_sel(branch_sel_t), .jal_sel(jal_sel_t), .jalr_sel(jalr_sel_t),
    .alu_asel_1(alu_asel_t[1]), .alu_asel_0(alu_asel_t[0]), .alu_bsel(alu_bsel_t), .imm_sel_2(imm_sel_t[2]),
    .imm_sel_1(imm_sel_t[1]), .imm_sel_0(imm_sel_t[0]), .alu_op_class_1(alu_opclass_t[1]),
    .alu_op_class_0(alu_opclass_t[0]));

  // Notes on the sheet:
  //   RV5-MAIN-CONTROL
endmodule
