// Digital circuit RV5-MEM-CONTROL.dig as structural Verilog
module RV5_MEM_CONTROL (
  input  is_load,
  input  is_store,
  input  [2:0] funct3,
  output ram_wen,
  output ram_ren,
  output reg_wen,
  output [1:0] wb_sel,
  output alu_bsel,
  output [2:0] imm_sel,
  output ram_b,
  output ram_h,
  output ld_signext
);

  wire and_1_out, nor_1_out, not_1_out, not_2_out;

  or or_1 (alu_bsel, is_load, is_store);
  nor nor_1 (nor_1_out, funct3[0], funct3[1]);
  not not_1 (not_1_out, funct3[1]);
  Multiplexer multiplexer_1 (.sel(alu_bsel), .in_0(1'b0), .in_1(nor_1_out), .out(ram_b));
  and and_1 (and_1_out, not_1_out, funct3[0]);
  Multiplexer multiplexer_2 (.sel(alu_bsel), .in_0(1'b0), .in_1(and_1_out), .out(ram_h));
  Multiplexer #(.Bits(3)) multiplexer_3 (.sel(is_store), .in_0(3'b000), .in_1(3'b001), .out(imm_sel));
  not not_2 (not_2_out, funct3[2]);
  Multiplexer #(.Bits(2)) multiplexer_4 (.sel(is_load), .in_0(2'b00), .in_1(2'b10), .out(wb_sel));
  and and_2 (ld_signext, is_load, not_2_out);

  assign ram_ren = is_load;
  assign ram_wen = is_store;
  assign reg_wen = is_load;

  // Notes on the sheet:
  //   RV5-MEM-CONTROL
  //   TODO: DOC
endmodule
