// Digital circuit RV5-MEMORY.dig as structural Verilog
module RV5_MEMORY (
  input  [31:0] addr,
  input  [31:0] wdata,
  input  wen,
  input  ren,
  input  clk,
  input  \byte ,
  input  half,
  input  signext,
  input  [31:0] addr_inst,
  input  [31:0] addr_dm,
  input  wen_dm,
  input  [31:0] wdata_dm,
  output [31:0] out,
  output [31:0] out_inst,
  output [31:0] out_dm,
  output [31:0] d0O
);

  wire addr_data0, addr_dm_data0, addr_dm_progbuf_0, addr_dm_progbuf_1, addr_dm_progbuf_2, addr_dm_progbuf_3,
       addr_dm_progbuf_4, addr_dm_progbuf_5, addr_dm_progbuf_6, addr_dm_progbuf_7, addr_inst_data0,
       addr_inst_progbuf_0, addr_inst_progbuf_1, addr_inst_progbuf_2, addr_inst_progbuf_3,
       addr_inst_progbuf_4, addr_inst_progbuf_5, addr_inst_progbuf_6, addr_inst_progbuf_7, addr_inst_ram,
       addr_inst_terminal, addr_progbuf_0, addr_progbuf_1, addr_progbuf_2, addr_progbuf_3, addr_progbuf_4,
       addr_progbuf_5, addr_progbuf_6, addr_progbuf_7, addr_ram, addr_terminal, and_1_out, and_2_out,
       and_3_out, and_4_out, and_5_out, and_6_out, and_7_out, and_8_out, and_9_out, and_10_out, and_11_out,
       and_12_out, and_13_out, decoder_1_out_1, decoder_1_out_2, decoder_1_out_3, multiplexer_1_out,
       multiplexer_2_out, multiplexer_3_out, or_1_out, wb0, wb1, wb2, wb3;
  wire [3:0] addr_dm_range, addr_inst_range, addr_range;
  wire [7:0] multiplexer_9_out, multiplexer_10_out, multiplexer_11_out, multiplexer_12_out, ob0, ob1, ob2,
       ob3;
  wire [31:0] bitextender_1_out, bitextender_2_out, multiplexer_4_out, multiplexer_8_out, multiplexer_14_out,
       multiplexer_15_out, multiplexer_16_out, multiplexer_17_out, multiplexer_18_out, progbuf_0, progbuf_1,
       progbuf_2, progbuf_3, progbuf_4, progbuf_5, progbuf_6, progbuf_7, RAM_d2, rv5_srl_1_out;

  Comparator #(.Bits(32)) comparator_1 (.a(addr), .b(32'hffc), .eq(addr_data0), .lt(addr_ram));  // open: gt
  Comparator #(.Bits(32)) comparator_2 (.a(addr), .b(32'h1000), .eq(addr_terminal));  // open: gt, lt
  Comparator #(.Bits(32)) comparator_3 (.a(addr), .b(32'h1004), .eq(addr_progbuf_0));  // open: gt, lt
  Comparator #(.Bits(32)) comparator_4 (.a(addr), .b(32'h1008), .eq(addr_progbuf_1));  // open: gt, lt
  Comparator #(.Bits(32)) comparator_5 (.a(addr), .b(32'h100c), .eq(addr_progbuf_2));  // open: gt, lt
  Comparator #(.Bits(32)) comparator_6 (.a(addr), .b(32'h1010), .eq(addr_progbuf_3));  // open: gt, lt
  Comparator #(.Bits(32)) comparator_7 (.a(addr), .b(32'h1014), .eq(addr_progbuf_4));  // open: gt, lt
  Comparator #(.Bits(32)) comparator_8 (.a(addr), .b(32'h1018), .eq(addr_progbuf_5));  // open: gt, lt
  Comparator #(.Bits(32)) comparator_9 (.a(addr), .b(32'h101c), .eq(addr_progbuf_6));  // open: gt, lt
  Comparator #(.Bits(32)) comparator_10 (.a(addr), .b(32'h1020), .eq(addr_progbuf_7));  // open: gt, lt
  Comparator #(.Bits(32)) comparator_11 (
    .a(addr_inst), .b(32'hffc), .eq(addr_inst_data0), .lt(addr_inst_ram));  // open: gt
  Comparator #(.Bits(32)) comparator_12 (.a(addr_inst), .b(32'h1000), .eq(addr_inst_terminal));  // open: gt, lt
  Comparator #(.Bits(32)) comparator_13 (.a(addr_inst), .b(32'h1004), .eq(addr_inst_progbuf_0));  // open: gt, lt
  Comparator #(.Bits(32)) comparator_14 (.a(addr_inst), .b(32'h1008), .eq(addr_inst_progbuf_1));  // open: gt, lt
  Comparator #(.Bits(32)) comparator_15 (.a(addr_inst), .b(32'h100c), .eq(addr_inst_progbuf_2));  // open: gt, lt
  Comparator #(.Bits(32)) comparator_16 (.a(addr_inst), .b(32'h1010), .eq(addr_inst_progbuf_3));  // open: gt, lt
  Comparator #(.Bits(32)) comparator_17 (.a(addr_inst), .b(32'h1014), .eq(addr_inst_progbuf_4));  // open: gt, lt
  Comparator #(.Bits(32)) comparator_18 (.a(addr_inst), .b(32'h1018), .eq(addr_inst_progbuf_5));  // open: gt, lt
  Comparator #(.Bits(32)) comparator_19 (.a(addr_inst), .b(32'h101c), .eq(addr_inst_progbuf_6));  // open: gt, lt
  Comparator #(.Bits(32)) comparator_20 (.a(addr_inst), .b(32'h1020), .eq(addr_inst_progbuf_7));  // open: gt, lt
  Decoder #(.Selector_Bits(2)) decoder_1 (
    .sel(addr[1:0]), .out_0(wb0), .out_1(decoder_1_out_1), .out_2(decoder_1_out_2), .out_3(decoder_1_out_3));
  Comparator #(.Bits(32)) comparator_21 (.a(addr_dm), .b(32'hffc), .eq(addr_dm_data0));  // open: gt, lt
  Comparator #(.Bits(32)) comparator_22 (.a(addr_dm), .b(32'h1004), .eq(addr_dm_progbuf_0));  // open: gt, lt
  Comparator #(.Bits(32)) comparator_23 (.a(addr_dm), .b(32'h1008), .eq(addr_dm_progbuf_1));  // open: gt, lt
  Comparator #(.Bits(32)) comparator_24 (.a(addr_dm), .b(32'h100c), .eq(addr_dm_progbuf_2));  // open: gt, lt
  Comparator #(.Bits(32)) comparator_25 (.a(addr_dm), .b(32'h1010), .eq(addr_dm_progbuf_3));  // open: gt, lt
  Comparator #(.Bits(32)) comparator_26 (.a(addr_dm), .b(32'h1014), .eq(addr_dm_progbuf_4));  // open: gt, lt
  Comparator #(.Bits(32)) comparator_27 (.a(addr_dm), .b(32'h1018), .eq(addr_dm_progbuf_5));  // open: gt, lt
  Comparator #(.Bits(32)) comparator_28 (.a(addr_dm), .b(32'h101c), .eq(addr_dm_progbuf_6));  // open: gt, lt
  Comparator #(.Bits(32)) comparator_29 (.a(addr_dm), .b(32'h1020), .eq(addr_dm_progbuf_7));  // open: gt, lt
  Multiplexer multiplexer_1 (.sel(half), .in_0(wb0), .in_1(wb0), .out(multiplexer_1_out));
  Multiplexer multiplexer_2 (.sel(half), .in_0(wb0), .in_1(decoder_1_out_2), .out(multiplexer_2_out));
  Multiplexer multiplexer_3 (.sel(half), .in_0(wb0), .in_1(decoder_1_out_2), .out(multiplexer_3_out));
  Multiplexer #(.Bits(32)) multiplexer_4 (
    .sel(\byte ), .in_0(wdata), .in_1({wdata[7:0], wdata[7:0], wdata[7:0], wdata[7:0]}),
    .out(multiplexer_4_out));
  Multiplexer multiplexer_5 (.sel(\byte ), .in_0(multiplexer_1_out), .in_1(decoder_1_out_1), .out(wb1));
  Multiplexer multiplexer_6 (.sel(\byte ), .in_0(multiplexer_2_out), .in_1(decoder_1_out_2), .out(wb2));
  Multiplexer multiplexer_7 (.sel(\byte ), .in_0(multiplexer_3_out), .in_1(decoder_1_out_3), .out(wb3));
  Multiplexer #(.Bits(32)) multiplexer_8 (
    .sel(half), .in_0(multiplexer_4_out), .in_1({wdata[15:0], wdata[15:0]}), .out(multiplexer_8_out));
  and and_1 (and_1_out, addr_terminal, wen);
  and and_2 (and_2_out, wen, addr_ram);
  and and_3 (and_3_out, ren, addr_ram);
  Terminal terminal_1 (.D(wdata), .C(clk), .en(and_1_out));
  Multiplexer #(.Bits(8)) multiplexer_9 (.sel(wb0), .in_0(ob0), .in_1(multiplexer_8_out[7:0]), .out(multiplexer_9_out));
  Multiplexer #(.Bits(8)) multiplexer_10 (
    .sel(wb1), .in_0(ob1), .in_1(multiplexer_8_out[15:8]), .out(multiplexer_10_out));
  Multiplexer #(.Bits(8)) multiplexer_11 (
    .sel(wb2), .in_0(ob2), .in_1(multiplexer_8_out[23:16]), .out(multiplexer_11_out));
  Multiplexer #(.Bits(8)) multiplexer_12 (
    .sel(wb3), .in_0(ob3), .in_1(multiplexer_8_out[31:24]), .out(multiplexer_12_out));
  RAMDualAccess #(.AddrBits(10), .isProgramMemory("true"), .Bits(32)) RAM (
    .str(and_2_out), .C(clk), .ld(and_3_out), .A1(addr[11:2]),
    .Din1({multiplexer_12_out, multiplexer_11_out, multiplexer_10_out, multiplexer_9_out}),
    .A2(addr_inst[11:2]), .D1({ob3, ob2, ob1, ob0}), .D2(RAM_d2));
  PriorityEncoder #(.Selector_Bits(4)) priorityencoder_1 (
    .in0(1'b0), .in1(1'b0), .in2(1'b0), .in3(addr_dm_progbuf_0), .in4(addr_dm_progbuf_1),
    .in5(addr_dm_progbuf_2), .in6(addr_dm_progbuf_3), .in7(addr_dm_progbuf_4), .in8(addr_dm_progbuf_5),
    .in9(addr_dm_progbuf_6), .in10(addr_dm_progbuf_7), .in11(addr_dm_data0), .in12(1'b0), .in13(1'b0),
    .in14(1'b0), .in15(1'b0), .num(addr_dm_range));  // open: any
  and and_4 (and_4_out, addr_dm_progbuf_0, wen_dm);
  and and_5 (and_5_out, addr_dm_progbuf_1, wen_dm);
  and and_6 (and_6_out, addr_dm_progbuf_2, wen_dm);
  and and_7 (and_7_out, addr_dm_progbuf_3, wen_dm);
  and and_8 (and_8_out, addr_dm_progbuf_4, wen_dm);
  and and_9 (and_9_out, addr_dm_progbuf_5, wen_dm);
  and and_10 (and_10_out, addr_dm_progbuf_6, wen_dm);
  and and_11 (and_11_out, addr_dm_progbuf_7, wen_dm);
  Register #(.Bits(32)) u_progbuf_0 (.D(wdata_dm), .C(clk), .en(and_4_out), .Q(progbuf_0));
  Register #(.Bits(32)) u_progbuf_1 (.D(wdata_dm), .C(clk), .en(and_5_out), .Q(progbuf_1));
  Register #(.Bits(32)) u_progbuf_2 (.D(wdata_dm), .C(clk), .en(and_6_out), .Q(progbuf_2));
  Register #(.Bits(32)) u_progbuf_3 (.D(wdata_dm), .C(clk), .en(and_7_out), .Q(progbuf_3));
  Register #(.Bits(32)) u_progbuf_4 (.D(wdata_dm), .C(clk), .en(and_8_out), .Q(progbuf_4));
  Register #(.Bits(32)) u_progbuf_5 (.D(wdata_dm), .C(clk), .en(and_9_out), .Q(progbuf_5));
  Register #(.Bits(32)) u_progbuf_6 (.D(wdata_dm), .C(clk), .en(and_10_out), .Q(progbuf_6));
  Register #(.Bits(32)) u_progbuf_7 (.D(wdata_dm), .C(clk), .en(and_11_out), .Q(progbuf_7));
  Multiplexer #(.Selector_Bits(4), .Bits(32)) multiplexer_13 (
    .sel(addr_inst_range), .in_0({32{1'b0}}), .in_1(RAM_d2), .in_2({32{1'b0}}), .in_3(progbuf_0),
    .in_4(progbuf_1), .in_5(progbuf_2), .in_6(progbuf_3), .in_7(progbuf_4), .in_8(progbuf_5),
    .in_9(progbuf_6), .in_10(progbuf_7), .in_11(d0O), .in_12({32{1'b0}}), .in_13({32{1'b0}}),
    .in_14({32{1'b0}}), .in_15({32{1'b0}}), .out(out_inst));
  PriorityEncoder #(.Selector_Bits(4)) priorityencoder_2 (
    .in0(1'b0), .in1(addr_ram), .in2(addr_terminal), .in3(addr_progbuf_0), .in4(addr_progbuf_1),
    .in5(addr_progbuf_2), .in6(addr_progbuf_3), .in7(addr_progbuf_4), .in8(addr_progbuf_5),
    .in9(addr_progbuf_6), .in10(addr_progbuf_7), .in11(addr_data0), .in12(1'b0), .in13(1'b0), .in14(1'b0),
    .in15(1'b0), .num(addr_range));  // open: any
  and and_12 (and_12_out, addr_dm_data0, wen_dm);
  and and_13 (and_13_out, addr_data0, wen);
  RV5_SRL rv5_srl_1 (.in({ob3, ob2, ob1, ob0}), .shift({addr[1:0], 3'b000}), .out(rv5_srl_1_out));
  Multiplexer #(.Bits(32)) multiplexer_14 (.sel(and_12_out), .in_0(wdata), .in_1(wdata_dm), .out(multiplexer_14_out));
  or or_1 (or_1_out, and_12_out, and_13_out);
  BitExtender #(.inputBits(16), .outputBits(32)) bitextender_1 (.in(rv5_srl_1_out[15:0]), .out(bitextender_1_out));
  Register #(.Bits(32)) data0 (.D(multiplexer_14_out), .C(clk), .en(or_1_out), .Q(d0O));
  BitExtender #(.outputBits(32)) bitextender_2 (.in(rv5_srl_1_out[7:0]), .out(bitextender_2_out));
  Multiplexer #(.Bits(32)) multiplexer_15 (
    .sel(signext), .in_0({{16{1'b0}}, rv5_srl_1_out[15:0]}), .in_1(bitextender_1_out),
    .out(multiplexer_15_out));
  Multiplexer #(.Bits(32)) multiplexer_16 (
    .sel(signext), .in_0({{24{1'b0}}, rv5_srl_1_out[7:0]}), .in_1(bitextender_2_out), .out(multiplexer_16_out));
  Multiplexer #(.Bits(32)) multiplexer_17 (
    .sel(\byte ), .in_0(rv5_srl_1_out), .in_1(multiplexer_16_out), .out(multiplexer_17_out));
  PriorityEncoder #(.Selector_Bits(4)) priorityencoder_3 (
    .in0(1'b0), .in1(addr_inst_ram), .in2(addr_inst_terminal), .in3(addr_inst_progbuf_0),
    .in4(addr_inst_progbuf_1), .in5(addr_inst_progbuf_2), .in6(addr_inst_progbuf_3),
    .in7(addr_inst_progbuf_4), .in8(addr_inst_progbuf_5), .in9(addr_inst_progbuf_6),
    .in10(addr_inst_progbuf_7), .in11(addr_inst_data0), .in12(1'b0), .in13(1'b0), .in14(1'b0), .in15(1'b0),
    .num(addr_inst_range));  // open: any
  Multiplexer #(.Bits(32)) multiplexer_18 (
    .sel(half), .in_0(multiplexer_17_out), .in_1(multiplexer_15_out), .out(multiplexer_18_out));
  Multiplexer #(.Selector_Bits(4), .Bits(32)) multiplexer_19 (
    .sel(addr_range), .in_0({32{1'b0}}), .in_1(multiplexer_18_out), .in_2({32{1'b0}}), .in_3(progbuf_0),
    .in_4(progbuf_1), .in_5(progbuf_2), .in_6(progbuf_3), .in_7(progbuf_4), .in_8(progbuf_5),
    .in_9(progbuf_6), .in_10(progbuf_7), .in_11(d0O), .in_12({32{1'b0}}), .in_13({32{1'b0}}),
    .in_14({32{1'b0}}), .in_15({32{1'b0}}), .out(out));
  Multiplexer #(.Selector_Bits(4), .Bits(32)) multiplexer_20 (
    .sel(addr_dm_range), .in_0({32{1'b0}}), .in_1({32{1'b0}}), .in_2({32{1'b0}}), .in_3(progbuf_0),
    .in_4(progbuf_1), .in_5(progbuf_2), .in_6(progbuf_3), .in_7(progbuf_4), .in_8(progbuf_5),
    .in_9(progbuf_6), .in_10(progbuf_7), .in_11(d0O), .in_12({32{1'b0}}), .in_13({32{1'b0}}),
    .in_14({32{1'b0}}), .in_15({32{1'b0}}), .out(out_dm));

  // Other names for the same wires on the sheet: data0[31:0] = d0O

  // Notes on the sheet:
  //   If we're storing a byte or a half,
  //   copy the value into all slots.
  //   Determine which bytes should
  //   be overwritten.
  //   Mix the old bytes with the
  //   new ones.
  //   Shift our output so 
  //   what we want
  //   starts at LSB.
  //   Handle optional sign extension
  //   for all read sizes.
endmodule
