// Digital circuit RV5-PCU.dig as structural Verilog
module RV5_PCU (
  input  [31:0] IMM_32,
  input  CLK,
  input  IS_BRANCH,
  input  IS_JAL,
  input  IS_JALR,
  input  COND_MET,
  input  [31:0] ALU_OUT,
  input  IS_ECALL,
  input  [31:0] MTVEC,
  input  [31:0] MEPC,
  input  IS_MRET,
  input  IS_EBREAK,
  input  IS_DEBUG,
  input  [31:0] DCSR,
  input  [31:0] DPC,
  input  IS_DRET,
  input  HALTREQ,
  input  JUMPPROGBUF,
  input  RESUMEREQ,
  output [31:0] PC
);

  wire and_1_out, and_2_out, or_1_out, or_2_out, rising_edge_1_o;
  wire [29:0] multiplexer_1_out, multiplexer_2_out, multiplexer_3_out, multiplexer_4_out, multiplexer_5_out,
       multiplexer_6_out, multiplexer_7_out, multiplexer_8_out, multiplexer_9_out, multiplexer_10_out,
       PC_Incr_s, PC_JumpRel_s;

  and and_1 (and_1_out, IS_BRANCH, COND_MET);
  or or_1 (or_1_out, IS_JAL, and_1_out);
  Multiplexer #(.Bits(30)) multiplexer_1 (
    .sel(or_1_out), .in_0(PC_Incr_s), .in_1(PC_JumpRel_s), .out(multiplexer_1_out));
  Multiplexer #(.Bits(30)) multiplexer_2 (
    .sel(IS_JALR), .in_0(multiplexer_1_out), .in_1(ALU_OUT[31:2]), .out(multiplexer_2_out));
  Multiplexer #(.Bits(30)) multiplexer_3 (
    .sel(IS_ECALL), .in_0(multiplexer_2_out), .in_1(MTVEC[31:2]), .out(multiplexer_3_out));
  Multiplexer #(.Bits(30)) multiplexer_4 (
    .sel(IS_MRET), .in_0(multiplexer_3_out), .in_1(MEPC[31:2]), .out(multiplexer_4_out));
  or or_2 (or_2_out, IS_DEBUG, DCSR[15]);
  Multiplexer #(.Bits(30)) multiplexer_5 (.sel(or_2_out), .in_0(MTVEC[31:2]), .in_1(30'h64), .out(multiplexer_5_out));
  Multiplexer #(.Bits(30)) multiplexer_6 (
    .sel(IS_EBREAK), .in_0(multiplexer_4_out), .in_1(multiplexer_5_out), .out(multiplexer_6_out));
  and and_2 (and_2_out, IS_DRET, IS_DEBUG);
  Multiplexer #(.Bits(30)) multiplexer_7 (
    .sel(and_2_out), .in_0(multiplexer_6_out), .in_1(DPC[31:2]), .out(multiplexer_7_out));
  Multiplexer #(.Bits(30)) multiplexer_8 (
    .sel(HALTREQ), .in_0(multiplexer_7_out), .in_1(30'h64), .out(multiplexer_8_out));
  Multiplexer #(.Bits(30)) multiplexer_9 (
    .sel(JUMPPROGBUF), .in_0(multiplexer_8_out), .in_1(30'h401), .out(multiplexer_9_out));
  RISING_EDGE rising_edge_1 (.clk(CLK), .d(RESUMEREQ), .o(rising_edge_1_o));
  Multiplexer #(.Bits(30)) multiplexer_10 (
    .sel(rising_edge_1_o), .in_0(multiplexer_9_out), .in_1(30'h65), .out(multiplexer_10_out));
  D_FF #(.Bits(30)) PC_w (.D(multiplexer_10_out), .C(CLK), .Q(PC[31:2]));  // open: nQ
  Add #(.Bits(30)) PC_Incr (.a(30'h1), .b(PC[31:2]), .c_i(1'b0), .s(PC_Incr_s));  // open: c_o
  Add #(.Bits(30)) PC_JumpRel (.a(IMM_32[31:2]), .b(PC[31:2]), .c_i(1'b0), .s(PC_JumpRel_s));  // open: c_o

  assign PC[1:0] = 2'b00;

  // Other names for the same wires on the sheet: sgn_ext_imm32[31:0] = IMM_32

  // Notes on the sheet:
  //   PCU(Program Control Unit)
  //   IMM_32 should probably be replaced 
  //   with sgn-ext-imm32 from RV5-IMM
  //   PC = PC + 4, or PC = PC += SBimm32
  //   or PC = ALU out or PC += sgn_ext-imm32
  //   for FMT U, and UJ
endmodule
