// Digital circuit RV5-ALU-ms.dig as structural Verilog
module RV5_ALU_ms (
  input  [2:0] OP,
  input  [31:0] A,
  input  [31:0] B,
  input  MOD,
  output [31:0] AopB,
  output AltB,
  output AeqB
);

  wire c, cry, eq, lt, n, not_4_out, not_5_out, not_6_out, slt, v, xnor_1_out, xor_2_out, z;
  wire [0:0] undriven;
  wire [31:0] \and , multiplexer_1_out, multiplexer_2_out, not_1_out, not_2_out, \or , sll, sr, SRA_out,
       SRL_out, sum, \xor ;

  assign not_1_out = ~B;  // Not not_1, 32 bits wide
  RV5_SLL u_SLL (.in(A), .shift(B[4:0]), .out(sll));
  RV5_SRL SRL (.in(A), .shift(B[4:0]), .out(SRL_out));
  RV5_SRA SRA (.in(A), .shift(B[4:0]), .out(SRA_out));
  Multiplexer #(.Bits(32)) multiplexer_1 (.sel(MOD), .in_0(B), .in_1(not_1_out), .out(multiplexer_1_out));
  Multiplexer #(.Bits(32)) multiplexer_2 (.sel(MOD), .in_0(B), .in_1(not_2_out), .out(multiplexer_2_out));
  assign not_2_out = ~B;  // Not not_2, 32 bits wide
  Multiplexer #(.Bits(32)) multiplexer_3 (.sel(MOD), .in_0(SRL_out), .in_1(SRA_out), .out(sr));
  Comparator #(.Signed("true"), .Bits(32)) comparator_1 (.a(A), .b(B), .gt(lt), .eq(eq), .lt(sum[0]));
  Add #(.Bits(32)) add_1 (.a(A), .b(multiplexer_1_out), .c_i(MOD), .s(sum), .c_o(cry));
  assign \or  = A | B;  // Or or_1, 32 bits wide
  assign \xor  = A ^ B;  // XOr xor_1, 32 bits wide
  assign \and  = A & B;  // And and_1, 32 bits wide
  Add #(.Bits(32)) add_2 (.a(A), .b(multiplexer_2_out), .c_i(MOD), .s(sum), .c_o(c));
  xor xor_2 (xor_2_out, A[31], multiplexer_2_out[31]);
  xnor xnor_1 (xnor_1_out, sum[31], A[31]);
  // Not not_3 has open pins: in=c, out=open
  Multiplexer #(.Selector_Bits(3), .Bits(32)) multiplexer_4 (
    .sel(OP), .in_0(sum), .in_1(sll), .in_2({{31{1'b0}}, slt}), .in_3({{31{1'b0}}, undriven[0]}),
    .in_4(\xor ), .in_5(sr), .in_6(\or ), .in_7(\and ), .out(AopB));
  Multiplexer #(.Selector_Bits(3)) multiplexer_5 (
    .sel(OP), .in_0(z), .in_1(not_4_out), .in_2(1'b0), .in_3(1'b0), .in_4(slt), .in_5(not_5_out),
    .in_6(not_6_out), .in_7(c), .out(AeqB));
  not not_4 (not_4_out, z);
  not not_5 (not_5_out, slt);
  not not_6 (not_6_out, c);
  Comparator #(.Signed("true"), .Bits(32)) comparator_2 (.a(sum), .b({32{1'b0}}), .eq(z), .lt(n));  // open: gt
  and and_2 (v, xnor_1_out, xor_2_out);
  xor xor_3 (slt, n, v);
  // Pins of 1 and 32 bits meet at sum

  assign AltB = AeqB;

  // Other names for the same wires on the sheet: br_cond = AeqB; y[31:0] = AopB

  // Notes on the sheet:
  //   RV-ALU : Combinational
  //   ADD/SUB/COMPARE
  //   REMOVE THIS FROM THIS MODULE
  //   AND ADD tO THE PCU.
  //   OR/XOR/AND
  //   OP SELECTOR
  //   ALU OP Select
  //   0: add
  //   1: sll
  //   2: ?
  //   3: ?
  //   4: xpr
  //   5: sr
  //   6: or
  //   7: and
endmodule
