// Digital circuit RV5-ALU-CONTROL.dig as structural Verilog
module RV5_ALU_CONTROL (
  input  is_op,
  input  is_op_imm,
  input  is_lui,
  input  is_auipc,
  input  [2:0] funct3,
  input  inst30,
  output reg_wen,
  output [1:0] alu_asel,
  output alu_bsel,
  output [2:0] imm_sel,
  output [2:0] alu_op,
  output alu_mod
);

  wire and_1_out, and_2_out, and_3_out, and_4_out, and_5_out, and_6_out, is_op_is_opp_imm, nor_1_out,
       not_1_out, not_2_out, or_3_out, or_5_out;

  nor nor_1 (nor_1_out, funct3[0], funct3[1], funct3[2]);
  and and_1 (and_1_out, funct3[0], not_1_out, funct3[2]);
  not not_1 (not_1_out, funct3[1]);
  and and_2 (and_2_out, is_op, nor_1_out);
  and and_3 (and_3_out, is_op_is_opp_imm, and_1_out);
  or or_1 (is_op_is_opp_imm, is_op, is_op_imm);
  or or_2 (imm_sel[1], is_lui, is_auipc);
  not not_2 (not_2_out, funct3[2]);
  or or_3 (or_3_out, and_2_out, and_3_out);
  and and_4 (and_4_out, funct3[1], not_2_out);
  or or_4 (reg_wen, is_op_is_opp_imm, imm_sel[1]);
  and and_5 (and_5_out, inst30, or_3_out);
  or or_5 (or_5_out, is_op, is_op_is_opp_imm);
  or or_6 (alu_bsel, is_op_imm, is_lui, is_auipc);
  and and_6 (and_6_out, or_5_out, and_4_out);
  or or_7 (alu_mod, and_5_out, and_6_out);
  Multiplexer #(.Bits(3)) multiplexer_1 (.sel(is_op_is_opp_imm), .in_0(3'b000), .in_1(funct3), .out(alu_op));

  assign alu_asel = {is_lui, is_auipc};
  assign {imm_sel[2], imm_sel[0]} = {1'b0, imm_sel[1]};

  // Other names for the same wires on the sheet: is_lui_is_auipc = imm_sel[1]

  // Notes on the sheet:
  //   RV5-ALU-CONTROL
  //   TODO: DOC
endmodule
