// Digital circuit RV5-BRANCH-CONTROL.dig as structural Verilog
module RV5_BRANCH_CONTROL (
  input  is_branch,
  input  [2:0] funct3,
  output branch_sel,
  output alu_mod,
  output [2:0] alu_op,
  output [2:0] imm_sel
);

  wire [2:0] bit_expand_3_1_o;

  BIT_EXPAND_3 bit_expand_3_1 (.I(is_branch), .O(bit_expand_3_1_o));
  assign alu_op = bit_expand_3_1_o & funct3;  // And and_1, 3 bits wide

  assign alu_mod = is_branch;
  assign branch_sel = is_branch;
  assign imm_sel = {1'b0, is_branch, 1'b0};

  // Notes on the sheet:
  //   RV5-BRANCH-CONTROL
  //   We subtract for all branches because
  //   it's useful for some types of conditions.
  //   The immediate is B-type! B for branch!
  //   We can directly use funct3 as the
  //   alu op.
endmodule
