// Digital circuit RV5-JUMP-CONTROL.dig as structural Verilog
module RV5_JUMP_CONTROL (
  input  is_jalr,
  input  is_jal,
  output reg_wen,
  output [1:0] wb_sel,
  output [1:0] alu_asel,
  output alu_bsel,
  output [2:0] imm_sel,
  output jal_sel,
  output jalr_sel
);

  Multiplexer #(.Bits(2)) multiplexer_1 (.sel(is_jal), .in_0(2'b00), .in_1(2'b01), .out(alu_asel));
  or or_1 (alu_bsel, is_jalr, is_jal);
  Multiplexer #(.Bits(3)) multiplexer_2 (.sel(is_jal), .in_0(3'b000), .in_1(3'b100), .out(imm_sel));
  Multiplexer #(.Bits(2)) multiplexer_3 (.sel(alu_bsel), .in_0(2'b00), .in_1(2'b01), .out(wb_sel));

  assign jal_sel = is_jal;
  assign jalr_sel = is_jalr;
  assign reg_wen = alu_bsel;

  // Notes on the sheet:
  //   RV5-JUMP-CONTROL
  //   TODO: DOC
endmodule
