// Digital circuit RV5-SYSTEM-CONTROL.dig as structural Verilog
module RV5_SYSTEM_CONTROL (
  input  is_system,
  input  [11:0] inst_20_31,
  input  [2:0] funct3,
  output reg_wen,
  output [1:0] wb_sel,
  output csr_wen,
  output csr_opset,
  output csr_opclear,
  output csr_useimm,
  output is_ecall,
  output is_ebreak,
  output is_mret,
  output is_dret
);

  wire is_priv, nor_1_out, not_1_out, or_1_out, system_imm_decode_1__000, system_imm_decode_1__001,
       system_imm_decode_1__7b2, system_imm_decode_1__302;

  or or_1 (or_1_out, funct3[0], funct3[1], funct3[2]);
  nor nor_1 (nor_1_out, funct3[0], funct3[1], funct3[2]);
  and and_1 (csr_wen, is_system, or_1_out);
  and and_2 (is_priv, nor_1_out, is_system);
  SYSTEM_IMM_DECODE system_imm_decode_1 (
    .inst31(inst_20_31[11]), .inst30(inst_20_31[10]), .inst29(inst_20_31[9]), .inst28(inst_20_31[8]),
    .inst27(inst_20_31[7]), .inst26(inst_20_31[6]), .inst25(inst_20_31[5]), .inst24(inst_20_31[4]),
    .inst23(inst_20_31[3]), .inst22(inst_20_31[2]), .inst21(inst_20_31[1]), .inst20(inst_20_31[0]),
    ._000(system_imm_decode_1__000), ._001(system_imm_decode_1__001), ._302(system_imm_decode_1__302),
    ._7b2(system_imm_decode_1__7b2));
  and and_3 (csr_opset, csr_wen, not_1_out, funct3[1]);
  not not_1 (not_1_out, funct3[0]);
  and and_4 (csr_opclear, csr_wen, funct3[0], funct3[1]);
  and and_5 (csr_useimm, csr_wen, funct3[2]);
  and and_6 (is_ecall, is_priv, system_imm_decode_1__000);
  and and_7 (is_ebreak, is_priv, system_imm_decode_1__001);
  and and_8 (is_mret, is_priv, system_imm_decode_1__302);
  and and_9 (is_dret, is_priv, system_imm_decode_1__7b2);

  assign reg_wen = csr_wen;
  assign wb_sel = {2{csr_wen}};

  // Other names for the same wires on the sheet: is_csr = csr_wen

  // Notes on the sheet:
  //   RV5-SYSTEM-CONTROL
  //   TODO: DOC
endmodule
