// Digital circuit RV5-CSR.dig as structural Verilog
module RV5_CSR (
  input  clk,
  input  [11:0] addr,
  input  [31:0] w_data,
  input  wen,
  input  [31:0] pc_in,
  input  ecall_sel,
  input  mret_sel,
  input  ebreak_sel,
  input  is_debug,
  input  haltreq,
  output [31:0] R_DATA,
  output [31:0] MTVEC_OUT,
  output [31:0] MEPC_OUT,
  output [31:0] DCSR_OUT,
  output [31:0] DPC_OUT
);

  wire and_1_out, and_2_out, and_3_out, and_4_out, and_5_out, and_6_out, and_7_out, and_8_out, and_9_out,
       and_10_out, and_11_out, dcsr_sel, dpc_sel, dscratch0_sel, dscratch1_sel, mcause_sel, mepc_sel,
       misa_sel, mscratch_sel, mstatus_sel, mtvec_sel, not_1_out, not_2_out, not_3_out, or_1_out, or_2_out,
       or_3_out, or_4_out, or_5_out, or_6_out;
  wire [31:0] and_12_out, and_13_out, and_14_out, and_15_out, and_16_out, and_17_out, and_18_out, and_19_out,
       and_20_out, and_21_out, bit_expand_32_1_o, bit_expand_32_2_o, bit_expand_32_3_o, bit_expand_32_4_o,
       bit_expand_32_5_o, bit_expand_32_6_o, bit_expand_32_7_o, bit_expand_32_8_o, bit_expand_32_9_o,
       bit_expand_32_10_o, dscratch0, dscratch1, mcause, mscratch, mstatus, multiplexer_1_out,
       multiplexer_2_out, multiplexer_3_out, multiplexer_4_out, multiplexer_5_out, or_7_out, or_8_out,
       or_9_out, or_10_out, or_11_out, or_12_out, or_13_out, or_14_out;

  Comparator #(.Bits(12)) comparator_1 (.a(addr), .b(12'h300), .eq(mstatus_sel));  // open: gt, lt
  Comparator #(.Bits(12)) comparator_2 (.a(addr), .b(12'h301), .eq(misa_sel));  // open: gt, lt
  Comparator #(.Bits(12)) comparator_3 (.a(addr), .b(12'h305), .eq(mtvec_sel));  // open: gt, lt
  Comparator #(.Bits(12)) comparator_4 (.a(addr), .b(12'h340), .eq(mscratch_sel));  // open: gt, lt
  Comparator #(.Bits(12)) comparator_5 (.a(addr), .b(12'h341), .eq(mepc_sel));  // open: gt, lt
  Comparator #(.Bits(12)) comparator_6 (.a(addr), .b(12'h342), .eq(mcause_sel));  // open: gt, lt
  Comparator #(.Bits(12)) comparator_7 (.a(addr), .b(12'h7b0), .eq(dcsr_sel));  // open: gt, lt
  Comparator #(.Bits(12)) comparator_8 (.a(addr), .b(12'h7b1), .eq(dpc_sel));  // open: gt, lt
  Comparator #(.Bits(12)) comparator_9 (.a(addr), .b(12'h7b2), .eq(dscratch0_sel));  // open: gt, lt
  Comparator #(.Bits(12)) comparator_10 (.a(addr), .b(12'h7b3), .eq(dscratch1_sel));  // open: gt, lt
  not not_1 (not_1_out, DCSR_OUT[15]);
  not not_2 (not_2_out, is_debug);
  and and_1 (and_1_out, wen, mstatus_sel);
  and and_2 (and_2_out, wen, mtvec_sel);
  and and_3 (and_3_out, wen, mscratch_sel);
  and and_4 (and_4_out, wen, dscratch0_sel);
  and and_5 (and_5_out, wen, dscratch1_sel);
  and and_6 (and_6_out, not_1_out, ebreak_sel, not_2_out);
  or or_1 (or_1_out, ecall_sel, and_6_out);
  and and_7 (and_7_out, DCSR_OUT[15], ebreak_sel, not_3_out);
  not not_3 (not_3_out, is_debug);
  Register #(.Bits(32)) u_mstatus (.D(w_data), .C(clk), .en(and_1_out), .Q(mstatus));
  Register #(.Bits(32)) mtvec (.D(w_data), .C(clk), .en(and_2_out), .Q(MTVEC_OUT));
  Register #(.Bits(32)) u_mscratch (.D(w_data), .C(clk), .en(and_3_out), .Q(mscratch));
  Register #(.Bits(32)) u_dscratch0 (.D(w_data), .C(clk), .en(and_4_out), .Q(dscratch0));
  Register #(.Bits(32)) u_dscratch1 (.D(w_data), .C(clk), .en(and_5_out), .Q(dscratch1));
  or or_2 (or_2_out, and_7_out, haltreq);
  Multiplexer #(.Bits(32)) multiplexer_1 (.sel(ecall_sel), .in_0(32'h3), .in_1(32'hb), .out(multiplexer_1_out));
  Multiplexer #(.Bits(32)) multiplexer_2 (.sel(or_2_out), .in_0(w_data), .in_1(pc_in), .out(multiplexer_2_out));
  Multiplexer #(.Bits(32)) multiplexer_3 (.sel(or_1_out), .in_0(w_data), .in_1(pc_in), .out(multiplexer_3_out));
  Multiplexer #(.Bits(32)) multiplexer_4 (
    .sel(or_1_out), .in_0(w_data), .in_1(multiplexer_1_out), .out(multiplexer_4_out));
  and and_8 (and_8_out, wen, dcsr_sel);
  and and_9 (and_9_out, wen, mepc_sel);
  and and_10 (and_10_out, wen, mcause_sel);
  and and_11 (and_11_out, wen, dpc_sel);
  or or_3 (or_3_out, and_9_out, or_1_out);
  or or_4 (or_4_out, and_10_out, or_1_out);
  Multiplexer #(.Bits(32)) multiplexer_5 (
    .sel(haltreq), .in_0(w_data), .in_1({DCSR_OUT[31:9], 3'b011, DCSR_OUT[5:2], 2'b11}),
    .out(multiplexer_5_out));
  or or_5 (or_5_out, and_8_out, haltreq);
  or or_6 (or_6_out, and_11_out, or_2_out);
  Register #(.Bits(32)) mepc (.D(multiplexer_3_out), .C(clk), .en(or_3_out), .Q(MEPC_OUT));
  Register #(.Bits(32)) u_mcause (.D(multiplexer_4_out), .C(clk), .en(or_4_out), .Q(mcause));
  Register #(.Bits(32)) dcsr (.D(multiplexer_5_out), .C(clk), .en(or_5_out), .Q(DCSR_OUT));
  Register #(.Bits(32)) dpc (.D(multiplexer_2_out), .C(clk), .en(or_6_out), .Q(DPC_OUT));
  BIT_EXPAND_32 bit_expand_32_1 (.I(mstatus_sel), .O(bit_expand_32_1_o));
  BIT_EXPAND_32 bit_expand_32_2 (.I(misa_sel), .O(bit_expand_32_2_o));
  BIT_EXPAND_32 bit_expand_32_3 (.I(mtvec_sel), .O(bit_expand_32_3_o));
  BIT_EXPAND_32 bit_expand_32_4 (.I(mscratch_sel), .O(bit_expand_32_4_o));
  BIT_EXPAND_32 bit_expand_32_5 (.I(mepc_sel), .O(bit_expand_32_5_o));
  BIT_EXPAND_32 bit_expand_32_6 (.I(mcause_sel), .O(bit_expand_32_6_o));
  BIT_EXPAND_32 bit_expand_32_7 (.I(dcsr_sel), .O(bit_expand_32_7_o));
  BIT_EXPAND_32 bit_expand_32_8 (.I(dpc_sel), .O(bit_expand_32_8_o));
  BIT_EXPAND_32 bit_expand_32_9 (.I(dscratch0_sel), .O(bit_expand_32_9_o));
  BIT_EXPAND_32 bit_expand_32_10 (.I(dscratch1_sel), .O(bit_expand_32_10_o));
  assign and_12_out = mstatus & bit_expand_32_1_o;  // And and_12, 32 bits wide
  assign and_13_out = 32'h40000100 & bit_expand_32_2_o;  // And and_13, 32 bits wide
  assign and_14_out = MTVEC_OUT & bit_expand_32_3_o;  // And and_14, 32 bits wide
  assign and_15_out = mscratch & bit_expand_32_4_o;  // And and_15, 32 bits wide
  assign and_16_out = MEPC_OUT & bit_expand_32_5_o;  // And and_16, 32 bits wide
  assign and_17_out = mcause & bit_expand_32_6_o;  // And and_17, 32 bits wide
  assign and_18_out = DCSR_OUT & bit_expand_32_7_o;  // And and_18, 32 bits wide
  assign and_19_out = DPC_OUT & bit_expand_32_8_o;  // And and_19, 32 bits wide
  assign and_20_out = dscratch0 & bit_expand_32_9_o;  // And and_20, 32 bits wide
  assign and_21_out = dscratch1 & bit_expand_32_10_o;  // And and_21, 32 bits wide
  assign or_7_out = and_12_out | and_13_out;  // Or or_7, 32 bits wide
  assign or_8_out = and_14_out | and_15_out;  // Or or_8, 32 bits wide
  assign or_9_out = and_16_out | and_17_out;  // Or or_9, 32 bits wide
  assign or_10_out = and_18_out | and_19_out;  // Or or_10, 32 bits wide
  assign or_11_out = and_20_out | and_21_out;  // Or or_11, 32 bits wide
  assign or_12_out = or_7_out | or_8_out;  // Or or_12, 32 bits wide
  assign or_13_out = or_9_out | or_10_out;  // Or or_13, 32 bits wide
  assign or_14_out = or_12_out | or_13_out;  // Or or_14, 32 bits wide
  assign R_DATA = or_14_out | or_11_out;  // Or or_15, 32 bits wide

  // Other names for the same wires on the sheet: dcsr[31:0] = DCSR_OUT; dpc[31:0] = DPC_OUT; mepc[31:0] = MEPC_OUT;
  //   mtvec[31:0] = MTVEC_OUT

  // Notes on the sheet:
  //   RV5-CSR
  //   Inputs
  //   Understanding the CSRs
  //   Control Status Registers (CSRs) are special registers that behave in special ways
  //   and are used for special tasks. Each register resides at an address that is
  //   spec-defined. The instructions to access these CSRs are part of the Ziscr
  //   extension.
  //   Address Parsing & Register Select
  //   TODO: OPTIMIZE
  //   Registers
  //   Who would have thought that in the control and status register file
  //   we'd find registers?
  //   The simple ones are simple:
  //   We need to update mepc with
  //   pc and mcause with the right
  //   value when we do an ecall
  //   or relevant ebreak:
  //   We write to the priv and cause fields
  //   when we act on haltreq:
  //   We need to put pc in dpc if we hit
  //   a breakpoint or act on haltreq:
  //   Outputs
  //   There's a few things we'll 
  //   need all of the time:
  //   We can just sum-of-products for the
  //   main output:
endmodule
