// Digital circuit ISOLATE-SIGNEXT.dig as structural Verilog
module ISOLATE_SIGNEXT (
  input  [31:0] data,
  input  [31:0] addr,
  input  want_byte,
  input  want_half,
  input  signext,
  output [31:0] out
);

  wire [31:0] bitextender_1_out, bitextender_2_out, multiplexer_1_out, multiplexer_2_out, multiplexer_3_out,
       srl_1_out;

  SRL srl_1 (.in(data), .shift({addr[1:0], 3'b000}), .out(srl_1_out));
  BitExtender #(.inputBits(16), .outputBits(32)) bitextender_1 (.in(srl_1_out[15:0]), .out(bitextender_1_out));
  BitExtender #(.outputBits(32)) bitextender_2 (.in(srl_1_out[7:0]), .out(bitextender_2_out));
  Multiplexer #(.Bits(32)) multiplexer_1 (
    .sel(signext), .in_0({{16{1'b0}}, srl_1_out[15:0]}), .in_1(bitextender_1_out), .out(multiplexer_1_out));
  Multiplexer #(.Bits(32)) multiplexer_2 (
    .sel(signext), .in_0({{24{1'b0}}, srl_1_out[7:0]}), .in_1(bitextender_2_out), .out(multiplexer_2_out));
  Multiplexer #(.Bits(32)) multiplexer_3 (
    .sel(want_byte), .in_0(srl_1_out), .in_1(multiplexer_2_out), .out(multiplexer_3_out));
  Multiplexer #(.Bits(32)) multiplexer_4 (
    .sel(want_half), .in_0(multiplexer_3_out), .in_1(multiplexer_1_out), .out(out));

  // Notes on the sheet:
  //   ISOLATE-SIGNEXT
  //   Shift our output so 
  //   what we want
  //   starts at LSB.
  //   Handle optional sign extension
  //   for all read sizes.
endmodule
