// Digital circuit MASKED-OVERLAY.dig as structural Verilog
module MASKED_OVERLAY (
  input  [31:0] base,
  input  [31:0] data,
  input  [31:0] addr,
  input  \byte ,
  input  half,
  output [31:0] out
);

  wire decoder_1_out_1, decoder_1_out_2, decoder_1_out_3, multiplexer_1_out, multiplexer_2_out,
       multiplexer_3_out, wb0, wb1, wb2, wb3;
  wire [31:0] multiplexer_4_out, multiplexer_8_out;

  Decoder #(.Selector_Bits(2)) decoder_1 (
    .sel(addr[1:0]), .out_0(wb0), .out_1(decoder_1_out_1), .out_2(decoder_1_out_2), .out_3(decoder_1_out_3));
  Multiplexer multiplexer_1 (.sel(half), .in_0(wb0), .in_1(wb0), .out(multiplexer_1_out));
  Multiplexer multiplexer_2 (.sel(half), .in_0(wb0), .in_1(decoder_1_out_2), .out(multiplexer_2_out));
  Multiplexer multiplexer_3 (.sel(half), .in_0(wb0), .in_1(decoder_1_out_2), .out(multiplexer_3_out));
  Multiplexer #(.Bits(32)) multiplexer_4 (
    .sel(\byte ), .in_0(data), .in_1({data[7:0], data[7:0], data[7:0], data[7:0]}), .out(multiplexer_4_out));
  Multiplexer multiplexer_5 (.sel(\byte ), .in_0(multiplexer_1_out), .in_1(decoder_1_out_1), .out(wb1));
  Multiplexer multiplexer_6 (.sel(\byte ), .in_0(multiplexer_2_out), .in_1(decoder_1_out_2), .out(wb2));
  Multiplexer multiplexer_7 (.sel(\byte ), .in_0(multiplexer_3_out), .in_1(decoder_1_out_3), .out(wb3));
  Multiplexer #(.Bits(32)) multiplexer_8 (
    .sel(half), .in_0(multiplexer_4_out), .in_1({data[15:0], data[15:0]}), .out(multiplexer_8_out));
  Multiplexer #(.Bits(8)) multiplexer_9 (.sel(wb0), .in_0(base[7:0]), .in_1(multiplexer_8_out[7:0]), .out(out[7:0]));
  Multiplexer #(.Bits(8)) multiplexer_10 (
    .sel(wb1), .in_0(base[15:8]), .in_1(multiplexer_8_out[15:8]), .out(out[15:8]));
  Multiplexer #(.Bits(8)) multiplexer_11 (
    .sel(wb2), .in_0(base[23:16]), .in_1(multiplexer_8_out[23:16]), .out(out[23:16]));
  Multiplexer #(.Bits(8)) multiplexer_12 (
    .sel(wb3), .in_0(base[31:24]), .in_1(multiplexer_8_out[31:24]), .out(out[31:24]));

  // Other names for the same wires on the sheet: ob0[7:0] = base[7:0]; ob1[7:0] = base[15:8]; ob2[7:0] = base[23:16];
  //   ob3[7:0] = base[31:24]

  // Notes on the sheet:
  //   MASKED-OVERLAY
  //   If we're storing a byte or a half,
  //   copy the value into all slots.
  //   Determine which bytes should
  //   be overwritten.
  //   Mix the old bytes with the
  //   new ones.
endmodule
