// Digital circuit RV5-PCU.dig as structural Verilog
module RV5_PCU (
  input  [31:0] imm,
  input  [31:0] alu_out,
  input  [31:0] mtvec,
  input  [31:0] mepc,
  input  [31:0] dpc,
  input  branch_sel,
  input  jal_sel,
  input  jalr_sel,
  input  ecall_sel,
  input  mret_sel,
  input  is_debug,
  input  [31:0] dcsr,
  input  dret_sel,
  input  haltreq,
  input  command_reg_jumpprogbuf,
  input  dmcontrol_resumereq,
  input  ebreak_sel,
  input  [2:0] funct3,
  input  eq,
  input  slt,
  input  carry,
  input  clk,
  output [31:0] pc
);

  wire and_1_out, and_2_out, br_cond, not_1_out, not_2_out, not_3_out, or_1_out, or_2_out, rising_edge_1_o;
  wire [29:0] add_1_s, multiplexer_1_out, multiplexer_3_out, multiplexer_4_out, multiplexer_5_out,
       multiplexer_6_out, multiplexer_7_out, multiplexer_8_out, multiplexer_9_out, multiplexer_10_out,
       multiplexer_11_out, PC_Incr_s;

  and and_1 (and_1_out, branch_sel, br_cond);
  Add #(.Bits(30)) add_1 (.a(pc[31:2]), .b(imm[31:2]), .c_i(1'b0), .s(add_1_s));  // open: c_o
  or or_1 (or_1_out, jal_sel, and_1_out);
  Multiplexer #(.Bits(30)) multiplexer_1 (.sel(or_1_out), .in_0(PC_Incr_s), .in_1(add_1_s), .out(multiplexer_1_out));
  Multiplexer #(.Selector_Bits(3)) multiplexer_2 (
    .sel(funct3), .in_0(eq), .in_1(not_1_out), .in_2(1'b0), .in_3(1'b0), .in_4(slt), .in_5(not_2_out),
    .in_6(not_3_out), .in_7(carry), .out(br_cond));
  not not_1 (not_1_out, eq);
  not not_2 (not_2_out, slt);
  not not_3 (not_3_out, carry);
  Multiplexer #(.Bits(30)) multiplexer_3 (
    .sel(jalr_sel), .in_0(multiplexer_1_out), .in_1(alu_out[31:2]), .out(multiplexer_3_out));
  Multiplexer #(.Bits(30)) multiplexer_4 (
    .sel(ecall_sel), .in_0(multiplexer_3_out), .in_1(mtvec[31:2]), .out(multiplexer_4_out));
  Multiplexer #(.Bits(30)) multiplexer_5 (
    .sel(mret_sel), .in_0(multiplexer_4_out), .in_1(mepc[31:2]), .out(multiplexer_5_out));
  or or_2 (or_2_out, is_debug, dcsr[15]);
  Multiplexer #(.Bits(30)) multiplexer_6 (.sel(or_2_out), .in_0(mtvec[31:2]), .in_1(30'hc4), .out(multiplexer_6_out));
  Multiplexer #(.Bits(30)) multiplexer_7 (
    .sel(ebreak_sel), .in_0(multiplexer_5_out), .in_1(multiplexer_6_out), .out(multiplexer_7_out));
  and and_2 (and_2_out, dret_sel, is_debug);
  Multiplexer #(.Bits(30)) multiplexer_8 (
    .sel(and_2_out), .in_0(multiplexer_7_out), .in_1(dpc[31:2]), .out(multiplexer_8_out));
  Multiplexer #(.Bits(30)) multiplexer_9 (
    .sel(haltreq), .in_0(multiplexer_8_out), .in_1(30'hc4), .out(multiplexer_9_out));
  Multiplexer #(.Bits(30)) multiplexer_10 (
    .sel(command_reg_jumpprogbuf), .in_0(multiplexer_9_out), .in_1(30'h4001), .out(multiplexer_10_out));
  RISING_EDGE rising_edge_1 (.clk(clk), .d(dmcontrol_resumereq), .o(rising_edge_1_o));
  Multiplexer #(.Bits(30)) multiplexer_11 (
    .sel(rising_edge_1_o), .in_0(multiplexer_10_out), .in_1(30'hc5), .out(multiplexer_11_out));
  D_FF #(.Bits(30)) u_PC (.D(multiplexer_11_out), .C(clk), .Q(pc[31:2]));  // open: nQ
  Add #(.Bits(30)) PC_Incr (.a(pc[31:2]), .b(30'h1), .c_i(1'b0), .s(PC_Incr_s));  // open: c_o

  assign pc[1:0] = 2'b00;

  // Notes on the sheet:
  //   RV5-PCU
  //   TODO: Organize
endmodule
