// Digital circuit RV5-TAP.dig as structural Verilog
module RV5_TAP (
  input  TCK,
  input  TMS,
  input  TDI,
  input  DMI_ACK,
  input  [31:0] DMI_RDATA,
  input  [1:0] DMI_STATUS,
  output TDO,
  output DMI_REQ,
  output [31:0] DMI_WDATA,
  output [6:0] DMI_ADDR,
  output DMI_WRITE
);

  wire and_9_out, bypass, bypass_wen, capture_dr, capture_ir, clear_dmistat, d_ff_1_q, dmi_ack_t,
       dmi_collision_error, dmi_op_rw, dmi_tx_end, dmi_tx_start, dmi_wen, dtcms_wen, exit1_dr, exit1_ir,
       exit2_dr, exit2_ir, idcode_wen, ir_bypass, ir_dmi, ir_dtmcs, ir_idcode, ir_wen, multiplexer_2_out,
       multiplexer_9_out, nor_1_out, nor_2_out, not_1_out, not_2_out, not_3_out, or_2_out, or_3_out,
       or_4_out, pause_dr, pause_ir, run_test_idle, select_dr_scan, select_ir_scan, shift_dr, shift_ir,
       tdo_t, test_logic_reset, update_dr, update_ir;
  wire [0:0] multiplexer_6_out;
  wire [1:0] dmi_op_d, dmi_status_t, dmistat_sticky, lookuptable_1_out, multiplexer_3_out, multiplexer_4_out,
       multiplexer_5_out, multiplexer_8_out, multiplexer_11_out_3;
  wire [2:0] multiplexer_11_out_4;
  wire [3:0] multiplexer_6_out_4, multiplexer_11_out, state_lut_out, state_q;
  wire [4:0] ir, multiplexer_1_out;
  wire [5:0] multiplexer_11_out_2;
  wire [6:0] multiplexer_8_out_3;
  wire [10:0] multiplexer_6_out_2;
  wire [13:0] multiplexer_11_out_6;
  wire [15:0] multiplexer_6_out_3;
  wire [17:15] multiplexer_11_out_5;
  wire [31:0] dmi_data_d, dtmcs, idcode, multiplexer_8_out_2;
  wire [40:0] dmi;

  or or_1 (ir_wen, capture_ir, shift_ir, test_logic_reset);
  xor xor_1 (dmi_op_rw, dmi[0], dmi[1]);
  and and_1 (dmi_collision_error, update_dr, ir_dmi, dmi_op_rw, DMI_REQ);
  Multiplexer #(.Bits(5)) multiplexer_1 (
    .sel(shift_ir), .in_0(5'b00001), .in_1({TDI, ir[4:1]}), .out(multiplexer_1_out));
  Register #(.Bits(5)) u_ir (.D(multiplexer_1_out), .C(TCK), .en(ir_wen), .Q(ir));
  or or_2 (or_2_out, capture_dr, shift_dr);
  Multiplexer multiplexer_2 (.sel(shift_dr), .in_0(1'b0), .in_1(TDI), .out(multiplexer_2_out));
  and and_2 (bypass_wen, or_2_out, ir_bypass);
  and and_3 (idcode_wen, or_2_out, ir_idcode);
  and and_4 (dtcms_wen, or_2_out, ir_dtmcs);
  and and_5 (dmi_wen, or_2_out, ir_dmi);
  Register u_bypass (.D(multiplexer_2_out), .C(TCK), .en(bypass_wen), .Q(bypass));
  Multiplexer #(.Bits(2)) multiplexer_3 (
    .sel(dmi_collision_error), .in_0(dmistat_sticky), .in_1(2'b11), .out(multiplexer_3_out));
  Multiplexer #(.Bits(2)) multiplexer_4 (.sel(DMI_REQ), .in_0(2'b00), .in_1(2'b11), .out(multiplexer_4_out));
  and and_6 (clear_dmistat, update_dr, ir_dtmcs, dtmcs[16]);
  Multiplexer #(.Bits(2)) multiplexer_5 (
    .sel(clear_dmistat), .in_0(multiplexer_3_out), .in_1(2'b00), .out(multiplexer_5_out));
  or or_3 (or_3_out, clear_dmistat, dmi_collision_error);
  nor nor_1 (nor_1_out, dmistat_sticky[0], dmistat_sticky[1]);
  Register #(.Bits(2)) register_1 (.D(multiplexer_5_out), .C(TCK), .en(or_3_out), .Q(dmistat_sticky));
  Multiplexer #(.Bits(32)) multiplexer_6 (
    .sel(shift_dr), .in_0(32'h1), .in_1({TDI, idcode[31:1]}),
    .out({multiplexer_6_out_4, multiplexer_6_out_3, multiplexer_6_out_2, multiplexer_6_out[0]}));
  Multiplexer #(.Bits(2)) multiplexer_7 (
    .sel(nor_1_out), .in_0(dmistat_sticky), .in_1(multiplexer_4_out), .out(dmi_op_d));
  D_FF d_ff_1 (.D(DMI_ACK), .C(TCK), .Q(d_ff_1_q));  // open: nQ
  Register #(.Bits(32)) register_2 (.D(DMI_RDATA), .C(TCK), .en(dmi_tx_end), .Q(dmi_data_d));
  Register #(.Bits(2)) register_3 (.D(DMI_STATUS), .C(TCK), .en(dmi_tx_end), .Q(dmi_status_t));
  D_FF d_ff_2 (.D(d_ff_1_q), .C(TCK), .Q(dmi_ack_t));  // open: nQ
  Register idcode_reserved0 (.D(multiplexer_6_out[0]), .C(TCK), .en(idcode_wen), .Q(idcode[0]));
  Register #(.Bits(11)) idcode_manufid (.D(multiplexer_6_out_2), .C(TCK), .en(idcode_wen), .Q(idcode[11:1]));
  Register #(.Bits(16)) idcode_partnumber (.D(multiplexer_6_out_3), .C(TCK), .en(idcode_wen), .Q(idcode[27:12]));
  Register #(.Bits(4)) idcode_version (.D(multiplexer_6_out_4), .C(TCK), .en(idcode_wen), .Q(idcode[31:28]));
  nor nor_2 (nor_2_out, dmistat_sticky[0], dmistat_sticky[1]);
  or or_4 (or_4_out, dmi_tx_start, dmi_tx_end);
  and and_7 (dmi_tx_end, DMI_REQ, dmi_ack_t);
  not not_1 (not_1_out, DMI_REQ);
  Register register_4 (.D(dmi_tx_start), .C(TCK), .en(or_4_out), .Q(DMI_REQ));
  and and_8 (dmi_tx_start, update_dr, ir_dmi, dmi_op_rw, nor_2_out, not_1_out);
  Register #(.Bits(4)) state (.D(state_lut_out), .C(TCK), .en(1'b1), .Q(state_q));
  Decoder #(.Selector_Bits(4)) decoder_1 (
    .sel(state_q), .out_0(test_logic_reset), .out_1(run_test_idle), .out_2(select_dr_scan),
    .out_3(select_ir_scan), .out_4(capture_ir), .out_5(shift_ir), .out_6(exit1_ir), .out_7(pause_ir),
    .out_8(exit2_ir), .out_9(update_ir), .out_10(capture_dr), .out_11(shift_dr), .out_12(exit1_dr),
    .out_13(pause_dr), .out_14(exit2_dr), .out_15(update_dr));
  LookUpTable #(.Bits(4)) state_lut (
    .in0(TMS), .in1(state_q[0]), .in2(state_q[1]), .in3(state_q[2]), .in4(state_q[3]), .out(state_lut_out));
  Multiplexer #(.Bits(41)) multiplexer_8 (
    .sel(shift_dr), .in_0({{7{1'b0}}, dmi_data_d, dmi_op_d}), .in_1({TDI, dmi[40:1]}),
    .out({multiplexer_8_out_3, multiplexer_8_out_2, multiplexer_8_out}));
  LookUpTable #(.Bits(2)) lookuptable_1 (
    .in0(ir[0]), .in1(ir[1]), .in2(ir[2]), .in3(ir[3]), .in4(ir[4]), .out(lookuptable_1_out));
  and and_9 (and_9_out, not_2_out, dmi[1]);
  not not_2 (not_2_out, dmi[0]);
  Register #(.Bits(2)) dmi_op (.D(multiplexer_8_out), .C(TCK), .en(dmi_wen), .Q(dmi[1:0]));
  Register #(.Bits(32)) dmi_data (.D(multiplexer_8_out_2), .C(TCK), .en(dmi_wen), .Q(dmi[33:2]));
  Register #(.Bits(7)) u_dmi_addr (.D(multiplexer_8_out_3), .C(TCK), .en(dmi_wen), .Q(dmi[40:34]));
  Multiplexer #(.Selector_Bits(2)) multiplexer_9 (
    .sel(lookuptable_1_out), .in_0(bypass), .in_1(idcode[0]), .in_2(dtmcs[0]), .in_3(dmi[0]),
    .out(multiplexer_9_out));
  Decoder #(.Selector_Bits(2)) decoder_2 (
    .sel(lookuptable_1_out), .out_0(ir_bypass), .out_1(ir_idcode), .out_2(ir_dtmcs), .out_3(ir_dmi));
  not not_3 (not_3_out, TCK);
  Register tdo_latch (.D(tdo_t), .C(not_3_out), .en(1'b1), .Q(TDO));
  Register dmi_op_latch (.D(and_9_out), .C(TCK), .en(dmi_tx_start), .Q(DMI_WRITE));
  Register #(.Bits(7)) dmi_addr_latch (.D(dmi[40:34]), .C(TCK), .en(dmi_tx_start), .Q(DMI_ADDR));
  Register #(.Bits(32)) dmi_wdata_latch (.D(dmi[33:2]), .C(TCK), .en(dmi_tx_start), .Q(DMI_WDATA));
  Multiplexer multiplexer_10 (.sel(shift_ir), .in_0(multiplexer_9_out), .in_1(ir[0]), .out(tdo_t));
  Multiplexer #(.Bits(32)) multiplexer_11 (
    .sel(shift_dr), .in_0({20'h1, dmi_op_d, 10'h71}), .in_1({TDI, dtmcs[31:1]}),
    .out({multiplexer_11_out_6, multiplexer_11_out_5, multiplexer_11_out_4, multiplexer_11_out_3, multiplexer_11_out_2, multiplexer_11_out}));
  Register #(.Bits(4)) dtmcs_version (.D(multiplexer_11_out), .C(TCK), .en(dtcms_wen), .Q(dtmcs[3:0]));
  Register #(.Bits(6)) dtmcs_abits (.D(multiplexer_11_out_2), .C(TCK), .en(dtcms_wen), .Q(dtmcs[9:4]));
  Register #(.Bits(2)) dtmcs_dmistat (.D(multiplexer_11_out_3), .C(TCK), .en(dtcms_wen), .Q(dtmcs[11:10]));
  Register #(.Bits(3)) dtmcs_idle (.D(multiplexer_11_out_4), .C(TCK), .en(dtcms_wen), .Q(dtmcs[14:12]));
  Register dtmcs_reserved0 (.D(multiplexer_11_out_5[15]), .C(TCK), .en(dtcms_wen), .Q(dtmcs[15]));
  Register dtmcs_dmireset (.D(multiplexer_11_out_5[16]), .C(TCK), .en(dtcms_wen), .Q(dtmcs[16]));
  Register dtmcs_dmihardreset (.D(multiplexer_11_out_5[17]), .C(TCK), .en(dtcms_wen), .Q(dtmcs[17]));
  Register #(.Bits(14)) dtmcs_reserved1 (.D(multiplexer_11_out_6), .C(TCK), .en(dtcms_wen), .Q(dtmcs[31:18]));

  // Other names for the same wires on the sheet: dmi_addr_t[6:0] = dmi[40:34]; dmi_busy = DMI_REQ;
  //   dmi_data[31:0] = dmi[33:2]; dmi_op[1:0] = dmi[1:0]; dmi_rdata_t[31:0] = dmi_data_d;
  //   dtmcs_abits[5:0] = dtmcs[9:4]; dtmcs_dmihardreset = dtmcs[17]; dtmcs_dmireset = dtmcs[16];
  //   dtmcs_dmistat[1:0] = dtmcs[11:10]; dmistat[1:0] = dmi_op_d; dtmcs_dmistat_d[1:0] = dmi_op_d;
  //   dtmcs_idle[2:0] = dtmcs[14:12]; dtmcs_reserved0 = dtmcs[15]; dtmcs_reserved1[13:0] = dtmcs[31:18];
  //   dtmcs_version[3:0] = dtmcs[3:0]; idcode_manufid[10:0] = idcode[11:1]; idcode_partnumber[15:0] = idcode[27:12];
  //   idcode_reserved0 = idcode[0]; idcode_version[3:0] = idcode[31:28]

  // Notes on the sheet:
  //   Understanding the TAP
  //   JTAG TAPs manage serial communication between a circuit and an outside device.
  //   The device pulses TCK while holding TMS high or low to navigate a state machine
  //   internal to the TAP. A good diagram of this state machine can be found at:
  //   https://adaptivesupport.amd.com/s/article/3203
  //   (If this goes down or moves, I'm sure you know how to look things up.)
  //   The point of the state machine is to manage shifting, capturing, and updating
  //   two locations. One of these is the ir (instruction register), and the other is the dr
  //   (data register). Of these two, the ir is the only one that is actually a register. The
  //   dr is a more meta construct that represents a multitude of registers, of which
  //   an active one is selected via the value in ir. To additionally complicate things, not
  //   every member of dr is required to be a physical register. Do you know the Unix
  //   "everything-is-a-file" mentality? That's sort of how the members of dr work. 
  //   Technically, they can be normal registers, but most have special behaviours.
  //   The dmi, for example, is a readable and writeable communication channel
  //   defined by the RISC-V debug specification, found here:
  //   https://riscv.org/wp-content/uploads/2024/12/riscv-debug-release.pdf
  //   The dmi is the singular outpoint of this particular TAP, and the only
  //   way for attached debuggers to communicate with the CPU's debug module.
  //   Register Write Enables
  //   We write to IR whenever we're in
  //   capture-ir, shift-ir, or test-logic-reset.
  //   I've implemented these registers
  //   in a way that makes them easy to
  //   deal with under the context of
  //   both shifting and writing by field.
  //   If we should be shifting, we shift.
  //   If we should be writing in parallel,
  //   we write in parallel. It's pretty simple.
  //   ir register
  //   dmi Management
  //   Is the dmi op either a read or write?
  //   We keep dmi-req high until we
  //   get a dmi-ack, so this is effectively dmi-busy.
  //   If we try to send an instruction to dmi while it
  //   is busy, we run into a collision!
  //   We write to one of the data registers
  //   when we're in capture-dr or shift-dr and
  //   the respective id is in ir.
  //   bypass register
  //   A dmireset being written to dtmcs
  //   means that we should clear dmistat.
  //   We modify dmistat on collision error
  //   and explicit clearing.
  //   We reflect the busy status in dmistat
  //   in a non-sticky way for nop usage.
  //   Inputs
  //   Things to load into registers on capture and test-logic-reset
  //   IR should point at IDCODE on test-logic-reset, and
  //   should contain the lower bits 0b01 on capture-ir.
  //   This does both.
  //   The bypass register should be 0 on its capture-dr.
  //   We don't have a real idcode, but we can make one up.
  //   We capture dmistat and rdata. The address doesn't matter,
  //   since we're capturing a result and not issuing a command.
  //   idcode register
  //   The clock for the state machine.
  //   Which of two places to go at each state machine transition.
  //   The bit to shift in (if shifting).
  //   Acknowledgement from the dmi. Indicates operation completion.
  //   The data being read back over the dmi (if reading).
  //   The status of the current operation.
  //   We can start a transation if our
  //   operation is a read or wite, dmi is
  //   not busy, and we don't have any 
  //   sticky error.
  //   If we were doing an operation (so
  //   dmi-req is high) but we've received
  //   an acknowledgement, it's time to
  //   end the transaction.
  //   dmi-req is set high whenever we have
  //   a dmi-tx_start and set low on every
  //   dmi-tx_end
  //   Respectively:
  //   Version 0.13 of debug spec, 
  //   7 bits of address in dmi,
  //   the current error code, a hint to avoid collisions,
  //   and a bunch of dummy or write-only data.
  //   State Machine
  //   We manage the state machine and
  //   decode the current state.
  //   dmi register
  //   contents of state_lut (hex, n*v repeats v):
  //   1,0,1,2,a,3,4,0,5,6,5,6,7,9,7,8,5,9,1,2,b,c,b,c,d,f,d,e,b,f,1,2
  //   IR Decoding & tdo
  //   Outputs
  //   tdo is latched out on the falling TCK.
  //   We hold dmi-req high from the moment
  //   we issue a command to when we're
  //   told it's been completed.
  //   Whether we're writing or reading for
  //   this transaction.
  //   Which address in the debug module
  //   we're reading from or writing to.
  //   The data we might be writing
  //   to a location in the debug module.
  //   We decode ir and determine what
  //   should go in tdo.
  //   contents of lookuptable_1 (hex, n*v repeats v):
  //   0,1,14*0,2,3
  //   dtcms register
endmodule
