// Digital circuit BIT-EXPAND-32.dig as structural Verilog
module BIT_EXPAND_32 (
  input  I,
  output [31:0] O
);

  // Pins of 1 and 32 bits meet at {32{I}}

  assign O = {32{I}};

  // Notes on the sheet:
  //   BIT-EXPAND-32
endmodule
