// Digital circuit MS-RV-PCU.dig as structural Verilog
module MS_RV_PCU (
  input  [29:0] Immed,
  input  br_jmp,
  input  CLK,
  input  [29:0] ALU_out,
  input  JALR,
  output [31:0] PC,
  output [31:0] PC_plus4
);

  wire [31:0] multiplexer_1_out, multiplexer_2_out;

  Multiplexer #(.Bits(30)) multiplexer_1 (.sel(br_jmp), .in_0(30'h4), .in_1(Immed), .out(multiplexer_1_out[29:0]));
  Add #(.Bits(32)) PC_Incr (.b(multiplexer_1_out), .c_i(1'b0), .s(PC_plus4));  // open: a, c_o
  Multiplexer #(.Bits(30)) multiplexer_2 (
    .in_0(PC_plus4[29:0]), .in_1(ALU_out), .out(multiplexer_2_out[29:0]));  // open: sel
  D_FF #(.Bits(32)) u_PC (.D(multiplexer_2_out), .C(CLK), .Q(PC));  // open: nQ
  // Pins of 30 and 32 bits meet at multiplexer_2_out
  // Pins of 30 and 32 bits meet at multiplexer_1_out
  // Pins of 30 and 32 bits meet at PC_plus4
  // Pins of 30 and 32 bits meet at 32'h4
  // Pins of 1 and 30 bits meet at ALU_out

  // Other names for the same wires on the sheet: is_jalr = JALR; jalr_dest[29:0] = ALU_out

  // Notes on the sheet:
  //   PROCESSOR CONTROL UNIT (PCU)
  //   Lowest 1 bit is 0 to allow for 16-bit instructions
  //   Next PC adds 4 (currently ignoring 16-bit instr)
  //   /31
endmodule
