// Digital circuit RV5-BRANCH-COND-GEN.dig as structural Verilog
module RV5_BRANCH_COND_GEN (
  input  carry,
  input  eq,
  input  slt,
  input  [2:0] funct3,
  input  branch_sel,
  input  jal_sel,
  output br_jmp
);

  wire and_1_out, br_cond, not_1_out, not_2_out, not_3_out;

  Multiplexer #(.Selector_Bits(3)) multiplexer_1 (
    .sel(funct3), .in_0(eq), .in_1(not_1_out), .in_2(1'b0), .in_3(1'b0), .in_4(slt), .in_5(not_2_out),
    .in_6(not_3_out), .in_7(carry), .out(br_cond));
  not not_1 (not_1_out, eq);
  not not_2 (not_2_out, slt);
  not not_3 (not_3_out, carry);
  and and_1 (and_1_out, branch_sel, br_cond);
  or or_1 (br_jmp, and_1_out, jal_sel);

  // Notes on the sheet:
  //   RV5-BRANCH-COND-GEN
  //   br-cond = is the conditional jump condition met?
  //   Branch funct3 legend
  //   0: beq
  //   1: bne
  //   2: reserved
  //   3: reserved
  //   4: blt
  //   5: bge
  //   6: bltu
  //   7: bgeu
  //   br-jmp = should we branch/jump?
  //   (Excluding jalr, since that's an
  //   absolute jump and we handle it
  //   differently than relative jumps in
  //   the PCU.)
endmodule
