// Digital circuit RV5-ALU-CONTROL.dig as structural Verilog
module RV5_ALU_CONTROL (
  input  is_op,
  input  is_op_imm,
  input  is_lui,
  input  is_auipc,
  input  [2:0] funct3,
  input  inst30,
  output reg_wen,
  output [1:0] alu_asel,
  output alu_bsel,
  output [2:0] imm_sel,
  output [3:0] alu_op
);

  wire and_1_out, and_2_out, and_3_out, and_4_out, and_5_out, is_op_is_op_imm, nor_1_out, not_1_out,
       not_2_out, or_3_out;

  or or_1 (is_op_is_op_imm, is_op, is_op_imm);
  or or_2 (imm_sel[1], is_lui, is_auipc);
  nor nor_1 (nor_1_out, funct3[0], funct3[1], funct3[2]);
  and and_1 (and_1_out, inst30, nor_1_out);
  not not_1 (not_1_out, funct3[2]);
  not not_2 (not_2_out, funct3[1]);
  and and_2 (and_2_out, is_op, and_1_out);
  or or_3 (or_3_out, inst30, not_1_out);
  and and_3 (and_3_out, funct3[0], not_2_out);
  and and_4 (and_4_out, or_3_out, and_3_out);
  or or_4 (alu_bsel, is_op_imm, is_lui, is_auipc);
  and and_5 (and_5_out, is_op_is_op_imm, and_4_out);
  or or_5 (reg_wen, is_op_is_op_imm, imm_sel[1]);
  or or_6 (alu_op[3], and_2_out, and_5_out);
  Multiplexer #(.Bits(3)) multiplexer_1 (.sel(is_op_is_op_imm), .in_0(3'b000), .in_1(funct3), .out(alu_op[2:0]));

  assign alu_asel = {is_lui, is_auipc};
  assign {imm_sel[2], imm_sel[0]} = {1'b0, imm_sel[1]};

  // Other names for the same wires on the sheet: alu_op1[2:0] = alu_op[2:0]; alu_op2 = alu_op[3];
  //   is_lui_is_auipc = imm_sel[1]

  // Notes on the sheet:
  //   RV5-ALU-CONTROL
  //   These turn out to be useful:
  //   All of the cases here involve writing
  //   to a register.
  //   For auipc we want the PC to be the first input of the ALU.
  //   For lui, we want the first input to be zero.
  //   There are some cases where we want the second input
  //   of the ALU to be the immediate.
  //   Only lui and auipc here need U-type immediates.
  //   Everything else we're handling here need I-types.
  //   We can use funct3 as the main alu operation in most
  //   cases. However, auipc and lui need a forced addition.
  //   We figure out whether we're subtracting or, (if this
  //   is a shift instruction) our shift direction.
endmodule
