// Digital circuit RV5-MEM-CONTROL.dig as structural Verilog
module RV5_MEM_CONTROL (
  input  is_load,
  input  is_store,
  input  [2:0] funct3,
  output mem_wen,
  output mem_ren,
  output reg_wen,
  output [1:0] wb_sel,
  output alu_bsel,
  output [2:0] imm_sel,
  output mem_b,
  output mem_h,
  output ld_signext
);

  wire and_1_out, nor_1_out, not_1_out, not_2_out;

  or or_1 (alu_bsel, is_load, is_store);
  nor nor_1 (nor_1_out, funct3[0], funct3[1]);
  not not_1 (not_1_out, funct3[1]);
  Multiplexer multiplexer_1 (.sel(alu_bsel), .in_0(1'b0), .in_1(nor_1_out), .out(mem_b));
  and and_1 (and_1_out, not_1_out, funct3[0]);
  Multiplexer multiplexer_2 (.sel(alu_bsel), .in_0(1'b0), .in_1(and_1_out), .out(mem_h));
  not not_2 (not_2_out, funct3[2]);
  and and_2 (ld_signext, is_load, not_2_out);

  assign imm_sel = {2'b00, is_store};
  assign mem_ren = is_load;
  assign mem_wen = is_store;
  assign reg_wen = is_load;
  assign wb_sel = {is_load, 1'b0};

  // Notes on the sheet:
  //   RV5-MEM-CONTROL
  //   If we're storing, we need
  //   to be able to write to memory.
  //   If we're loading, we need to be
  //   able to read from memory and
  //   write to our destination register.
  //   If we're loading, we need the writeback
  //   to select memory.
  //   We use an immediate offset whenever we
  //   load or store.
  //   If storing we need an S-type immediate.
  //   (I-type is default, so we leave it be for
  //   load).
  //   We parse out our loading characteristics:
  //   whether we're loading a byte, a half, and
  //   whether we need to sign extend.
endmodule
