// Digital circuit RV5-OPCODE-DECODE.dig as structural Verilog
module RV5_OPCODE_DECODE (
  input  [6:0] opcode,
  output is_load,
  output is_op_imm,
  output is_auipc,
  output is_store,
  output is_op,
  output is_lui,
  output is_branch,
  output is_jalr,
  output is_jal,
  output is_system
);

  RV5_OPCODE_DECODE rv5_opcode_decode_1 (
    .op6(opcode[6]), .op5(opcode[5]), .op4(opcode[4]), .op3(opcode[3]), .op2(opcode[2]), .op1(opcode[1]),
    .op0(opcode[0]), .is_load(is_load), .is_op_imm(is_op_imm), .is_auipc(is_auipc), .is_store(is_store),
    .is_op(is_op), .is_lui(is_lui), .is_branch(is_branch), .is_jalr(is_jalr), .is_jal(is_jal),
    .is_system(is_system));

  // Notes on the sheet:
  //   RV5-OPCODE-DECODE
  //   This parses the opcode field of the risc-v instruction.
  //   Really, this field represents what is called the "major opcode".
  //   I think it's called "opcode" in instruction layout diagrams in the
  //   spec for brevity.
  //   This block contains the actual logic.
  //   I like to keep it encapsulated like
  //   this because I synthesize it from a
  //   script-generated LUT. This layout
  //   lets me cleanly separate what is manually
  //   authored and what is synthesized. What
  //   if my opcode splitting and opcode description
  //   were in there and I regenerated for some
  //   reason?
  //   That would suck! It would be gone!
endmodule
