// Digital circuit _RV5-OPCODE-DECODE.dig as structural Verilog
module RV5_OPCODE_DECODE (
  input  op6,
  input  op5,
  input  op4,
  input  op3,
  input  op2,
  input  op1,
  input  op0,
  output is_load,
  output is_op_imm,
  output is_auipc,
  output is_store,
  output is_op,
  output is_lui,
  output is_branch,
  output is_jalr,
  output is_jal,
  output is_system
);

  wire and_1_out, and_2_out, and_3_out, and_4_out, and_5_out, and_6_out, and_7_out, and_8_out, and_9_out,
       and_10_out, and_11_out, and_12_out, and_13_out, and_14_out, and_15_out, and_16_out, and_17_out,
       and_18_out, and_19_out, and_20_out, and_21_out, and_22_out, and_23_out, and_24_out, and_25_out,
       and_26_out, and_27_out, and_28_out, and_29_out, and_30_out, and_31_out, and_32_out, and_33_out,
       and_34_out, and_35_out, and_36_out, and_37_out, and_38_out, and_39_out, and_40_out, and_41_out,
       and_42_out, and_43_out, and_44_out, and_45_out, and_46_out, and_47_out, and_48_out, and_49_out,
       and_50_out, not_1_out, not_2_out, not_3_out, not_4_out, not_5_out;

  not not_1 (not_1_out, op6);
  not not_2 (not_2_out, op5);
  not not_3 (not_3_out, op4);
  not not_4 (not_4_out, op3);
  not not_5 (not_5_out, op2);
  and and_1 (and_1_out, op1, not_5_out);
  and and_2 (and_2_out, not_4_out, not_3_out);
  and and_3 (and_3_out, not_2_out, not_1_out);
  and and_4 (and_4_out, op1, not_5_out);
  and and_5 (and_5_out, not_4_out, op4);
  and and_6 (and_6_out, not_2_out, not_1_out);
  and and_7 (and_7_out, op1, op2);
  and and_8 (and_8_out, not_4_out, op4);
  and and_9 (and_9_out, not_2_out, not_1_out);
  and and_10 (and_10_out, op1, not_5_out);
  and and_11 (and_11_out, not_4_out, not_3_out);
  and and_12 (and_12_out, op5, not_1_out);
  and and_13 (and_13_out, op1, not_5_out);
  and and_14 (and_14_out, not_4_out, op4);
  and and_15 (and_15_out, op5, not_1_out);
  and and_16 (and_16_out, op1, op2);
  and and_17 (and_17_out, not_4_out, op4);
  and and_18 (and_18_out, op5, not_1_out);
  and and_19 (and_19_out, op1, not_5_out);
  and and_20 (and_20_out, not_4_out, not_3_out);
  and and_21 (and_21_out, op5, op6);
  and and_22 (and_22_out, op1, op2);
  and and_23 (and_23_out, not_4_out, not_3_out);
  and and_24 (and_24_out, op5, op6);
  and and_25 (and_25_out, op1, op2);
  and and_26 (and_26_out, op3, not_3_out);
  and and_27 (and_27_out, op5, op6);
  and and_28 (and_28_out, op1, not_5_out);
  and and_29 (and_29_out, not_4_out, op4);
  and and_30 (and_30_out, op5, op6);
  and and_31 (and_31_out, op0, and_1_out);
  and and_32 (and_32_out, and_2_out, and_3_out);
  and and_33 (and_33_out, op0, and_4_out);
  and and_34 (and_34_out, and_5_out, and_6_out);
  and and_35 (and_35_out, op0, and_7_out);
  and and_36 (and_36_out, and_8_out, and_9_out);
  and and_37 (and_37_out, op0, and_10_out);
  and and_38 (and_38_out, and_11_out, and_12_out);
  and and_39 (and_39_out, op0, and_13_out);
  and and_40 (and_40_out, and_14_out, and_15_out);
  and and_41 (and_41_out, op0, and_16_out);
  and and_42 (and_42_out, and_17_out, and_18_out);
  and and_43 (and_43_out, op0, and_19_out);
  and and_44 (and_44_out, and_20_out, and_21_out);
  and and_45 (and_45_out, op0, and_22_out);
  and and_46 (and_46_out, and_23_out, and_24_out);
  and and_47 (and_47_out, op0, and_25_out);
  and and_48 (and_48_out, and_26_out, and_27_out);
  and and_49 (and_49_out, op0, and_28_out);
  and and_50 (and_50_out, and_29_out, and_30_out);
  and and_51 (is_load, and_31_out, and_32_out);
  and and_52 (is_op_imm, and_33_out, and_34_out);
  and and_53 (is_auipc, and_35_out, and_36_out);
  and and_54 (is_store, and_37_out, and_38_out);
  and and_55 (is_op, and_39_out, and_40_out);
  and and_56 (is_lui, and_41_out, and_42_out);
  and and_57 (is_branch, and_43_out, and_44_out);
  and and_58 (is_jalr, and_45_out, and_46_out);
  and and_59 (is_jal, and_47_out, and_48_out);
  and and_60 (is_system, and_49_out, and_50_out);
endmodule
