// Digital circuit RV5-CONTROL-LOGIC.dig as structural Verilog
module RV5_CONTROL_LOGIC (
  input  [6:0] opcode,
  input  [2:0] funct3,
  input  [11:0] funct12,
  output [2:0] imm_sel,
  output reg_wen,
  output [1:0] wb_sel,
  output ram_wen,
  output ram_ren,
  output ram_b,
  output ram_h,
  output ld_signext,
  output [1:0] alu_asel,
  output [2:0] alu_op,
  output alu_bsel,
  output alu_mod,
  output branch_sel,
  output jal_sel,
  output jalr_sel,
  output csr_wen,
  output csr_opset,
  output csr_opclear,
  output csr_useimm,
  output ecall_sel,
  output ebreak_sel,
  output mret_sel,
  output dret_sel
);

  wire alu_ctrl_bsel, alu_ctrl_mod, alu_ctrl_reg_wen, br_ctrl_mod, jump_ctrl_bsel, jump_ctrl_reg_wen,
       mem_ctrl_bsel, mem_ctrl_reg_wen, rv5_opcode_decode_1_is_auipc, rv5_opcode_decode_1_is_branch,
       rv5_opcode_decode_1_is_jal, rv5_opcode_decode_1_is_jalr, rv5_opcode_decode_1_is_load,
       rv5_opcode_decode_1_is_lui, rv5_opcode_decode_1_is_op, rv5_opcode_decode_1_is_opimm,
       rv5_opcode_decode_1_is_store, rv5_opcode_decode_1_is_system, sys_ctrl_reg_wen;
  wire [1:0] alu_ctrl_asel, jump_ctrl_asel, jump_ctrl_wb_sel, mem_ctrl_wb_sel, sys_ctrl_wb_sel;
  wire [2:0] alu_ctrl_imm_sel, alu_ctrl_op, br_ctrl_imm_sel, br_ctrl_op, jump_ctrl_imm_sel, mem_ctrl_imm_sel;

  RV5_OPCODE_DECODE rv5_opcode_decode_1 (
    .opcode(opcode), .is_load(rv5_opcode_decode_1_is_load), .is_opimm(rv5_opcode_decode_1_is_opimm),
    .is_auipc(rv5_opcode_decode_1_is_auipc), .is_store(rv5_opcode_decode_1_is_store),
    .is_op(rv5_opcode_decode_1_is_op), .is_lui(rv5_opcode_decode_1_is_lui),
    .is_branch(rv5_opcode_decode_1_is_branch), .is_jalr(rv5_opcode_decode_1_is_jalr),
    .is_jal(rv5_opcode_decode_1_is_jal), .is_system(rv5_opcode_decode_1_is_system));
  RV5_MEM_CONTROL rv5_mem_control_1 (
    .is_load(rv5_opcode_decode_1_is_load), .is_store(rv5_opcode_decode_1_is_store), .funct3(funct3),
    .ram_wen(ram_wen), .ram_ren(ram_ren), .reg_wen(mem_ctrl_reg_wen), .wb_sel(mem_ctrl_wb_sel),
    .alu_bsel(mem_ctrl_bsel), .imm_sel(mem_ctrl_imm_sel), .ram_b(ram_b), .ram_h(ram_h),
    .ld_signext(ld_signext));
  RV5_ALU_CONTROL rv5_alu_control_1 (
    .is_op(rv5_opcode_decode_1_is_op), .is_op_imm(rv5_opcode_decode_1_is_opimm),
    .is_lui(rv5_opcode_decode_1_is_lui), .is_auipc(rv5_opcode_decode_1_is_auipc), .funct3(funct3),
    .inst30(funct12[10]), .reg_wen(alu_ctrl_reg_wen), .alu_asel(alu_ctrl_asel), .alu_bsel(alu_ctrl_bsel),
    .imm_sel(alu_ctrl_imm_sel), .alu_op(alu_ctrl_op), .alu_mod(alu_ctrl_mod));
  RV5_BRANCH_CONTROL rv5_branch_control_1 (
    .is_branch(rv5_opcode_decode_1_is_branch), .funct3(funct3), .branch_sel(branch_sel),
    .alu_mod(br_ctrl_mod), .alu_op(br_ctrl_op), .imm_sel(br_ctrl_imm_sel));
  RV5_JUMP_CONTROL rv5_jump_control_1 (
    .is_jalr(rv5_opcode_decode_1_is_jalr), .is_jal(rv5_opcode_decode_1_is_jal), .reg_wen(jump_ctrl_reg_wen),
    .wb_sel(jump_ctrl_wb_sel), .alu_asel(jump_ctrl_asel), .alu_bsel(jump_ctrl_bsel),
    .imm_sel(jump_ctrl_imm_sel), .jal_sel(jal_sel), .jalr_sel(jalr_sel));
  RV5_SYSTEM_CONTROL rv5_system_control_1 (
    .is_system(rv5_opcode_decode_1_is_system), .funct12(funct12), .funct3(funct3),
    .reg_wen(sys_ctrl_reg_wen), .wb_sel(sys_ctrl_wb_sel), .csr_wen(csr_wen), .csr_opset(csr_opset),
    .csr_opclear(csr_opclear), .csr_useimm(csr_useimm), .is_ecall(ecall_sel), .is_ebreak(ebreak_sel),
    .is_mret(mret_sel), .is_dret(dret_sel));
  or or_1 (reg_wen, mem_ctrl_reg_wen, alu_ctrl_reg_wen, jump_ctrl_reg_wen, sys_ctrl_reg_wen);
  assign wb_sel = mem_ctrl_wb_sel | jump_ctrl_wb_sel | sys_ctrl_wb_sel;  // Or or_2, 2 bits wide
  assign alu_asel = alu_ctrl_asel | jump_ctrl_asel;  // Or or_3, 2 bits wide
  or or_4 (alu_bsel, mem_ctrl_bsel, alu_ctrl_bsel, jump_ctrl_bsel);
  assign imm_sel = mem_ctrl_imm_sel | alu_ctrl_imm_sel | br_ctrl_imm_sel | jump_ctrl_imm_sel;  // Or or_5, 3 bits wide
  assign alu_op = alu_ctrl_op | br_ctrl_op;  // Or or_6, 3 bits wide
  or or_7 (alu_mod, alu_ctrl_mod, br_ctrl_mod);

  // Other names for the same wires on the sheet: inst30 = funct12[10]

  // Notes on the sheet:
  //   RV5-CONTROL
  //   With the opcode we can determine the
  //   category of instruction we're working with
  //   and handle it with the relevant sub-circuit.
  //   Sub-circuits that are non-active output zeros
  //   so that we can just sum everything together
  //   to get our final control signal outputs.
endmodule
