// Digital circuit RV5-JUMP-CONTROL.dig as structural Verilog
module RV5_JUMP_CONTROL (
  input  is_jalr,
  input  is_jal,
  output reg_wen,
  output [1:0] wb_sel,
  output [1:0] alu_asel,
  output alu_bsel,
  output [2:0] imm_sel,
  output jal_sel,
  output jalr_sel
);

  or or_1 (alu_bsel, is_jalr, is_jal);

  assign alu_asel = {1'b0, is_jal};
  assign imm_sel = {is_jal, 2'b00};
  assign jal_sel = is_jal;
  assign jalr_sel = is_jalr;
  assign reg_wen = alu_bsel;
  assign wb_sel = {1'b0, alu_bsel};

  // Notes on the sheet:
  //   RV5-JUMP-CONTROL
  //   Both jal and jalr need to save into rd.
  //   Both need the immediate.
  //   We need to grab pc+4 to store in rd.
  //   Unlike jalr, jal is PC-relative.
  //   Jal needs a J-type immediate.
endmodule
