// Digital circuit _RV5-CSR-ADDR-DECODE.dig as structural Verilog
module RV5_CSR_ADDR_DECODE (
  input  addr11,
  input  addr10,
  input  addr9,
  input  addr8,
  input  addr7,
  input  addr6,
  input  addr5,
  input  addr4,
  input  addr3,
  input  addr2,
  input  addr1,
  input  addr0,
  output _300,
  output _301,
  output _305,
  output _340,
  output _341,
  output _342,
  output _7b0,
  output _7b1,
  output _7b2,
  output _7b3
);

  wire and_1_out, and_2_out, and_3_out, and_4_out, and_5_out, and_6_out, and_7_out, and_8_out, and_9_out,
       and_10_out, and_11_out, and_12_out, and_13_out, and_14_out, and_15_out, and_16_out, and_17_out,
       and_18_out, and_19_out, and_20_out, and_21_out, and_22_out, and_23_out, and_24_out, and_25_out,
       and_26_out, and_27_out, and_28_out, and_29_out, and_30_out, and_31_out, and_32_out, and_33_out,
       and_34_out, and_35_out, and_36_out, and_37_out, and_38_out, and_39_out, and_40_out, and_41_out,
       and_42_out, and_43_out, and_44_out, and_45_out, and_46_out, and_47_out, and_48_out, and_49_out,
       and_50_out, and_51_out, and_52_out, and_53_out, and_54_out, and_55_out, and_56_out, and_57_out,
       and_58_out, and_59_out, and_60_out, and_61_out, and_62_out, and_63_out, and_64_out, and_65_out,
       and_66_out, and_67_out, and_68_out, and_69_out, and_70_out, and_71_out, and_72_out, and_73_out,
       and_74_out, and_75_out, and_76_out, and_77_out, and_78_out, and_79_out, and_80_out, and_81_out,
       and_82_out, and_83_out, and_84_out, and_85_out, and_86_out, and_87_out, and_88_out, and_89_out,
       and_90_out, and_91_out, and_92_out, and_93_out, and_94_out, and_95_out, and_96_out, and_97_out,
       and_98_out, and_99_out, and_100_out, not_1_out, not_2_out, not_3_out, not_4_out, not_5_out, not_6_out,
       not_7_out, not_8_out, not_9_out, not_10_out;

  not not_1 (not_1_out, addr11);
  not not_2 (not_2_out, addr10);
  not not_3 (not_3_out, addr7);
  not not_4 (not_4_out, addr6);
  not not_5 (not_5_out, addr5);
  not not_6 (not_6_out, addr4);
  not not_7 (not_7_out, addr3);
  not not_8 (not_8_out, addr2);
  not not_9 (not_9_out, addr1);
  not not_10 (not_10_out, addr0);
  and and_1 (and_1_out, not_10_out, not_9_out);
  and and_2 (and_2_out, not_2_out, not_1_out);
  and and_3 (and_3_out, not_8_out, not_7_out);
  and and_4 (and_4_out, not_6_out, not_5_out);
  and and_5 (and_5_out, not_4_out, not_3_out);
  and and_6 (and_6_out, addr8, addr9);
  and and_7 (and_7_out, addr0, not_9_out);
  and and_8 (and_8_out, not_2_out, not_1_out);
  and and_9 (and_9_out, not_8_out, not_7_out);
  and and_10 (and_10_out, not_6_out, not_5_out);
  and and_11 (and_11_out, not_4_out, not_3_out);
  and and_12 (and_12_out, addr8, addr9);
  and and_13 (and_13_out, addr0, not_9_out);
  and and_14 (and_14_out, not_2_out, not_1_out);
  and and_15 (and_15_out, addr2, not_7_out);
  and and_16 (and_16_out, not_6_out, not_5_out);
  and and_17 (and_17_out, not_4_out, not_3_out);
  and and_18 (and_18_out, addr8, addr9);
  and and_19 (and_19_out, not_10_out, not_9_out);
  and and_20 (and_20_out, not_2_out, not_1_out);
  and and_21 (and_21_out, not_8_out, not_7_out);
  and and_22 (and_22_out, not_6_out, not_5_out);
  and and_23 (and_23_out, addr6, not_3_out);
  and and_24 (and_24_out, addr8, addr9);
  and and_25 (and_25_out, addr0, not_9_out);
  and and_26 (and_26_out, not_2_out, not_1_out);
  and and_27 (and_27_out, not_8_out, not_7_out);
  and and_28 (and_28_out, not_6_out, not_5_out);
  and and_29 (and_29_out, addr6, not_3_out);
  and and_30 (and_30_out, addr8, addr9);
  and and_31 (and_31_out, not_10_out, addr1);
  and and_32 (and_32_out, not_2_out, not_1_out);
  and and_33 (and_33_out, not_8_out, not_7_out);
  and and_34 (and_34_out, not_6_out, not_5_out);
  and and_35 (and_35_out, addr6, not_3_out);
  and and_36 (and_36_out, addr8, addr9);
  and and_37 (and_37_out, not_10_out, not_9_out);
  and and_38 (and_38_out, addr10, not_1_out);
  and and_39 (and_39_out, not_8_out, not_7_out);
  and and_40 (and_40_out, addr4, addr5);
  and and_41 (and_41_out, not_4_out, addr7);
  and and_42 (and_42_out, addr8, addr9);
  and and_43 (and_43_out, addr0, not_9_out);
  and and_44 (and_44_out, addr10, not_1_out);
  and and_45 (and_45_out, not_8_out, not_7_out);
  and and_46 (and_46_out, addr4, addr5);
  and and_47 (and_47_out, not_4_out, addr7);
  and and_48 (and_48_out, addr8, addr9);
  and and_49 (and_49_out, not_10_out, addr1);
  and and_50 (and_50_out, addr10, not_1_out);
  and and_51 (and_51_out, not_8_out, not_7_out);
  and and_52 (and_52_out, addr4, addr5);
  and and_53 (and_53_out, not_4_out, addr7);
  and and_54 (and_54_out, addr8, addr9);
  and and_55 (and_55_out, addr0, addr1);
  and and_56 (and_56_out, addr10, not_1_out);
  and and_57 (and_57_out, not_8_out, not_7_out);
  and and_58 (and_58_out, addr4, addr5);
  and and_59 (and_59_out, not_4_out, addr7);
  and and_60 (and_60_out, addr8, addr9);
  and and_61 (and_61_out, and_1_out, and_2_out);
  and and_62 (and_62_out, and_3_out, and_4_out);
  and and_63 (and_63_out, and_5_out, and_6_out);
  and and_64 (and_64_out, and_7_out, and_8_out);
  and and_65 (and_65_out, and_9_out, and_10_out);
  and and_66 (and_66_out, and_11_out, and_12_out);
  and and_67 (and_67_out, and_13_out, and_14_out);
  and and_68 (and_68_out, and_15_out, and_16_out);
  and and_69 (and_69_out, and_17_out, and_18_out);
  and and_70 (and_70_out, and_19_out, and_20_out);
  and and_71 (and_71_out, and_21_out, and_22_out);
  and and_72 (and_72_out, and_23_out, and_24_out);
  and and_73 (and_73_out, and_25_out, and_26_out);
  and and_74 (and_74_out, and_27_out, and_28_out);
  and and_75 (and_75_out, and_29_out, and_30_out);
  and and_76 (and_76_out, and_31_out, and_32_out);
  and and_77 (and_77_out, and_33_out, and_34_out);
  and and_78 (and_78_out, and_35_out, and_36_out);
  and and_79 (and_79_out, and_37_out, and_38_out);
  and and_80 (and_80_out, and_39_out, and_40_out);
  and and_81 (and_81_out, and_41_out, and_42_out);
  and and_82 (and_82_out, and_43_out, and_44_out);
  and and_83 (and_83_out, and_45_out, and_46_out);
  and and_84 (and_84_out, and_47_out, and_48_out);
  and and_85 (and_85_out, and_49_out, and_50_out);
  and and_86 (and_86_out, and_51_out, and_52_out);
  and and_87 (and_87_out, and_53_out, and_54_out);
  and and_88 (and_88_out, and_55_out, and_56_out);
  and and_89 (and_89_out, and_57_out, and_58_out);
  and and_90 (and_90_out, and_59_out, and_60_out);
  and and_91 (and_91_out, and_62_out, and_63_out);
  and and_92 (and_92_out, and_65_out, and_66_out);
  and and_93 (and_93_out, and_68_out, and_69_out);
  and and_94 (and_94_out, and_71_out, and_72_out);
  and and_95 (and_95_out, and_74_out, and_75_out);
  and and_96 (and_96_out, and_77_out, and_78_out);
  and and_97 (and_97_out, and_80_out, and_81_out);
  and and_98 (and_98_out, and_83_out, and_84_out);
  and and_99 (and_99_out, and_86_out, and_87_out);
  and and_100 (and_100_out, and_89_out, and_90_out);
  and and_101 (_300, and_61_out, and_91_out);
  and and_102 (_301, and_64_out, and_92_out);
  and and_103 (_305, and_67_out, and_93_out);
  and and_104 (_340, and_70_out, and_94_out);
  and and_105 (_341, and_73_out, and_95_out);
  and and_106 (_342, and_76_out, and_96_out);
  and and_107 (_7b0, and_79_out, and_97_out);
  and and_108 (_7b1, and_82_out, and_98_out);
  and and_109 (_7b2, and_85_out, and_99_out);
  and and_110 (_7b3, and_88_out, and_100_out);
endmodule
