// Digital circuit RV5-CSR.dig as structural Verilog
module RV5_CSR (
  input  clk,
  input  [11:0] addr,
  input  [31:0] wdata,
  input  wen,
  input  [31:0] pc,
  input  ecall_sel,
  input  mret_sel,
  input  ebreak_sel,
  input  is_debug,
  input  haltreq,
  output [31:0] csr_out,
  output [31:0] mtvec,
  output [31:0] mepc,
  output [31:0] dcsr,
  output [31:0] dpc
);

  wire and_1_out, and_2_out, and_3_out, and_4_out, and_5_out, and_6_out, and_7_out, and_8_out, and_9_out,
       and_10_out, and_11_out, dcsr_sel, dpc_sel, dscratch0_sel, dscratch1_sel, mcause_sel, mepc_sel,
       misa_sel, mscratch_sel, mstatus_sel, mtvec_sel, not_1_out, not_2_out, not_3_out, or_1_out, or_2_out,
       or_3_out, or_4_out, or_5_out, or_6_out;
  wire [31:0] dscratch0, dscratch1, mcause, mscratch, mstatus, multiplexer_1_out, multiplexer_2_out,
       multiplexer_3_out, multiplexer_4_out, multiplexer_5_out;

  // AddressDecoder #(.addressDecoderRules("0x300: 300\n0x301: 301\n0x305: 305\n0x340: 340\n0x341: 341\n0x342: 342\n0x7b0: 7b0\n0x7b1: 7b1\n0x7b2: 7b2\n0x7b3: 7b3"), .Bits(12)) addressdecoder_1: pin names not known; wires that end beside it: addr, mstatus_sel, misa_sel, mtvec_sel, mscratch_sel, mepc_sel, mcause_sel, dcsr_sel, dpc_sel, dscratch0_sel, dscratch1_sel
  not not_1 (not_1_out, dcsr[15]);
  not not_2 (not_2_out, is_debug);
  and and_1 (and_1_out, wen, mstatus_sel);
  and and_2 (and_2_out, wen, mtvec_sel);
  and and_3 (and_3_out, wen, mscratch_sel);
  and and_4 (and_4_out, wen, dscratch0_sel);
  and and_5 (and_5_out, wen, dscratch1_sel);
  and and_6 (and_6_out, not_1_out, ebreak_sel, not_2_out);
  or or_1 (or_1_out, ecall_sel, and_6_out);
  and and_7 (and_7_out, dcsr[15], ebreak_sel, not_3_out);
  not not_3 (not_3_out, is_debug);
  Register #(.Bits(32)) u_mstatus (.D(wdata), .C(clk), .en(and_1_out), .Q(mstatus));
  Register #(.Bits(32)) u_mtvec (.D(wdata), .C(clk), .en(and_2_out), .Q(mtvec));
  Register #(.Bits(32)) u_mscratch (.D(wdata), .C(clk), .en(and_3_out), .Q(mscratch));
  Register #(.Bits(32)) u_dscratch0 (.D(wdata), .C(clk), .en(and_4_out), .Q(dscratch0));
  Register #(.Bits(32)) u_dscratch1 (.D(wdata), .C(clk), .en(and_5_out), .Q(dscratch1));
  or or_2 (or_2_out, and_7_out, haltreq);
  Multiplexer #(.Bits(32)) multiplexer_1 (.sel(ecall_sel), .in_0(32'h3), .in_1(32'hb), .out(multiplexer_1_out));
  Multiplexer #(.Bits(32)) multiplexer_2 (.sel(or_2_out), .in_0(wdata), .in_1(pc), .out(multiplexer_2_out));
  Multiplexer #(.Bits(32)) multiplexer_3 (.sel(or_1_out), .in_0(wdata), .in_1(pc), .out(multiplexer_3_out));
  Multiplexer #(.Bits(32)) multiplexer_4 (
    .sel(or_1_out), .in_0(wdata), .in_1(multiplexer_1_out), .out(multiplexer_4_out));
  and and_8 (and_8_out, wen, dcsr_sel);
  and and_9 (and_9_out, wen, mepc_sel);
  and and_10 (and_10_out, wen, mcause_sel);
  and and_11 (and_11_out, wen, dpc_sel);
  or or_3 (or_3_out, and_9_out, or_1_out);
  or or_4 (or_4_out, and_10_out, or_1_out);
  Multiplexer #(.Bits(32)) multiplexer_5 (
    .sel(haltreq), .in_0(wdata), .in_1({dcsr[31:9], 3'b011, dcsr[5:2], 2'b11}), .out(multiplexer_5_out));
  or or_5 (or_5_out, and_8_out, haltreq);
  or or_6 (or_6_out, and_11_out, or_2_out);
  Register #(.Bits(32)) u_mepc (.D(multiplexer_3_out), .C(clk), .en(or_3_out), .Q(mepc));
  Register #(.Bits(32)) u_mcause (.D(multiplexer_4_out), .C(clk), .en(or_4_out), .Q(mcause));
  Register #(.Bits(32)) u_dcsr (.D(multiplexer_5_out), .C(clk), .en(or_5_out), .Q(dcsr));
  Register #(.Bits(32)) u_dpc (.D(multiplexer_2_out), .C(clk), .en(or_6_out), .Q(dpc));
  // OneHotMultiplexer #(.Bits(32)) onehotmultiplexer_1: pin names not known; wires that end beside it: mstatus_sel, misa_sel, mtvec_sel, mscratch_sel, mepc_sel, mcause_sel, dcsr_sel, dpc_sel, dscratch0_sel, dscratch1_sel, mstatus, 32'h40000100, mtvec, mscratch, mepc, mcause, dcsr, dpc, dscratch0, dscratch1, csr_out

  // Notes on the sheet:
  //   RV5-CSR
  //   Inputs
  //   Understanding the CSRs
  //   Control Status Registers (CSRs) are special registers that behave in special ways
  //   and are used for special tasks. Each register resides at an address that is
  //   spec-defined. The instructions to access these CSRs are part of the Ziscr
  //   extension.
  //   Address Parsing & Register Select
  //   This is equivilent to _RV5-CSR-ADDR-DECODE,
  //   but much faster in the sim.
  //   Registers
  //   Who would have thought that in the control and status register file
  //   we'd find registers?
  //   The simple ones are simple:
  //   We need to update mepc with
  //   pc and mcause with the right
  //   value when we do an ecall
  //   or relevant ebreak:
  //   We write to the priv and cause fields
  //   when we act on haltreq:
  //   We need to put pc in dpc if we hit
  //   a breakpoint or act on haltreq:
  //   Outputs
  //   There's a few things we'll 
  //   need all of the time:
  //   We can just sum-of-products for the
  //   main output:
  //   (Like ONE-HOT-SEL-32x10 but
  //   faster in the sim.)
endmodule
