// Digital circuit RV5-DEBUG-MODULE.dig as structural Verilog
module RV5_DEBUG_MODULE (
  input  [31:0] dcsr,
  input  clk,
  input  d_regwen,
  input  [31:0] d_rdin,
  input  [31:0] out_dm,
  input  [31:0] ra,
  input  is_debug,
  input  in_progbuf,
  input  d_memwen,
  input  [4:0] d_rd,
  input  [4:0] d_rs1,
  output [4:0] d_rd_2,
  output [4:0] d_rs1_2,
  output [31:0] d_rdin_2,
  output d_regwen_2,
  output d_memwen_2,
  output dmcontrol_resumereq,
  output command_reg_jumpprogbuf,
  output haltreq,
  output [31:0] dm_wdata,
  output dm_wen,
  output [31:0] addr_dm
);

  wire abstractauto_wen, abstractcs_wen, ack_drop, and_5_out, and_8_out, and_9_out, and_11_out, and_12_out,
       and_13_out, and_14_out, and_15_out, and_16_out, and_17_out, and_18_out, and_19_out, and_21_out,
       and_22_out, and_25_out, autoexec, command_exec, command_reg_aarpostincrement, command_reg_arg0wen,
       command_reg_exec, command_reg_postexec, command_reg_regnoinvalid, command_reg_regwen, command_reg_sel,
       command_reg_transfer, command_reg_validtransferex, command_reg_write, command_unsuported_sel,
       command_wen, comparator_1_eq, comparator_2_eq, comparator_3_eq, comparator_4_eq, comparator_5_eq,
       comparator_6_eq, comparator_7_eq, comparator_8_eq, comparator_9_eq, comparator_11_eq,
       comparator_12_gt, comparator_14_lt, comparator_15_gt, d_ff_1_q, d_ff_2_q, d_ff_3_q, d_ff_4_q,
       d_ff_7_nq, dm_ack, dm_done, dmcontrol_ackhavereset, dmcontrol_clrresethaltreq, dmcontrol_dmactive,
       dmcontrol_haltreq, dmcontrol_hartreset, dmcontrol_hasel, dmcontrol_ndmreset, dmcontrol_wen,
       dmi_access, dmi_ren, dmi_req, dmi_req_rise, dmi_wen, dmstatus_allnonexistent, dmstatus_allresumeack,
       dmstatus_allrunning, gdbservervpi_1_p2, gdbservervpi_1_p4, nor_1_out, nor_2_out, not_1_out, not_2_out,
       not_4_out, not_5_out, not_7_out, not_8_out, not_9_out, or_1_out, or_2_out, or_3_out, or_4_out,
       or_6_out, or_7_out, or_8_out, or_9_out, rv5_tap_vpi_1_dmi_req, rv5_tap_vpi_1_dmi_write, sbcs_wen;
  wire [2:0] abstractcs_cmderr, and_23_out, command_reg_aarsize, dmi_rdata_lut_out, dmi_wen_lut_out,
       gdbservervpi_1_p5, multiplexer_8_out, multiplexer_9_out, not_6_out;
  wire [3:3] dmcontrol_rdata;
  wire [4:0] command_reg_gprno;
  wire [6:0] rv5_tap_vpi_1_dmi_addr;
  wire [7:0] command_cmdtype, gdbservervpi_1_p6;
  wire [11:0] abstractauto_autoexecdata;
  wire [15:0] abstractauto_autoexecprogbuf, command_reg_regno;
  wire [15:5] sub_1_s;
  wire [15:12] abstractauto_persistent;
  wire [19:0] dmcontrol_hartsel;
  wire [23:23] multiplexer_10_out;
  wire [30:2] dmcontrol_persistent;
  wire [31:0] command_persistent_q, dmi_memaddr, dmi_rdata, dmi_wdata, multiplexer_1_out;
  wire [40:0] gdbservervpi_1_p1, gdbservervpi_1_p7, gdbservervpi_1_p8;

  // GdbServerVpi #(.openOCDTargetArch("riscv"), .openOCDDebugLevel(3), .jtagVpiWordWidth(41)) gdbservervpi_1: pin names not known; wires that end beside it: gdbservervpi_1_p1, gdbservervpi_1_p2, clk, gdbservervpi_1_p4, gdbservervpi_1_p5, gdbservervpi_1_p6, gdbservervpi_1_p7, gdbservervpi_1_p8
  RV5_TAP_VPI rv5_tap_vpi_1 (
    .CLK(clk), .REQ(gdbservervpi_1_p4), .CMD(gdbservervpi_1_p5), .NBITS(gdbservervpi_1_p6),
    .TMS(gdbservervpi_1_p7), .TDI(gdbservervpi_1_p8), .DMI_ACK(dm_ack), .DMI_RDATA(dmi_rdata),
    .DMI_STATUS({2{in_progbuf}}), .TDO(gdbservervpi_1_p1), .ACK(gdbservervpi_1_p2),
    .DMI_REQ(rv5_tap_vpi_1_dmi_req), .DMI_WDATA(dmi_wdata), .DMI_ADDR(rv5_tap_vpi_1_dmi_addr),
    .DMI_WRITE(rv5_tap_vpi_1_dmi_write));
  Register #(.Bits(32)) u_dmcontrol_persistent (
    .D(dmi_wdata), .C(clk), .en(dmcontrol_wen),
    .Q({dmcontrol_haltreq, dmcontrol_persistent[30], dmcontrol_hartreset, dmcontrol_persistent[28:27], dmcontrol_hasel, dmcontrol_hartsel[9:0], dmcontrol_hartsel[19:10], dmcontrol_persistent[5:2], dmcontrol_ndmreset, dmcontrol_dmactive}));
  and and_1 (dmcontrol_clrresethaltreq, dmcontrol_wen, dmi_wdata[2]);
  and and_2 (dmcontrol_rdata[3], dmcontrol_wen, dmi_wdata[3]);
  and and_3 (dmcontrol_ackhavereset, dmcontrol_wen, dmi_wdata[28]);
  and and_4 (dmcontrol_resumereq, dmcontrol_wen, dmi_wdata[30]);
  and and_5 (and_5_out, dmcontrol_resumereq, dcsr[2]);
  D_FF d_ff_1 (.D(and_5_out), .C(clk), .Q(d_ff_1_q));  // open: nQ
  D_FF d_ff_2 (.D(d_ff_1_q), .C(clk), .Q(d_ff_2_q));  // open: nQ
  D_FF d_ff_3 (.D(rv5_tap_vpi_1_dmi_req), .C(clk), .Q(d_ff_3_q));  // open: nQ
  D_FF d_ff_4 (.D(d_ff_2_q), .C(clk), .Q(d_ff_4_q));  // open: nQ
  D_FF d_ff_5 (.D(d_ff_3_q), .C(clk), .Q(dmi_req));  // open: nQ
  not not_1 (not_1_out, rv5_tap_vpi_1_dmi_write);
  or or_1 (or_1_out, dmcontrol_haltreq, d_ff_4_q);
  and and_6 (dmi_wen, rv5_tap_vpi_1_dmi_write, dmi_req_rise);
  and and_7 (dmi_ren, not_1_out, dmi_req_rise);
  and and_8 (and_8_out, or_1_out, not_2_out);
  not not_2 (not_2_out, is_debug);
  RISING_EDGE rising_edge_1 (.clk(clk), .d(dmi_req), .o(dmi_req_rise));
  RISING_EDGE rising_edge_2 (.clk(clk), .d(and_8_out), .o(haltreq));
  LookUpTable #(.Bits(3)) dmi_rdata_lut (
    .in0(rv5_tap_vpi_1_dmi_addr[0]), .in1(rv5_tap_vpi_1_dmi_addr[1]), .in2(rv5_tap_vpi_1_dmi_addr[2]),
    .in3(rv5_tap_vpi_1_dmi_addr[3]), .in4(rv5_tap_vpi_1_dmi_addr[4]), .in5(rv5_tap_vpi_1_dmi_addr[5]),
    .in6(rv5_tap_vpi_1_dmi_addr[6]), .out(dmi_rdata_lut_out));
  LookUpTable #(.Bits(3)) dmi_wen_lut (
    .in0(rv5_tap_vpi_1_dmi_addr[0]), .in1(rv5_tap_vpi_1_dmi_addr[1]), .in2(rv5_tap_vpi_1_dmi_addr[2]),
    .in3(rv5_tap_vpi_1_dmi_addr[3]), .in4(rv5_tap_vpi_1_dmi_addr[4]), .in5(rv5_tap_vpi_1_dmi_addr[5]),
    .in6(rv5_tap_vpi_1_dmi_addr[6]), .out(dmi_wen_lut_out));
  LookUpTable #(.Bits(32)) dmi_memaddr_lut (
    .in0(rv5_tap_vpi_1_dmi_addr[0]), .in1(rv5_tap_vpi_1_dmi_addr[1]), .in2(rv5_tap_vpi_1_dmi_addr[2]),
    .in3(rv5_tap_vpi_1_dmi_addr[3]), .in4(rv5_tap_vpi_1_dmi_addr[4]), .in5(rv5_tap_vpi_1_dmi_addr[5]),
    .in6(rv5_tap_vpi_1_dmi_addr[6]), .out(dmi_memaddr));
  Multiplexer #(.Selector_Bits(3), .Bits(32)) multiplexer_1 (
    .sel(dmi_rdata_lut_out), .in_0({32{1'b0}}), .in_1(out_dm),
    .in_2({dmcontrol_haltreq, dmcontrol_resumereq, dmcontrol_hartreset, dmcontrol_ackhavereset, 1'b0, dmcontrol_hasel, dmcontrol_hartsel[9:0], dmcontrol_hartsel[19:10], 2'b00, dmcontrol_rdata[3], dmcontrol_clrresethaltreq, dmcontrol_ndmreset, dmcontrol_dmactive}),
    .in_3({{14{1'b0}}, {2{dmstatus_allresumeack}}, {2{dmstatus_allnonexistent}}, 2'b00, {2{dmstatus_allrunning}}, {2{is_debug}}, 8'h82}),
    .in_4(32'h111418), .in_5({19'h4000, in_progbuf, 1'b0, abstractcs_cmderr, 8'h1}), .in_6(32'h20000000),
    .in_7({abstractauto_autoexecprogbuf, 4'b0000, abstractauto_autoexecdata}), .out(multiplexer_1_out));
  Demultiplexer #(.Selector_Bits(3)) demultiplexer_1 (
    .sel(dmi_wen_lut_out), .in(dmi_wen), .out_1(dmcontrol_wen), .out_2(abstractcs_wen), .out_3(command_wen),
    .out_4(sbcs_wen), .out_5(abstractauto_wen));  // open: out_0, out_6, out_7
  and and_9 (and_9_out, dmi_ren, dmi_req_rise);
  or or_2 (or_2_out, dmi_ren, dmi_wen);
  Comparator #(.Bits(32)) comparator_1 (.a(dmi_memaddr), .b(32'h418), .eq(comparator_1_eq));  // open: gt, lt
  Comparator #(.Bits(32)) comparator_2 (.a(dmi_memaddr), .b(32'h10004), .eq(comparator_2_eq));  // open: gt, lt
  Comparator #(.Bits(32)) comparator_3 (.a(dmi_memaddr), .b(32'h10008), .eq(comparator_3_eq));  // open: gt, lt
  Comparator #(.Bits(32)) comparator_4 (.a(dmi_memaddr), .b(32'h1000c), .eq(comparator_4_eq));  // open: gt, lt
  Comparator #(.Bits(32)) comparator_5 (.a(dmi_memaddr), .b(32'h10010), .eq(comparator_5_eq));  // open: gt, lt
  Comparator #(.Bits(32)) comparator_6 (.a(dmi_memaddr), .b(32'h10014), .eq(comparator_6_eq));  // open: gt, lt
  Comparator #(.Bits(32)) comparator_7 (.a(dmi_memaddr), .b(32'h10018), .eq(comparator_7_eq));  // open: gt, lt
  Comparator #(.Bits(32)) comparator_8 (.a(dmi_memaddr), .b(32'h1001c), .eq(comparator_8_eq));  // open: gt, lt
  Comparator #(.Bits(32)) comparator_9 (.a(dmi_memaddr), .b(32'h10020), .eq(comparator_9_eq));  // open: gt, lt
  Register #(.Bits(32)) register_1 (.D(multiplexer_1_out), .C(clk), .en(and_9_out), .Q(dmi_rdata));
  and and_10 (dmi_access, or_2_out, dmi_req_rise);
  and and_11 (and_11_out, comparator_1_eq, dmi_access, abstractauto_autoexecdata[0]);
  and and_12 (and_12_out, comparator_2_eq, dmi_access, abstractauto_autoexecprogbuf[0]);
  and and_13 (and_13_out, comparator_3_eq, dmi_access, abstractauto_autoexecprogbuf[1]);
  and and_14 (and_14_out, comparator_4_eq, dmi_access, abstractauto_autoexecprogbuf[2]);
  and and_15 (and_15_out, comparator_5_eq, dmi_access, abstractauto_autoexecprogbuf[3]);
  and and_16 (and_16_out, comparator_6_eq, dmi_access, abstractauto_autoexecprogbuf[4]);
  and and_17 (and_17_out, comparator_7_eq, dmi_access, abstractauto_autoexecprogbuf[5]);
  and and_18 (and_18_out, comparator_8_eq, dmi_access, abstractauto_autoexecprogbuf[6]);
  and and_19 (and_19_out, comparator_9_eq, dmi_access, abstractauto_autoexecprogbuf[7]);
  Comparator #(.Bits(20)) comparator_10 (
    .a(dmcontrol_hartsel), .b({20{1'b0}}), .gt(dmstatus_allnonexistent));  // open: eq, lt
  RS_FF rs_ff_1 (.S(dmcontrol_resumereq), .C(clk), .R(dmcontrol_haltreq), .Q(dmstatus_allresumeack));  // open: nQ
  not not_3 (dmstatus_allrunning, is_debug);
  nor nor_1 (nor_1_out, dmi_req_rise, in_progbuf);
  or or_3 (or_3_out, dm_done, ack_drop);
  not not_4 (not_4_out, dmi_req);
  or or_4 (or_4_out, and_11_out, and_12_out, and_13_out, and_14_out, and_15_out, and_16_out, and_17_out, and_18_out, and_19_out);
  and and_20 (ack_drop, not_4_out, dm_ack);
  RISING_EDGE rising_edge_3 (.clk(clk), .d(nor_1_out), .o(dm_done));
  Register register_2 (.D(dm_done), .C(clk), .en(or_3_out), .Q(dm_ack));
  D_FF d_ff_6 (.D(or_4_out), .C(clk), .Q(autoexec));  // open: nQ
  Comparator #(.Bits(32)) comparator_11 (.a(dmi_memaddr), .b({32{1'b0}}), .eq(comparator_11_eq));  // open: gt, lt
  not not_5 (not_5_out, comparator_11_eq);
  and and_21 (and_21_out, dmi_wen, not_5_out);
  or or_5 (dm_wen, and_21_out, command_reg_arg0wen);
  Multiplexer #(.Bits(32)) multiplexer_2 (.sel(command_reg_arg0wen), .in_0(dmi_wdata), .in_1(ra), .out(dm_wdata));
  Multiplexer #(.Bits(32)) multiplexer_3 (
    .sel(command_reg_validtransferex), .in_0(dmi_memaddr), .in_1(32'h418), .out(addr_dm));
  and and_22 (and_22_out, command_reg_regnoinvalid, command_reg_transfer);
  Comparator #(.Bits(3)) comparator_12 (.a(command_reg_aarsize), .b(3'b010), .gt(comparator_12_gt));  // open: eq, lt
  Multiplexer #(.Bits(5)) multiplexer_4 (.sel(command_reg_exec), .in_0(d_rs1), .in_1(command_reg_gprno), .out(d_rs1_2));
  Multiplexer #(.Bits(32)) multiplexer_5 (.sel(command_reg_exec), .in_0(d_rdin), .in_1(out_dm), .out(d_rdin_2));
  Multiplexer #(.Bits(5)) multiplexer_6 (.sel(command_reg_regwen), .in_0(d_rd), .in_1(command_reg_gprno), .out(d_rd_2));
  or or_6 (or_6_out, d_regwen, command_reg_regwen);
  or or_7 (or_7_out, command_unsuported_sel, comparator_12_gt, and_22_out, command_reg_aarpostincrement);
  Multiplexer multiplexer_7 (.sel(haltreq), .in_0(or_6_out), .in_1(1'b0), .out(d_regwen_2));
  Multiplexer #(.Bits(3)) multiplexer_8 (.sel(or_7_out), .in_0(3'b000), .in_1(3'b010), .out(multiplexer_8_out));
  assign and_23_out = not_6_out & abstractcs_cmderr;  // And and_23, 3 bits wide
  assign not_6_out = ~dmi_wdata[10:8];  // Not not_6, 3 bits wide
  not not_7 (not_7_out, haltreq);
  Multiplexer #(.Bits(3)) multiplexer_9 (
    .sel(command_reg_exec), .in_0(and_23_out), .in_1(multiplexer_8_out), .out(multiplexer_9_out));
  and and_24 (d_memwen_2, d_memwen, not_7_out);
  or or_8 (or_8_out, abstractcs_wen, command_exec);
  Register #(.Bits(3)) u_abstractcs_cmderr (.D(multiplexer_9_out), .C(clk), .en(or_8_out), .Q(abstractcs_cmderr));
  Register #(.Bits(32)) command_persistent (.D(dmi_wdata), .C(clk), .en(command_wen), .Q(command_persistent_q));
  D_FF d_ff_7 (.D(command_wen), .C(clk), .nQ(d_ff_7_nq));  // open: Q
  and and_25 (and_25_out, d_ff_7_nq, command_wen);
  Comparator #(.Bits(8)) comparator_13 (
    .a(command_cmdtype), .b({8{1'b0}}), .gt(command_unsuported_sel), .eq(command_reg_sel));  // open: lt
  and and_26 (command_reg_exec, command_exec, command_reg_sel);
  Multiplexer #(.Bits(32)) multiplexer_10 (
    .sel(and_25_out), .in_0(command_persistent_q), .in_1(dmi_wdata),
    .out({command_cmdtype, multiplexer_10_out[23], command_reg_aarsize, command_reg_aarpostincrement, command_reg_postexec, command_reg_transfer, command_reg_write, command_reg_regno}));
  or or_9 (or_9_out, command_wen, autoexec);
  nor nor_2 (nor_2_out, abstractcs_cmderr[0], abstractcs_cmderr[1], abstractcs_cmderr[2]);
  Comparator #(.Bits(16)) comparator_14 (.a(command_reg_regno), .b(16'h1000), .lt(comparator_14_lt));  // open: gt, eq
  Comparator #(.Bits(16)) comparator_15 (.a(command_reg_regno), .b(16'h101f), .gt(comparator_15_gt));  // open: eq, lt
  or or_10 (command_reg_regnoinvalid, comparator_14_lt, comparator_15_gt);
  and and_27 (command_exec, or_9_out, nor_2_out);
  not not_8 (not_8_out, command_reg_regnoinvalid);
  not not_9 (not_9_out, command_reg_write);
  Sub #(.Bits(16)) sub_1 (
    .a(command_reg_regno), .b(16'h1000), .c_i(1'b0), .s({sub_1_s, command_reg_gprno}));  // open: c_o
  and and_28 (command_reg_jumpprogbuf, command_reg_postexec, command_reg_exec);
  and and_29 (command_reg_validtransferex, command_reg_exec, command_reg_transfer, not_8_out);
  and and_30 (command_reg_arg0wen, not_9_out, command_reg_validtransferex);
  and and_31 (command_reg_regwen, command_reg_write, command_reg_validtransferex);
  Register #(.Bits(32)) u_abstractauto_persistent (
    .D(dmi_wdata), .C(clk), .en(abstractauto_wen),
    .Q({abstractauto_autoexecprogbuf, abstractauto_persistent, abstractauto_autoexecdata}));

  // Other names for the same wires on the sheet: abstractauto_persistent (some bits) = {abstractauto_autoexecprogbuf, abstractauto_autoexecdata};
  //   abstractauto_rdata (some bits) = {abstractauto_autoexecprogbuf, abstractauto_autoexecdata};
  //   abstractcs_busy = in_progbuf; abstractcs_rdata (some bits) = {in_progbuf, abstractcs_cmderr};
  //   d_memwen_t = d_memwen_2; d_rd_t[4:0] = d_rd_2; d_rdin_t[31:0] = d_rdin_2; d_regwen_t = d_regwen_2;
  //   d_rs1_t[4:0] = d_rs1_2;
  //   dmcontrol_rdata (some bits) = {dmcontrol_haltreq, dmcontrol_resumereq, dmcontrol_hartreset, dmcontrol_ackhavereset, dmcontrol_hasel, dmcontrol_hartsel[9:0], dmcontrol_hartsel[19:10], dmcontrol_clrresethaltreq, dmcontrol_ndmreset, dmcontrol_dmactive};
  //   dmcontrol_persistent (some bits) = {dmcontrol_haltreq, dmcontrol_hartreset, dmcontrol_hasel, dmcontrol_hartsel[9:0], dmcontrol_hartsel[19:10], dmcontrol_ndmreset, dmcontrol_dmactive};
  //   dmcontrol_hartselhi[9:0] = dmcontrol_hartsel[19:10]; dmcontrol_hartsello[9:0] = dmcontrol_hartsel[9:0];
  //   dmcontrol_setresethaltreq = dmcontrol_rdata[3]; dmstatus_allhalted = is_debug; dmstatus_anyhalted = is_debug;
  //   dmstatus_rdata (some bits) = {{2{dmstatus_allresumeack}}, {2{dmstatus_allnonexistent}}, {2{dmstatus_allrunning}}, {2{is_debug}}};
  //   dmstatus_anynonexistent = dmstatus_allnonexistent; dmstatus_anyresumeack = dmstatus_allresumeack;
  //   dmstatus_anyrunning = dmstatus_allrunning

  // Notes on the sheet:
  //   Debug module control:
  //   GDB & TAP
  //   This is where the GDB server component and JTAG TAP live. We just plug them
  //   into each other, decode what the TAP wants us to do, and provide it with output
  //   from the circuit.
  //   Debug module registers:
  //   dmcontrol
  //   Additional debug module logic:
  //   halting
  //   We should halt if we're being asked to via dmcontrol or if we've just completed
  //   a single-step:
  //   We store any fields that need to be
  //   persistent in a register:
  //   Every RW field can be directly
  //   extracted for use from the
  //   persistent register:
  //   W1 fields should only be high
  //   for the clock cycle that they're written:
  //   Debug park loop > dret
  //   (We can get away with a hardcoded
  //   number of clock cycles for single-step.)
  //   dret > curr. instr
  //   It's useful to have each field separate
  //   for implementing their functionality,
  //   but let's also pack them up
  //   so that the debugger can read them:
  //   curr. instr > next instr
  //   (And for convenience, let's 
  //   also expose this:)
  //   We know our CPU handles halts in a
  //   single clock cycle, so to avoid complication
  //   we won't hold this signal high.
  //   sbcs
  //   contents of dmi_rdata_lut (hex, n*v repeats v):
  //   4*0,1,11*0,2,3,4,0,0,0,5,0,7,7*0,8*1,16*0,6
  //   contents of dmi_wen_lut (hex, n*v repeats v):
  //   16*0,1,5*0,2,3,5,31*0,4
  //   contents of dmi_memaddr_lut (hex, n*v repeats v):
  //   4*0,418,27*0,10004,10008,1000c,10010,10014,10018,1001c,10020
  //   We don't support system bus
  //   access, so we can treat this entire
  //   register as effectively read-only:
  //   autoexec
  //   We just check if we're accessing any data/progbuf words
  //   that we're supposed to autoexec on access of:
  //   TODO: Simplify
  //   dmstatus
  //   Every field in mstatus is read-only.
  //   (Pretty useful)
  //   Transaction signals
  //   We are done working if we're not
  //   in progbuf and dmi-req didn't just go high:
  //   We should raise dmi-ack if we are done and
  //   lower it if we need to lower it:
  //   Specifically, we should lower dmi-ack when
  //   dmi-req is lowered by the TAP in acknowledgement
  //   of our acknowledgement:
  //   Determine each field's value:
  //   Wait for access to complete.
  //   (Matters more for writes than
  //   reads.)
  //   Pack them up so the debugger
  //   can read them:
  //   memory access
  //   If the debug module is accessing RAM,
  //   it is either because one of the dmi
  //   registers is memory-mapped, or 
  //   we are executing a command that
  //   requires us to do so.
  //   IO
  //   abstractcs
  //   Determine each field's value:
  //   (especially cmderr...)
  //   cpu "hooks"
  //   Sometimes we want to read or write
  //   a register:
  //   We should never do an instruction's
  //   memory write while jumping for haltreq:
  //   (We process the instruction when we get
  //   back. We don't want duplicate execution!)
  //   hartinfo
  //   command
  //   This is a write-only register. 
  //   We choose to process it entirely on the same cycle it is written.
  //   I should mention that we only implement the access register
  //   command. This is because it contains functionality for arbitrary
  //   code execution, which allows us to do everything else.
  //   Handle persistence and extract all fields:
  //   Figure out if we should be executing
  //   the command:
  //   Split out cmdtype to selectors:
  //   Determine if we need to execute a register access
  //   command:
  //   Figure out if regno is invalid:
  //   If we end up reading or writing a
  //   register, we'll need its number in
  //   the standard format:
  //   And finally figure out if we need to
  //   jump to the progbuf:
  //   Determine if a valid transfer is to be executed:
  //   Will we end up reading a register?
  //   Let's see:
  //   What about writing?
  //   abstractauto
  //   This is an optional register, but OpenOCD
  //   is bugged and requires it. (riscv-collab/riscv-openocd/issues/587)
  //   Store for persistence:
  //   Extract the fields:
  //   Pack up:
endmodule
