// Digital circuit RV5-OPCODE-SYSTEM-DECODE.dig as structural Verilog
module RV5_OPCODE_SYSTEM_DECODE (
  input  [6:0] opcode,
  output is_system
);

  RV5_OPCODE_SYSTEM_DECODE rv5_opcode_system_decode_1 (
    .op6(opcode[6]), .op5(opcode[5]), .op4(opcode[4]), .op3(opcode[3]), .op2(opcode[2]), .op1(opcode[1]),
    .op0(opcode[0]), .is_system(is_system));

  // Notes on the sheet:
  //   RV5-OPCODE-SYSTEM-DECODE
  //   This parses the opcode field of the risc-v instruction.
  //   Really, this field represents what is called the "major opcode".
  //   I think it's called "opcode" in instruction layout diagrams in the
  //   spec for brevity.
  //   This block contains the actual logic.
  //   I like to keep it encapsulated like
  //   this because I synthesize it from a
  //   script-generated LUT. This layout
  //   lets me cleanly separate what is manually
  //   authored and what is synthesized. What
  //   if my opcode splitting and opcode description
  //   were in there and I regenerated for some
  //   reason?
  //   That would suck! It would be gone!
endmodule
