// Digital circuit RV5-DEBUG-SYSTEM.dig as structural Verilog
module RV5_DEBUG_SYSTEM (
  input  clk,
  input  [31:0] dm_mem_rdata,
  input  [31:0] R_rs1,
  input  regwen,
  input  memwen,
  input  [4:0] rd,
  input  [4:0] rs1,
  input  [31:0] wb,
  input  [31:0] pc,
  input  [31:0] npc,
  input  [6:0] opcode,
  input  [2:0] funct3,
  input  [11:0] funct12,
  output haltreq,
  output resumereq,
  output jump_progbuf,
  output [31:0] dm_mem_wdata,
  output dm_mem_wen,
  output [31:0] dm_mem_addr,
  output regwen_2,
  output memwen_2,
  output [4:0] rd_2,
  output [4:0] rs1_2,
  output [31:0] wb_2,
  output [31:0] npc_2
);

  wire csr_opclear, csr_opset, csr_useimm, csr_wen, is_debug, is_dret, is_ebreak, is_ecall, is_mret,
       is_progbuf, regwen_t, rv5_opcode_system_decode_1_is_system, sys_ctrl_reg_wen;
  wire [1:0] sys_ctrl_wb_sel;
  wire [31:0] and_1_out, csr_out, dcsr, dpc, mepc, mtvec, multiplexer_1_out, multiplexer_2_out,
       multiplexer_3_out, not_1_out, or_1_out, wb_t;

  RV5_DEBUG_MODULE rv5_debug_module_1 (
    .clk(clk), .dcsr(dcsr), .dm_mem_rdata(dm_mem_rdata), .ra(R_rs1), .is_debug(is_debug),
    .is_progbuf(is_progbuf), .regwen(regwen_t), .R_rd_in(wb_t), .memwen(memwen), .rd(rd), .rs1(rs1),
    .haltreq(haltreq), .resumereq(resumereq), .jump_progbuf(jump_progbuf), .dm_mem_wdata(dm_mem_wdata),
    .dm_mem_wen(dm_mem_wen), .dm_mem_addr(dm_mem_addr), .regwen_2(regwen_2), .R_rd_in_2(wb_2),
    .memwen_2(memwen_2), .rd_2(rd_2), .rs1_2(rs1_2));
  RV5_DEBUG_SYSTEM_PCU rv5_debug_system_pcu_1 (
    .npc(npc), .mtvec(mtvec), .mepc(mepc), .dpc(dpc), .ecall_sel(is_ecall), .mret_sel(is_mret), .dcsr(dcsr),
    .dret_sel(is_dret), .haltreq(haltreq), .jump_progbuf(jump_progbuf), .resumereq(resumereq),
    .ebreak_sel(is_ebreak), .clk(clk), .npc_2(npc_2), .is_debug(is_debug), .is_progbuf(is_progbuf));
  RV5_OPCODE_SYSTEM_DECODE rv5_opcode_system_decode_1 (
    .opcode(opcode), .is_system(rv5_opcode_system_decode_1_is_system));
  Multiplexer #(.Bits(32)) multiplexer_1 (
    .sel(csr_useimm), .in_0(R_rs1), .in_1({{27{1'b0}}, rs1}), .out(multiplexer_1_out));
  assign and_1_out = not_1_out & csr_out;  // And and_1, 32 bits wide
  assign not_1_out = ~multiplexer_1_out;  // Not not_1, 32 bits wide
  assign or_1_out = multiplexer_1_out | csr_out;  // Or or_1, 32 bits wide
  Multiplexer #(.Bits(32)) multiplexer_2 (
    .sel(csr_opclear), .in_0(multiplexer_1_out), .in_1(and_1_out), .out(multiplexer_2_out));
  Multiplexer #(.Bits(32)) multiplexer_3 (
    .sel(csr_opset), .in_0(multiplexer_2_out), .in_1(or_1_out), .out(multiplexer_3_out));
  RV5_SYSTEM_CONTROL rv5_system_control_1 (
    .is_system(rv5_opcode_system_decode_1_is_system), .funct12(funct12), .funct3(funct3),
    .reg_wen(sys_ctrl_reg_wen), .wb_sel(sys_ctrl_wb_sel), .csr_wen(csr_wen), .csr_opset(csr_opset),
    .csr_opclear(csr_opclear), .csr_useimm(csr_useimm), .is_ecall(is_ecall), .is_ebreak(is_ebreak),
    .is_mret(is_mret), .is_dret(is_dret));
  or or_2 (regwen_t, sys_ctrl_reg_wen, regwen);
  RV5_CSR rv5_csr_1 (
    .clk(clk), .addr(funct12), .wdata(multiplexer_3_out), .wen(csr_wen), .pc(pc), .ecall_sel(is_ecall),
    .mret_sel(is_mret), .ebreak_sel(is_ebreak), .is_debug(is_debug), .haltreq(haltreq), .csr_out(csr_out),
    .mtvec(mtvec), .mepc(mepc), .dcsr(dcsr), .dpc(dpc));
  Multiplexer #(.Selector_Bits(2), .Bits(32)) multiplexer_4 (
    .sel(sys_ctrl_wb_sel), .in_0(wb), .in_1(wb), .in_2(wb), .in_3(csr_out), .out(wb_t));

  // Other names for the same wires on the sheet: memwen_t = memwen_2; npc_t[31:0] = npc_2; rd_t[4:0] = rd_2;
  //   regwen_t_t = regwen_2; rs1_t[4:0] = rs1_2; wb_t_t[31:0] = wb_2

  // Notes on the sheet:
  //   Debug & system control:
  //   IO
  //   About
  //   This is a smish-smosh of things related to implementing debug.
  //   It's all stuffed here to keep the CPU base instruction set as 
  //   clean as possible.
  //   Things here:
  //   * RV5-DEBUG-MODULE: an implementation of the RISC-V debug spec.
  //   * RV5-DEBUG-SYSTEM-PCU: an extension for the PCU that handles 
  //   some system-type instructions as well as certain signals from the
  //   debug module. In a real CPU this would just be part of the PCU.
  //   * System control logic: This is the logic for handling system
  //   instruction decoding and overriding any necessary control signals.
  //   This is another thing that would be in the control logic like anything
  //   else in a real system.
  //   * CSR registers: We need a few CSRs for debug stuff. Those are
  //   defined here.
  //   CSR registers
  //   System control logic
endmodule
