// Digital circuit RV5-DEBUG-SYSTEM-PCU.dig as structural Verilog
module RV5_DEBUG_SYSTEM_PCU (
  input  [31:0] npc,
  input  [31:0] mtvec,
  input  [31:0] mepc,
  input  [31:0] dpc,
  input  ecall_sel,
  input  mret_sel,
  input  [31:0] dcsr,
  input  dret_sel,
  input  haltreq,
  input  jump_progbuf,
  input  resumereq,
  input  ebreak_sel,
  input  clk,
  output [31:0] npc_2,
  output is_debug,
  output is_progbuf
);

  wire and_1_out, and_2_out, or_1_out, or_2_out, or_3_out, or_5_out;
  wire [8:8] rising_edge_1_o;
  wire [29:0] multiplexer_1_out, onehotmultiplexer_1_p9, or_4_out, or_6_out;
  wire [31:0] multiplexer_2_out;

  and and_1 (and_1_out, ebreak_sel, dcsr[15]);
  or or_1 (or_1_out, haltreq, and_1_out);
  RS_FF rs_ff_1 (.S(or_1_out), .C(clk), .R(dret_sel), .Q(is_debug));  // open: nQ
  RS_FF rs_ff_2 (.S(jump_progbuf), .C(clk), .R(ebreak_sel), .Q(is_progbuf));  // open: nQ
  RISING_EDGE rising_edge_1 (.clk(clk), .d(resumereq), .o(rising_edge_1_o[8]));
  or or_2 (or_2_out, is_debug, dcsr[15]);
  or or_3 (or_3_out, rising_edge_1_o[8], jump_progbuf, haltreq);
  and and_2 (and_2_out, dret_sel, is_debug);
  Multiplexer #(.Bits(30)) multiplexer_1 (.sel(or_2_out), .in_0(mtvec[31:2]), .in_1(30'h104), .out(multiplexer_1_out));
  assign or_4_out = {{21{1'b0}}, haltreq, {5{1'b0}}, haltreq, 2'b00} | {{15{1'b0}}, jump_progbuf, {13{1'b0}}, jump_progbuf};  // Or or_4, 30 bits wide
  or or_5 (or_5_out, ebreak_sel, ebreak_sel, ebreak_sel, and_2_out);
  // OneHotMultiplexer #(.Bits(30)) onehotmultiplexer_1: pin names not known; wires that end beside it: ecall_sel, mret_sel, ebreak_sel, and_2_out, mtvec[31:2], mepc[31:2], multiplexer_1_out, dpc[31:2], onehotmultiplexer_1_p9
  assign or_6_out = or_4_out | {{21{1'b0}}, rising_edge_1_o[8], {5{1'b0}}, rising_edge_1_o[8], 1'b0, rising_edge_1_o[8]};  // Or or_6, 30 bits wide
  Multiplexer #(.Bits(32)) multiplexer_2 (
    .sel(or_5_out), .in_0(npc), .in_1({onehotmultiplexer_1_p9, 2'b00}), .out(multiplexer_2_out));
  Multiplexer #(.Bits(32)) multiplexer_3 (
    .sel(or_3_out), .in_0(multiplexer_2_out), .in_1({or_6_out, 2'b00}), .out(npc_2));

  // Notes on the sheet:
  //   RV5-DEBUG-SYSTEM-PCU
  //   We use some of the same conditions as the PC
  //   select to figure out if we're in the debug ROM/progbuf.
  //   We could do an address range check, which would
  //   be hard to get wrong.
  //   We two one-hot groups of selectors.
  //   The first is for the instructions we're processing.
  //   The second is for signals from the debug module.
  //   The debug signals take priority over the instruction
  //   signals, which take priority over the PC increment.
  //   0x104:
  //   0x4001:
  //   0x105:
endmodule
