// Digital circuit _RV5-OPCODE-SYSTEM-DECODE.dig as structural Verilog
module RV5_OPCODE_SYSTEM_DECODE (
  input  op6,
  input  op5,
  input  op4,
  input  op3,
  input  op2,
  input  op1,
  input  op0,
  output is_system
);

  wire and_1_out, and_2_out, and_3_out, and_4_out, and_5_out, not_1_out, not_2_out;

  not not_1 (not_1_out, op3);
  not not_2 (not_2_out, op2);
  and and_1 (and_1_out, op1, not_2_out);
  and and_2 (and_2_out, not_1_out, op4);
  and and_3 (and_3_out, op5, op6);
  and and_4 (and_4_out, op0, and_1_out);
  and and_5 (and_5_out, and_2_out, and_3_out);
  and and_6 (is_system, and_4_out, and_5_out);
endmodule
