// Digital circuit RV5-GPR.dig as structural Verilog
module RV5_GPR (
  input  [4:0] rs1,
  input  [4:0] rs2,
  input  [31:0] rdin,
  input  clk,
  input  [4:0] rd,
  input  wen,
  output [31:0] ra,
  output [31:0] rb,
  output rd0
);

  wire src1is0, src2is0;
  wire [31:0] REGS_da, REGS_db;

  and and_1 (src1is0, ~rs1[0], ~rs1[1], ~rs1[2], ~rs1[3], ~rs1[4]);  // And
  and and_2 (src2is0, ~rs2[0], ~rs2[1], ~rs2[2], ~rs2[3], ~rs2[4]);  // And
  RegisterFile #(.AddrBits(5), .Bits(32)) REGS (
    .Din(rdin), .we(wen), .Rw(rd), .C(clk), .Ra(rs1), .Rb(rs2), .Da(REGS_da), .Db(REGS_db));
  Multiplexer #(.Bits(32)) multiplexer_1 (.sel(src1is0), .in_0(REGS_da), .in_1({32{1'b0}}), .out(ra));
  Multiplexer #(.Bits(32)) multiplexer_2 (.sel(src2is0), .in_0(REGS_db), .in_1({32{1'b0}}), .out(rb));
  and and_3 (rd0, ~rd[0], ~rd[1], ~rd[2], ~rd[3], ~rd[4]);  // And

  // Notes on the sheet:
  //   RV5-REGS
  //   2-Port Register Bank
  //   Zero Detector
  //   Immediate Selector
  //   /5
  //   /32
  //   Zero Reg Decode
  //   Reg/Reg0
  //   RA-bus
  //   RB-bus
endmodule
