// Digital circuit RV5-IMM-GEN.dig as structural Verilog
module RV5_IMM_GEN (
  input  [31:0] inst,
  input  [4:0] inst_format,
  output [31:0] out
);

  wire [31:12] imm_b;

  BitExtender #(.inputBits(1), .outputBits(20)) bitextender_1 (.in(inst[31]), .out(imm_b));
  assign out = inst_format[0] ? {imm_b, inst[31:20]} : 32'bz;  // Driver driver_1
  assign out = inst_format[1] ? {imm_b, inst[31:25], inst[11:7]} : 32'bz;  // Driver driver_2
  assign out = inst_format[2] ? {imm_b, inst[7], inst[30:25], inst[11:8], 1'b0} : 32'bz;  // Driver driver_3
  assign out = inst_format[3] ? {inst[31:12], {12{1'b0}}} : 32'bz;  // Driver driver_4
  assign out = inst_format[4] ? {imm_b[23:12], inst[19:12], inst[20], inst[30:21], 1'b0} : 32'bz;  // Driver driver_5

  // Other names for the same wires on the sheet: imm_opt_signext[31:0] = out;
  //   imm_b[11:1] = {inst[7], inst[30:25], inst[11:8]}; imm_s[31:0] = {imm_b, inst[31:25], inst[11:7]};
  //   imm_j[31:1] = {imm_b[23:12], inst[19:12], inst[20], inst[30:21]}; imm_u[31:12] = inst[31:12];
  //   imm_i[31:0] = {imm_b, inst[31:20]}; fmt_i = inst_format[0]; fmt_s = inst_format[1]; fmt_b = inst_format[2];
  //   fmt_u = inst_format[3]; fmt_j = inst_format[4]; sign_ext12[11:0] = imm_b[23:12]; sign_ext20[19:0] = imm_b

  // Notes on the sheet:
  //   RV5-IMM-GEN
  //   Different instruction types have different layouts, 
  //   so we need different logic to extract the immediates.
  //   All signed formats (I, S, B, J) share a single 
  //   sign-extender on inst[31]. U-type is zero-padded.
  //   Immediate Select (tri-state bus)
  //   Immediate extract split & sign-extend
endmodule
