// Digital circuit RV5-MEM-ADDR-DECODE.dig as structural Verilog
module RV5_MEM_ADDR_DECODE (
  input  [31:0] addr,
  output addr_data0,
  output addr_terminal,
  output addr_progbuf_0,
  output addr_progbuf_1,
  output addr_progbuf_2,
  output addr_progbuf_3,
  output addr_progbuf_4,
  output addr_progbuf_5,
  output addr_progbuf_6,
  output addr_progbuf_7,
  output addr_filemap,
  output addr_ram
);

  wire and_1_out, and_2_out, and_3_out, and_4_out, and_5_out, and_6_out, and_7_out, and_8_out, and_9_out,
       and_10_out, and_11_out, and_12_out, and_13_out, and_14_out, and_15_out, and_16_out, and_17_out,
       and_18_out, and_19_out, and_20_out, and_21_out, and_22_out, and_23_out, and_24_out, and_25_out,
       and_26_out, and_27_out, and_28_out, and_29_out, and_30_out, and_31_out, and_32_out, and_33_out,
       and_35_out, and_36_out, and_37_out, and_38_out, and_39_out, and_40_out, and_41_out, and_42_out,
       and_43_out, and_53_out, and_54_out, nor_1_out, nor_2_out, nor_3_out, nor_4_out, nor_5_out, nor_6_out,
       nor_7_out, not_1_out, not_2_out, not_3_out, not_4_out, not_5_out, not_6_out, not_7_out, not_8_out,
       not_9_out, not_10_out, not_11_out, or_1_out, or_2_out, or_3_out, or_4_out, or_5_out, or_6_out,
       or_7_out, or_8_out, or_9_out, or_10_out, or_11_out, or_12_out, or_13_out, or_14_out, or_15_out,
       or_16_out, or_17_out, or_18_out, or_19_out, or_20_out, or_21_out, or_22_out, or_23_out, or_24_out;

  not not_1 (not_1_out, addr[0]);
  not not_2 (not_2_out, addr[2]);
  not not_3 (not_3_out, addr[1]);
  not not_4 (not_4_out, addr[4]);
  not not_5 (not_5_out, addr[3]);
  not not_6 (not_6_out, addr[6]);
  not not_7 (not_7_out, addr[5]);
  not not_8 (not_8_out, addr[8]);
  not not_9 (not_9_out, addr[7]);
  not not_10 (not_10_out, addr[9]);
  not not_11 (not_11_out, addr[16]);
  or or_1 (or_1_out, addr[31], addr[30]);
  or or_2 (or_2_out, addr[29], addr[28]);
  or or_3 (or_3_out, addr[27], addr[26]);
  or or_4 (or_4_out, addr[25], addr[24]);
  or or_5 (or_5_out, addr[23], addr[22]);
  or or_6 (or_6_out, addr[21], addr[20]);
  or or_7 (or_7_out, addr[19], addr[18]);
  or or_8 (or_8_out, addr[15], addr[14]);
  or or_9 (or_9_out, addr[13], addr[12]);
  and and_1 (and_1_out, addr[10], not_10_out);
  and and_2 (and_2_out, not_8_out, not_9_out);
  and and_3 (and_3_out, not_6_out, not_7_out);
  and and_4 (and_4_out, addr[4], addr[3]);
  and and_5 (and_5_out, not_2_out, not_3_out);
  or or_10 (or_10_out, addr[10], addr[9]);
  or or_11 (or_11_out, addr[8], addr[7]);
  or or_12 (or_12_out, addr[5], addr[4]);
  or or_13 (or_13_out, addr[3], addr[2]);
  or or_14 (or_14_out, addr[1], addr[0]);
  and and_6 (and_6_out, not_3_out, not_1_out);
  or or_15 (or_15_out, addr[4], addr[3]);
  and and_7 (and_7_out, not_7_out, not_4_out);
  and and_8 (and_8_out, not_7_out, addr[4]);
  and and_9 (and_9_out, addr[5], not_4_out);
  and and_10 (and_10_out, not_5_out, addr[2]);
  and and_11 (and_11_out, addr[3], not_2_out);
  and and_12 (and_12_out, addr[3], addr[2]);
  and and_13 (and_13_out, not_5_out, not_2_out);
  or or_16 (or_16_out, or_7_out, addr[17]);
  or or_17 (or_17_out, or_9_out, addr[11]);
  and and_14 (and_14_out, and_5_out, not_1_out);
  or or_18 (or_18_out, or_11_out, addr[6]);
  nor nor_1 (nor_1_out, or_15_out, addr[2]);
  or or_19 (or_19_out, or_2_out, or_3_out);
  or or_20 (or_20_out, or_4_out, or_5_out);
  and and_15 (and_15_out, and_1_out, and_2_out);
  and and_16 (and_16_out, and_3_out, and_4_out);
  or or_21 (or_21_out, or_13_out, or_14_out);
  nor nor_2 (nor_2_out, or_1_out, or_19_out);
  or or_22 (or_22_out, or_6_out, or_16_out);
  nor nor_3 (nor_3_out, or_8_out, or_17_out);
  and and_17 (and_17_out, and_15_out, and_16_out);
  nor nor_4 (nor_4_out, or_10_out, or_18_out);
  nor nor_5 (nor_5_out, or_12_out, or_21_out);
  or or_23 (or_23_out, nor_1_out, not_7_out);
  nor nor_6 (nor_6_out, or_20_out, or_22_out);
  and and_18 (and_18_out, and_17_out, and_14_out);
  and and_19 (and_19_out, and_7_out, and_10_out);
  and and_20 (and_20_out, and_7_out, and_11_out);
  and and_21 (and_21_out, and_7_out, and_12_out);
  and and_22 (and_22_out, nor_4_out, nor_5_out);
  and and_23 (and_23_out, and_8_out, and_13_out);
  and and_24 (and_24_out, and_8_out, and_10_out);
  and and_25 (and_25_out, and_8_out, and_11_out);
  and and_26 (and_26_out, and_8_out, and_12_out);
  and and_27 (and_27_out, and_9_out, and_13_out);
  and and_28 (and_28_out, nor_2_out, nor_6_out);
  and and_29 (and_29_out, nor_3_out, and_22_out);
  and and_30 (and_30_out, and_28_out, addr[16]);
  and and_31 (and_31_out, and_28_out, not_11_out);
  and and_32 (and_32_out, nor_3_out, nor_4_out);
  and and_33 (and_33_out, and_31_out, nor_3_out);
  and and_34 (addr_terminal, and_30_out, and_29_out);
  and and_35 (and_35_out, and_30_out, and_32_out);
  and and_36 (and_36_out, and_6_out, and_19_out);
  and and_37 (and_37_out, and_6_out, and_20_out);
  and and_38 (and_38_out, and_6_out, and_21_out);
  and and_39 (and_39_out, and_6_out, and_23_out);
  and and_40 (and_40_out, and_6_out, and_24_out);
  and and_41 (and_41_out, and_6_out, and_25_out);
  and and_42 (and_42_out, and_6_out, and_26_out);
  and and_43 (and_43_out, and_6_out, and_27_out);
  and and_44 (addr_data0, and_33_out, and_18_out);
  and and_45 (addr_progbuf_0, and_35_out, and_36_out);
  and and_46 (addr_progbuf_1, and_35_out, and_37_out);
  and and_47 (addr_progbuf_2, and_35_out, and_38_out);
  and and_48 (addr_progbuf_3, and_35_out, and_39_out);
  and and_49 (addr_progbuf_4, and_35_out, and_40_out);
  and and_50 (addr_progbuf_5, and_35_out, and_41_out);
  and and_51 (addr_progbuf_6, and_35_out, and_42_out);
  and and_52 (addr_progbuf_7, and_35_out, and_43_out);
  and and_53 (and_53_out, and_35_out, and_6_out);
  and and_54 (and_54_out, and_53_out, or_23_out);
  or or_24 (or_24_out, addr_data0, addr_terminal);
  nor nor_7 (nor_7_out, or_24_out, and_54_out);
  not not_12 (addr_filemap, nor_2_out);
  and and_55 (addr_ram, nor_2_out, nor_7_out);

  // Notes on the sheet:
  //   RV5-MEM-ADDR-DECODE
  //   filemap: addr > 0x3FFFFFF
  //   data0: addr == 0x418
  //   terminal: addr == 0x10000
  //   progbuf[0-7]: addr == 0x10004, 0x10008, 0x1000C, 0x10010, 0x10014, 0x10018, 0x1001C, 0x10020
  //   ram: everything else
endmodule
