// Digital circuit RV5-PCU.dig as structural Verilog
module RV5_PCU (
  input  [31:0] imm_signext,
  input  [31:0] alu_out,
  input  [31:0] mtvec,
  input  [31:0] mepc,
  input  [31:0] dpc,
  input  branch_sel,
  input  jal_sel,
  input  jalr_sel,
  input  ecall_sel,
  input  mret_sel,
  input  [31:0] dcsr,
  input  dret_sel,
  input  haltreq,
  input  jump_progbuf,
  input  resumereq,
  input  ebreak_sel,
  input  [2:0] funct3,
  input  eq,
  input  slt,
  input  carry,
  input  clk,
  output [31:0] pc,
  output is_debug,
  output is_progbuf
);

  wire and_1_out, and_2_out, and_3_out, br_cond, not_1_out, not_2_out, not_3_out, or_1_out, or_2_out,
       or_3_out, or_4_out, or_5_out, or_6_out, or_7_out;
  wire [8:8] rising_edge_1_o;
  wire [29:0] and_4_out, and_5_out, and_6_out, and_7_out, and_8_out, and_9_out, bit_expand_30_1_o,
       bit_expand_30_2_o, bit_expand_30_3_o, bit_expand_30_4_o, bit_expand_30_5_o, bit_expand_30_6_o,
       multiplexer_2_out, multiplexer_3_out, multiplexer_4_out, or_8_out, or_9_out, or_10_out, or_11_out,
       or_12_out, or_13_out, or_14_out, PC_Incr_s, PC_JumpRel_s;

  and and_1 (and_1_out, ebreak_sel, dcsr[15]);
  Multiplexer #(.Selector_Bits(3)) multiplexer_1 (
    .sel(funct3), .in_0(eq), .in_1(not_1_out), .in_2(1'b0), .in_3(1'b0), .in_4(slt), .in_5(not_2_out),
    .in_6(not_3_out), .in_7(carry), .out(br_cond));
  not not_1 (not_1_out, eq);
  not not_2 (not_2_out, slt);
  not not_3 (not_3_out, carry);
  or or_1 (or_1_out, haltreq, and_1_out);
  RS_FF rs_ff_1 (.S(or_1_out), .C(clk), .R(dret_sel), .Q(is_debug));  // open: nQ
  RS_FF rs_ff_2 (.S(jump_progbuf), .C(clk), .R(ebreak_sel), .Q(is_progbuf));  // open: nQ
  and and_2 (and_2_out, branch_sel, br_cond);
  or or_2 (or_2_out, is_debug, dcsr[15]);
  Multiplexer #(.Bits(30)) multiplexer_2 (.sel(or_2_out), .in_0(mtvec[31:2]), .in_1(30'h104), .out(multiplexer_2_out));
  or or_3 (or_3_out, jal_sel, and_2_out);
  and and_3 (and_3_out, dret_sel, is_debug);
  Add #(.Bits(30)) PC_JumpRel (.a(pc[31:2]), .b(imm_signext[31:2]), .c_i(1'b0), .s(PC_JumpRel_s));  // open: c_o
  RISING_EDGE rising_edge_1 (.clk(clk), .d(resumereq), .o(rising_edge_1_o[8]));
  BIT_EXPAND_30 bit_expand_30_1 (.I(or_3_out), .O(bit_expand_30_1_o));
  BIT_EXPAND_30 bit_expand_30_2 (.I(jalr_sel), .O(bit_expand_30_2_o));
  BIT_EXPAND_30 bit_expand_30_3 (.I(ecall_sel), .O(bit_expand_30_3_o));
  BIT_EXPAND_30 bit_expand_30_4 (.I(mret_sel), .O(bit_expand_30_4_o));
  BIT_EXPAND_30 bit_expand_30_5 (.I(ebreak_sel), .O(bit_expand_30_5_o));
  BIT_EXPAND_30 bit_expand_30_6 (.I(and_3_out), .O(bit_expand_30_6_o));
  or or_4 (or_4_out, and_3_out, ebreak_sel, mret_sel);
  or or_5 (or_5_out, ecall_sel, jalr_sel, or_3_out);
  or or_6 (or_6_out, rising_edge_1_o[8], jump_progbuf, haltreq);
  assign and_4_out = PC_JumpRel_s & bit_expand_30_1_o;  // And and_4, 30 bits wide
  assign and_5_out = alu_out[31:2] & bit_expand_30_2_o;  // And and_5, 30 bits wide
  assign and_6_out = mtvec[31:2] & bit_expand_30_3_o;  // And and_6, 30 bits wide
  assign and_7_out = mepc[31:2] & bit_expand_30_4_o;  // And and_7, 30 bits wide
  assign and_8_out = multiplexer_2_out & bit_expand_30_5_o;  // And and_8, 30 bits wide
  assign and_9_out = dpc[31:2] & bit_expand_30_6_o;  // And and_9, 30 bits wide
  or or_7 (or_7_out, or_4_out, or_5_out);
  assign or_8_out = and_4_out | and_5_out;  // Or or_8, 30 bits wide
  assign or_9_out = and_6_out | and_7_out;  // Or or_9, 30 bits wide
  assign or_10_out = and_8_out | and_9_out;  // Or or_10, 30 bits wide
  assign or_11_out = {{21{1'b0}}, haltreq, {5{1'b0}}, haltreq, 2'b00} | {{15{1'b0}}, jump_progbuf, {13{1'b0}}, jump_progbuf};  // Or or_11, 30 bits wide
  assign or_12_out = or_8_out | or_9_out;  // Or or_12, 30 bits wide
  assign or_13_out = or_11_out | {{21{1'b0}}, rising_edge_1_o[8], {5{1'b0}}, rising_edge_1_o[8], 1'b0, rising_edge_1_o[8]};  // Or or_13, 30 bits wide
  assign or_14_out = or_12_out | or_10_out;  // Or or_14, 30 bits wide
  Multiplexer #(.Bits(30)) multiplexer_3 (.sel(or_7_out), .in_0(PC_Incr_s), .in_1(or_14_out), .out(multiplexer_3_out));
  Multiplexer #(.Bits(30)) multiplexer_4 (
    .sel(or_6_out), .in_0(multiplexer_3_out), .in_1(or_13_out), .out(multiplexer_4_out));
  D_FF #(.Bits(30)) u_PC (.D(multiplexer_4_out), .C(clk), .Q(pc[31:2]));  // open: nQ
  Add #(.Bits(30)) PC_Incr (.a(pc[31:2]), .b(30'h1), .c_i(1'b0), .s(PC_Incr_s));  // open: c_o

  assign pc[1:0] = 2'b00;

  // Notes on the sheet:
  //   RV5-PCU
  //   If this is a conditional branch, should we branch?
  //   Branch funct3 legend
  //   0: beq
  //   1: bne
  //   2: reserved
  //   3: reserved
  //   4: blt
  //   5: bge
  //   6: bltu
  //   7: bgeu
  //   We use some of the seame conditions as the PC
  //   select to figure out if we're in the debug ROM/progbuf.
  //   We could do an address range check, which would
  //   be hard to get wrong.
  //   We two one-hot groups of selectors.
  //   The first is for the instructions we're processing.
  //   The second is for signals from the debug module.
  //   The debug signals take priority over the instruction
  //   signals, which take priority over the PC increment.
  //   0x104:
  //   0x4001:
  //   0x105:
endmodule
