// Digital circuit RV5-TAP-VPI.dig as structural Verilog
module RV5_TAP_VPI (
  input  CLK,
  input  REQ,
  input  [2:0] CMD,
  input  [7:0] NBITS,
  input  [40:0] TMS,
  input  [40:0] TDI,
  input  DMI_ACK,
  input  [31:0] DMI_RDATA,
  input  [1:0] DMI_STATUS,
  output [40:0] TDO,
  output ACK,
  output DMI_REQ,
  output [31:0] DMI_WDATA,
  output [6:0] DMI_ADDR,
  output DMI_WRITE
);

  wire and_13_out, and_18_out, and_19_out, bypass, bypass_wen, capture_dr, capture_ir, clear_dmistat,
       cmd_reset, cmd_scanchain, cmd_scanchainfliptms, cmd_stopsimu, cmd_tmsseq, cmd_tmsseqdone,
       cmd_tmsseqenter, cmd_tmsseqoperating, comparator_1_eq, d_ff_1_q, decoder_1_out_0, decoder_1_out_1,
       decoder_1_out_2, decoder_1_out_3, decoder_1_out_4, dmi_ack_t, dmi_collision_error, dmi_op_rw,
       dmi_tx_end, dmi_tx_start, dmi_wen, dtcms_wen, exit1_dr, exit1_ir, exit2_dr, exit2_ir, idcode_wen,
       ir_bypass, ir_dmi, ir_dtmcs, ir_idcode, ir_wen, multiplexer_2_out, nor_1_out, nor_2_out, not_1_out,
       not_2_out, not_3_out, not_4_out, not_5_out, not_6_out, not_7_out, not_8_out, not_9_out, not_10_out,
       not_11_out, operating, or_1_out, or_2_out, or_3_out, or_4_out, or_5_out, or_6_out, or_7_out, pause_dr,
       pause_ir, run_test_idle, select_dr_scan, select_ir_scan, shift_dr, shift_ir, test_logic_reset, tms_0,
       update_dr, update_ir;
  wire [0:0] d_ff_5_q, multiplexer_7_out, register_5_q;
  wire [1:0] dmi_op_d, dmi_status_t, dmistat_sticky, lookuptable_1_out, multiplexer_3_out, multiplexer_4_out,
       multiplexer_5_out, multiplexer_9_out, multiplexer_13_out_3;
  wire [2:0] multiplexer_13_out_4;
  wire [3:0] multiplexer_7_out_4, multiplexer_12_out, multiplexer_13_out, state_lut_out, state_q;
  wire [4:0] barrelshifter_1_out, d_ff_9_q, ir, multiplexer_1_out;
  wire [5:0] multiplexer_13_out_2, sub_1_s, sub_2_s, sub_3_s, sub_5_s, sub_6_s;
  wire [6:0] multiplexer_9_out_3;
  wire [7:0] d_ff_3_q, multiplexer_6_out, sub_4_s;
  wire [10:0] multiplexer_7_out_2;
  wire [13:0] multiplexer_13_out_6;
  wire [15:0] multiplexer_7_out_3;
  wire [17:15] multiplexer_13_out_5;
  wire [31:0] barrelshifter_3_out, barrelshifter_5_out, d_ff_6_q, d_ff_7_q, dmi_data_d, dtmcs, idcode,
       multiplexer_9_out_2;
  wire [39:0] register_5_q_2;
  wire [40:0] barrelshifter_2_out, barrelshifter_4_out, d_ff_8_q, dmi, multiplexer_10_out, multiplexer_14_out;
  wire [40:5] barrelshifter_1_out_2;
  wire [40:32] barrelshifter_3_out_2, barrelshifter_5_out_2;

  or or_1 (or_1_out, capture_ir, shift_ir, test_logic_reset);
  Sub #(.Bits(6)) sub_1 (.a(NBITS[5:0]), .b(6'b000101), .c_i(1'b0), .s(sub_1_s));  // open: c_o
  BarrelShifter #(.Bits(41), .direction("right")) barrelshifter_1 (
    .in(TDI), .shift(sub_1_s), .out({barrelshifter_1_out_2, barrelshifter_1_out}));
  and and_1 (ir_wen, operating, or_1_out);
  Multiplexer #(.Bits(5)) multiplexer_1 (
    .sel(shift_ir), .in_0(5'b00001), .in_1(barrelshifter_1_out), .out(multiplexer_1_out));
  Register #(.Bits(5)) u_ir (.D(multiplexer_1_out), .C(CLK), .en(ir_wen), .Q(ir));
  and and_2 (dmi_collision_error, update_dr, ir_dmi, dmi_op_rw, DMI_REQ);
  or or_2 (or_2_out, capture_dr, shift_dr);
  xor xor_1 (dmi_op_rw, dmi[0], dmi[1]);
  and and_3 (bypass_wen, or_2_out, operating, ir_bypass);
  and and_4 (idcode_wen, or_2_out, operating, ir_idcode);
  and and_5 (dtcms_wen, or_2_out, operating, ir_dtmcs);
  and and_6 (dmi_wen, or_2_out, operating, ir_dmi);
  Sub #(.Bits(6)) sub_2 (.a(NBITS[5:0]), .b(6'b000001), .c_i(1'b0), .s(sub_2_s));  // open: c_o
  BarrelShifter #(.Bits(41), .direction("right")) barrelshifter_2 (
    .in(TDI), .shift(sub_2_s), .out(barrelshifter_2_out));
  D_FF d_ff_1 (.D(DMI_ACK), .C(CLK), .Q(d_ff_1_q));  // open: nQ
  Register #(.Bits(32)) register_1 (.D(DMI_RDATA), .C(CLK), .en(dmi_tx_end), .Q(dmi_data_d));
  Register #(.Bits(2)) register_2 (.D(DMI_STATUS), .C(CLK), .en(dmi_tx_end), .Q(dmi_status_t));
  D_FF d_ff_2 (.D(d_ff_1_q), .C(CLK), .Q(dmi_ack_t));  // open: nQ
  Multiplexer multiplexer_2 (.sel(shift_dr), .in_0(1'b0), .in_1(barrelshifter_2_out[0]), .out(multiplexer_2_out));
  Register u_bypass (.D(multiplexer_2_out), .C(CLK), .en(bypass_wen), .Q(bypass));
  Multiplexer #(.Bits(2)) multiplexer_3 (
    .sel(dmi_collision_error), .in_0(dmistat_sticky), .in_1(2'b11), .out(multiplexer_3_out));
  Multiplexer #(.Bits(2)) multiplexer_4 (.sel(DMI_REQ), .in_0(2'b00), .in_1(2'b11), .out(multiplexer_4_out));
  and and_7 (clear_dmistat, update_dr, ir_dtmcs, dtmcs[16]);
  Multiplexer #(.Bits(2)) multiplexer_5 (
    .sel(clear_dmistat), .in_0(multiplexer_3_out), .in_1(2'b00), .out(multiplexer_5_out));
  Sub #(.Bits(6)) sub_3 (.a(NBITS[5:0]), .b(6'b100000), .c_i(1'b0), .s(sub_3_s));  // open: c_o
  or or_3 (or_3_out, clear_dmistat, dmi_collision_error);
  Decoder #(.Selector_Bits(3)) decoder_1 (
    .sel(CMD), .out_0(decoder_1_out_0), .out_1(decoder_1_out_1), .out_2(decoder_1_out_2),
    .out_3(decoder_1_out_3), .out_4(decoder_1_out_4));  // open: out_5, out_6, out_7
  BarrelShifter #(.Bits(41), .direction("right")) barrelshifter_3 (
    .in(TDI), .shift(sub_3_s), .out({barrelshifter_3_out_2, barrelshifter_3_out}));
  nor nor_1 (nor_1_out, dmistat_sticky[0], dmistat_sticky[1]);
  Multiplexer #(.Bits(8)) multiplexer_6 (.sel(cmd_tmsseqenter), .in_0(sub_4_s), .in_1(NBITS), .out(multiplexer_6_out));
  Multiplexer #(.Bits(32)) multiplexer_7 (
    .sel(shift_dr), .in_0(32'h1), .in_1(barrelshifter_3_out),
    .out({multiplexer_7_out_4, multiplexer_7_out_3, multiplexer_7_out_2, multiplexer_7_out[0]}));
  Register #(.Bits(2)) register_3 (.D(multiplexer_5_out), .C(CLK), .en(or_3_out), .Q(dmistat_sticky));
  Multiplexer #(.Bits(2)) multiplexer_8 (
    .sel(nor_1_out), .in_0(dmistat_sticky), .in_1(multiplexer_4_out), .out(dmi_op_d));
  and and_8 (cmd_reset, decoder_1_out_0, REQ);
  and and_9 (cmd_tmsseq, decoder_1_out_1, REQ);
  and and_10 (cmd_scanchain, decoder_1_out_2, REQ);
  and and_11 (cmd_scanchainfliptms, decoder_1_out_3, REQ);
  and and_12 (cmd_stopsimu, decoder_1_out_4, REQ);
  D_FF #(.Bits(8)) d_ff_3 (.D(multiplexer_6_out), .C(CLK), .Q(d_ff_3_q));  // open: nQ
  Sub #(.Bits(8)) sub_4 (.a(d_ff_3_q), .b(8'h1), .c_i(1'b0), .s(sub_4_s));  // open: c_o
  Register idcode_reserved0 (.D(multiplexer_7_out[0]), .C(CLK), .en(idcode_wen), .Q(idcode[0]));
  Register #(.Bits(11)) idcode_manufid (.D(multiplexer_7_out_2), .C(CLK), .en(idcode_wen), .Q(idcode[11:1]));
  Register #(.Bits(16)) idcode_partnumber (.D(multiplexer_7_out_3), .C(CLK), .en(idcode_wen), .Q(idcode[27:12]));
  Register #(.Bits(4)) idcode_version (.D(multiplexer_7_out_4), .C(CLK), .en(idcode_wen), .Q(idcode[31:28]));
  Comparator #(.Signed("true"), .Bits(8)) comparator_1 (
    .a(sub_4_s), .b({8{1'b0}}), .eq(comparator_1_eq));  // open: gt, lt
  or or_4 (or_4_out, cmd_scanchain, cmd_scanchainfliptms);
  nor nor_2 (nor_2_out, dmistat_sticky[0], dmistat_sticky[1]);
  or or_5 (or_5_out, dmi_tx_start, dmi_tx_end);
  not not_1 (not_1_out, cmd_tmsseqdone);
  not not_2 (not_2_out, cmd_tmsseqdone);
  and and_13 (and_13_out, cmd_tmsseq, comparator_1_eq);
  and and_14 (cmd_tmsseqoperating, REQ, not_1_out);
  RISING_EDGE rising_edge_1 (.clk(CLK), .d(cmd_tmsseq), .o(cmd_tmsseqenter));
  or or_6 (or_6_out, not_2_out, or_4_out);
  not not_3 (not_3_out, DMI_REQ);
  and and_15 (dmi_tx_end, DMI_REQ, dmi_ack_t);
  Register register_4 (.D(dmi_tx_start), .C(CLK), .en(or_5_out), .Q(DMI_REQ));
  and and_16 (operating, REQ, or_6_out);
  RS_FF_AS rs_ff_as_1 (.S(and_13_out), .R(not_4_out), .Q(cmd_tmsseqdone));  // open: nQ
  not not_4 (not_4_out, cmd_tmsseq);
  and and_17 (dmi_tx_start, update_dr, ir_dmi, dmi_op_rw, nor_2_out, not_3_out);
  Sub #(.Bits(6)) sub_5 (.a(NBITS[5:0]), .b(6'b101001), .c_i(1'b0), .s(sub_5_s));  // open: c_o
  and and_18 (and_18_out, REQ, not_5_out);
  not not_5 (not_5_out, cmd_tmsseq);
  and and_19 (and_19_out, not_6_out, dmi[1]);
  not not_6 (not_6_out, dmi[0]);
  BarrelShifter #(.Bits(41), .direction("right")) barrelshifter_4 (
    .in(TDI), .shift(sub_5_s), .out(barrelshifter_4_out));
  Multiplexer #(.Bits(41)) multiplexer_9 (
    .sel(shift_dr), .in_0({{7{1'b0}}, dmi_data_d, dmi_op_d}), .in_1(barrelshifter_4_out),
    .out({multiplexer_9_out_3, multiplexer_9_out_2, multiplexer_9_out}));
  or or_7 (or_7_out, cmd_tmsseqdone, and_18_out);
  Multiplexer #(.Bits(41)) multiplexer_10 (
    .sel(cmd_tmsseqenter), .in_0({1'b0, register_5_q_2}), .in_1(TMS), .out(multiplexer_10_out));
  Register dmi_op_latch (.D(and_19_out), .C(CLK), .en(dmi_tx_start), .Q(DMI_WRITE));
  Register #(.Bits(7)) dmi_addr_latch (.D(dmi[40:34]), .C(CLK), .en(dmi_tx_start), .Q(DMI_ADDR));
  Register #(.Bits(32)) dmi_wdata_latch (.D(dmi[33:2]), .C(CLK), .en(dmi_tx_start), .Q(DMI_WDATA));
  D_FF d_ff_4 (.D(or_7_out), .C(CLK), .Q(ACK));  // open: nQ
  Multiplexer multiplexer_11 (.sel(cmd_tmsseq), .in_0(cmd_scanchainfliptms), .in_1(multiplexer_10_out[0]), .out(tms_0));
  Register #(.Bits(41)) register_5 (
    .D(multiplexer_10_out), .C(CLK), .en(cmd_tmsseq), .Q({register_5_q_2, register_5_q[0]}));
  Register #(.Bits(2)) dmi_op (.D(multiplexer_9_out), .C(CLK), .en(dmi_wen), .Q(dmi[1:0]));
  Register #(.Bits(32)) dmi_data (.D(multiplexer_9_out_2), .C(CLK), .en(dmi_wen), .Q(dmi[33:2]));
  Register #(.Bits(7)) u_dmi_addr (.D(multiplexer_9_out_3), .C(CLK), .en(dmi_wen), .Q(dmi[40:34]));
  Multiplexer #(.Bits(4)) multiplexer_12 (
    .sel(cmd_reset), .in_0(state_lut_out), .in_1(4'b0000), .out(multiplexer_12_out));
  Register #(.Bits(4)) state (.D(multiplexer_12_out), .C(CLK), .en(cmd_tmsseqoperating), .Q(state_q));
  Demultiplexer #(.Selector_Bits(4)) demultiplexer_1 (
    .sel(state_q), .in(operating), .out_0(test_logic_reset), .out_1(run_test_idle), .out_2(select_dr_scan),
    .out_3(select_ir_scan), .out_4(capture_ir), .out_5(shift_ir), .out_6(exit1_ir), .out_7(pause_ir),
    .out_8(exit2_ir), .out_9(update_ir), .out_10(capture_dr), .out_11(shift_dr), .out_12(exit1_dr),
    .out_13(pause_dr), .out_14(exit2_dr), .out_15(update_dr));
  LookUpTable #(.Bits(4)) state_lut (
    .in0(tms_0), .in1(state_q[0]), .in2(state_q[1]), .in3(state_q[2]), .in4(state_q[3]), .out(state_lut_out));
  Sub #(.Bits(6)) sub_6 (.a(NBITS[5:0]), .b(6'b100000), .c_i(1'b0), .s(sub_6_s));  // open: c_o
  BarrelShifter #(.Bits(41), .direction("right")) barrelshifter_5 (
    .in(TDI), .shift(sub_6_s), .out({barrelshifter_5_out_2, barrelshifter_5_out}));
  not not_7 (not_7_out, CLK);
  not not_8 (not_8_out, CLK);
  Multiplexer #(.Bits(32)) multiplexer_13 (
    .sel(shift_dr), .in_0({20'h1, dmi_op_d, 10'h71}), .in_1(barrelshifter_5_out),
    .out({multiplexer_13_out_6, multiplexer_13_out_5, multiplexer_13_out_4, multiplexer_13_out_3, multiplexer_13_out_2, multiplexer_13_out}));
  D_FF d_ff_5 (.D(bypass), .C(not_7_out), .Q(d_ff_5_q[0]));  // open: nQ
  D_FF #(.Bits(32)) d_ff_6 (.D(idcode), .C(not_9_out), .Q(d_ff_6_q));  // open: nQ
  not not_9 (not_9_out, CLK);
  D_FF #(.Bits(32)) d_ff_7 (.D(dtmcs), .C(not_8_out), .Q(d_ff_7_q));  // open: nQ
  D_FF #(.Bits(41)) d_ff_8 (.D(dmi), .C(not_10_out), .Q(d_ff_8_q));  // open: nQ
  not not_10 (not_10_out, CLK);
  LookUpTable #(.Bits(2)) lookuptable_1 (
    .in0(ir[0]), .in1(ir[1]), .in2(ir[2]), .in3(ir[3]), .in4(ir[4]), .out(lookuptable_1_out));
  Multiplexer #(.Selector_Bits(2), .Bits(41)) multiplexer_14 (
    .sel(lookuptable_1_out), .in_0({TDI[39:0], d_ff_5_q[0]}), .in_1({TDI[8:0], d_ff_6_q}),
    .in_2({TDI[8:0], d_ff_7_q}), .in_3(d_ff_8_q), .out(multiplexer_14_out));
  Decoder #(.Selector_Bits(2)) decoder_2 (
    .sel(lookuptable_1_out), .out_0(ir_bypass), .out_1(ir_idcode), .out_2(ir_dtmcs), .out_3(ir_dmi));
  Register #(.Bits(4)) dtmcs_version (.D(multiplexer_13_out), .C(CLK), .en(dtcms_wen), .Q(dtmcs[3:0]));
  Register #(.Bits(6)) dtmcs_abits (.D(multiplexer_13_out_2), .C(CLK), .en(dtcms_wen), .Q(dtmcs[9:4]));
  Register #(.Bits(2)) dtmcs_dmistat (.D(multiplexer_13_out_3), .C(CLK), .en(dtcms_wen), .Q(dtmcs[11:10]));
  Register #(.Bits(3)) dtmcs_idle (.D(multiplexer_13_out_4), .C(CLK), .en(dtcms_wen), .Q(dtmcs[14:12]));
  Register dtmcs_reserved0 (.D(multiplexer_13_out_5[15]), .C(CLK), .en(dtcms_wen), .Q(dtmcs[15]));
  Register dtmcs_dmireset (.D(multiplexer_13_out_5[16]), .C(CLK), .en(dtcms_wen), .Q(dtmcs[16]));
  Register dtmcs_dmihardreset (.D(multiplexer_13_out_5[17]), .C(CLK), .en(dtcms_wen), .Q(dtmcs[17]));
  Register #(.Bits(14)) dtmcs_reserved1 (.D(multiplexer_13_out_6), .C(CLK), .en(dtcms_wen), .Q(dtmcs[31:18]));
  not not_11 (not_11_out, CLK);
  D_FF #(.Bits(5)) d_ff_9 (.D(ir), .C(not_11_out), .Q(d_ff_9_q));  // open: nQ
  Multiplexer #(.Bits(41)) multiplexer_15 (
    .sel(shift_ir), .in_0(multiplexer_14_out), .in_1({TDI[35:0], d_ff_9_q}), .out(TDO));

  // Other names for the same wires on the sheet: dmi_addr_t[6:0] = dmi[40:34]; dmi_busy = DMI_REQ;
  //   dmi_data[31:0] = dmi[33:2]; dmi_op[1:0] = dmi[1:0]; dmi_rdata_t[31:0] = dmi_data_d;
  //   dtmcs_abits[5:0] = dtmcs[9:4]; dtmcs_dmihardreset = dtmcs[17]; dtmcs_dmireset = dtmcs[16];
  //   dtmcs_dmistat[1:0] = dtmcs[11:10]; dmistat[1:0] = dmi_op_d; dtmcs_dmistat_d[1:0] = dmi_op_d;
  //   dtmcs_idle[2:0] = dtmcs[14:12]; dtmcs_reserved0 = dtmcs[15]; dtmcs_reserved1[13:0] = dtmcs[31:18];
  //   dtmcs_version[3:0] = dtmcs[3:0]; idcode_manufid[10:0] = idcode[11:1]; idcode_partnumber[15:0] = idcode[27:12];
  //   idcode_reserved0 = idcode[0]; idcode_version[3:0] = idcode[31:28]

  // Notes on the sheet:
  //   Read!
  //   This is a version of the JTAG TAP modified
  //   for parallel reads and writes. This is 
  //   to make debugging performance better.
  //   If you want to see a real TAP, look at
  //   RV5-TAP.dig.
  //   Register Write Enables
  //   We write to IR whenever we're in
  //   capture-ir, shift-ir, or test-logic-reset.
  //   ir register
  //   dmi Management
  //   Is the dmi op either a read or write?
  //   We keep dmi-req high until we
  //   get a dmi-ack, so this is effectively dmi-busy.
  //   If we try to send an instruction to dmi while it
  //   is busy, we run into a collision!
  //   We write to one of the data registers
  //   when we're in capture-dr or shift-dr and
  //   the respective id is in ir.
  //   Inputs
  //   bypass register
  //   The clock for the state machine.
  //   Acknowledgement from the dmi. Indicates operation completion.
  //   The data being read back over the dmi (if reading).
  //   The status of the current operation.
  //   Things to load into registers on capture and test-logic-reset
  //   IR should point at IDCODE on test-logic-reset, and
  //   should contain the lower bits 0b01 on capture-ir.
  //   This does both.
  //   The bypass register should be 0 on its capture-dr.
  //   We don't have a real idcode, but we can make one up.
  //   We capture dmistat and rdata. The address doesn't matter,
  //   since we're capturing a result and not issuing a command.
  //   A dmireset being written to dtmcs
  //   means that we should clear dmistat.
  //   We modify dmistat on collision error
  //   and explicit clearing.
  //   We reflect the busy status in dmistat
  //   in a non-sticky way for nop usage.
  //   idcode register
  //   CMD parsing & operation
  //   Parse out cmd
  //   Count through TMS
  //   Respectively:
  //   Version 0.13 of debug spec, 
  //   7 bits of address in dmi,
  //   the current error code, a hint to avoid collisions,
  //   and a bunch of dummy or write-only data.
  //   We can start a transation if our
  //   operation is a read or wite, dmi is
  //   not busy, and we don't have any 
  //   sticky error.
  //   If we were doing an operation (so
  //   dmi-req is high) but we've received
  //   an acknowledgement, it's time to
  //   end the transaction.
  //   dmi-req is set high whenever we have
  //   a dmi-tx_start and set low on every
  //   dmi-tx_end
  //   Outputs
  //   We hold dmi-req high from the moment
  //   we issue a command to when we're
  //   told it's been completed.
  //   Whether we're writing or reading for
  //   this transaction.
  //   Which address in the debug module
  //   we're reading from or writing to.
  //   The data we might be writing
  //   to a location in the debug module.
  //   dmi register
  //   Raise ack the tick after we finish our work
  //   Get the next bit of tms every tick
  //   State Machine
  //   We manage the state machine and
  //   decode the current state.
  //   dtmcs register
  //   contents of state_lut (hex, n*v repeats v):
  //   1,0,1,2,a,3,4,0,5,6,5,6,7,9,7,8,5,9,1,2,b,c,b,c,d,f,d,e,b,f,1,2
  //   IR Decoding & tdo
  //   We decode ir and determine what
  //   should go in tdo.
  //   contents of lookuptable_1 (hex, n*v repeats v):
  //   0,1,14*0,2,3
endmodule
