// Digital circuit ONE-HOT-SEL-32x12.dig as structural Verilog
module ONE_HOT_SEL_32x12 (
  input  [31:0] _0,
  input  _0_sel,
  input  [31:0] _1,
  input  _1_sel,
  input  [31:0] _2,
  input  _2_sel,
  input  [31:0] _3,
  input  _3_sel,
  input  [31:0] _4,
  input  _4_sel,
  input  [31:0] _5,
  input  _5_sel,
  input  [31:0] _6,
  input  _6_sel,
  input  [31:0] _7,
  input  _7_sel,
  input  [31:0] _8,
  input  _8_sel,
  input  [31:0] _9,
  input  _9_sel,
  input  [31:0] _10,
  input  _10_sel,
  input  [31:0] _11,
  input  _11_sel,
  output [31:0] out
);

  wire [31:0] and_1_out, and_2_out, and_3_out, and_4_out, and_5_out, and_6_out, and_7_out, and_8_out,
       and_9_out, and_10_out, and_11_out, and_12_out, bit_expand_32_1_o, bit_expand_32_2_o,
       bit_expand_32_3_o, bit_expand_32_4_o, bit_expand_32_5_o, bit_expand_32_6_o, bit_expand_32_7_o,
       bit_expand_32_8_o, bit_expand_32_9_o, bit_expand_32_10_o, bit_expand_32_11_o, bit_expand_32_12_o,
       or_1_out, or_2_out, or_3_out, or_4_out, or_5_out, or_6_out, or_7_out, or_8_out, or_9_out, or_10_out;

  BIT_EXPAND_32 bit_expand_32_1 (.I(_0_sel), .O(bit_expand_32_1_o));
  BIT_EXPAND_32 bit_expand_32_2 (.I(_1_sel), .O(bit_expand_32_2_o));
  BIT_EXPAND_32 bit_expand_32_3 (.I(_2_sel), .O(bit_expand_32_3_o));
  BIT_EXPAND_32 bit_expand_32_4 (.I(_3_sel), .O(bit_expand_32_4_o));
  BIT_EXPAND_32 bit_expand_32_5 (.I(_4_sel), .O(bit_expand_32_5_o));
  BIT_EXPAND_32 bit_expand_32_6 (.I(_5_sel), .O(bit_expand_32_6_o));
  BIT_EXPAND_32 bit_expand_32_7 (.I(_6_sel), .O(bit_expand_32_7_o));
  BIT_EXPAND_32 bit_expand_32_8 (.I(_7_sel), .O(bit_expand_32_8_o));
  BIT_EXPAND_32 bit_expand_32_9 (.I(_8_sel), .O(bit_expand_32_9_o));
  BIT_EXPAND_32 bit_expand_32_10 (.I(_9_sel), .O(bit_expand_32_10_o));
  BIT_EXPAND_32 bit_expand_32_11 (.I(_10_sel), .O(bit_expand_32_11_o));
  BIT_EXPAND_32 bit_expand_32_12 (.I(_11_sel), .O(bit_expand_32_12_o));
  assign and_1_out = _0 & bit_expand_32_1_o;  // And and_1, 32 bits wide
  assign and_2_out = _1 & bit_expand_32_2_o;  // And and_2, 32 bits wide
  assign and_3_out = _2 & bit_expand_32_3_o;  // And and_3, 32 bits wide
  assign and_4_out = _3 & bit_expand_32_4_o;  // And and_4, 32 bits wide
  assign and_5_out = _4 & bit_expand_32_5_o;  // And and_5, 32 bits wide
  assign and_6_out = _5 & bit_expand_32_6_o;  // And and_6, 32 bits wide
  assign and_7_out = _6 & bit_expand_32_7_o;  // And and_7, 32 bits wide
  assign and_8_out = _7 & bit_expand_32_8_o;  // And and_8, 32 bits wide
  assign and_9_out = _8 & bit_expand_32_9_o;  // And and_9, 32 bits wide
  assign and_10_out = _9 & bit_expand_32_10_o;  // And and_10, 32 bits wide
  assign and_11_out = _10 & bit_expand_32_11_o;  // And and_11, 32 bits wide
  assign and_12_out = _11 & bit_expand_32_12_o;  // And and_12, 32 bits wide
  assign or_1_out = and_1_out | and_2_out;  // Or or_1, 32 bits wide
  assign or_2_out = and_3_out | and_4_out;  // Or or_2, 32 bits wide
  assign or_3_out = and_5_out | and_6_out;  // Or or_3, 32 bits wide
  assign or_4_out = and_7_out | and_8_out;  // Or or_4, 32 bits wide
  assign or_5_out = and_9_out | and_10_out;  // Or or_5, 32 bits wide
  assign or_6_out = and_11_out | and_12_out;  // Or or_6, 32 bits wide
  assign or_7_out = or_1_out | or_2_out;  // Or or_7, 32 bits wide
  assign or_8_out = or_3_out | or_4_out;  // Or or_8, 32 bits wide
  assign or_9_out = or_5_out | or_6_out;  // Or or_9, 32 bits wide
  assign or_10_out = or_7_out | or_8_out;  // Or or_10, 32 bits wide
  assign out = or_10_out | or_9_out;  // Or or_11, 32 bits wide

  // Notes on the sheet:
  //   ONE-HOT-SEl-32x12
endmodule
