// Digital circuit ONE-HOT-SEL-32x5.dig as structural Verilog
module ONE_HOT_SEL_32x5 (
  input  [31:0] _0,
  input  _0_sel,
  input  [31:0] _1,
  input  _1_sel,
  input  [31:0] _2,
  input  _2_sel,
  input  [31:0] _3,
  input  _3_sel,
  input  [31:0] _4,
  input  _4_sel,
  output [31:0] out
);

  wire [31:0] and_1_out, and_2_out, and_3_out, and_4_out, and_5_out, bit_expand_32_1_o, bit_expand_32_2_o,
       bit_expand_32_3_o, bit_expand_32_4_o, bit_expand_32_5_o, or_1_out, or_2_out, or_3_out;

  BIT_EXPAND_32 bit_expand_32_1 (.I(_0_sel), .O(bit_expand_32_1_o));
  BIT_EXPAND_32 bit_expand_32_2 (.I(_1_sel), .O(bit_expand_32_2_o));
  BIT_EXPAND_32 bit_expand_32_3 (.I(_2_sel), .O(bit_expand_32_3_o));
  BIT_EXPAND_32 bit_expand_32_4 (.I(_3_sel), .O(bit_expand_32_4_o));
  BIT_EXPAND_32 bit_expand_32_5 (.I(_4_sel), .O(bit_expand_32_5_o));
  assign and_1_out = _0 & bit_expand_32_1_o;  // And and_1, 32 bits wide
  assign and_2_out = _1 & bit_expand_32_2_o;  // And and_2, 32 bits wide
  assign and_3_out = _2 & bit_expand_32_3_o;  // And and_3, 32 bits wide
  assign and_4_out = _3 & bit_expand_32_4_o;  // And and_4, 32 bits wide
  assign and_5_out = _4 & bit_expand_32_5_o;  // And and_5, 32 bits wide
  assign or_1_out = and_1_out | and_2_out;  // Or or_1, 32 bits wide
  assign or_2_out = and_3_out | and_4_out;  // Or or_2, 32 bits wide
  assign or_3_out = or_1_out | or_2_out;  // Or or_3, 32 bits wide
  assign out = or_3_out | and_5_out;  // Or or_4, 32 bits wide

  // Notes on the sheet:
  //   ONE-HOT-SEl-32x5
endmodule
