// Digital circuit RISING-EDGE.dig as structural Verilog
module RISING_EDGE (
  input  clk,
  input  d,
  output o
);

  wire d_ff_1_nq;

  D_FF d_ff_1 (.D(d), .C(clk), .nQ(d_ff_1_nq));  // open: Q
  and and_1 (o, d, d_ff_1_nq);
endmodule
