// Digital circuit RV5-PROCESSOR.dig as structural Verilog
module RV5_PROCESSOR (
  input  clock,
  input  in_2,
  input  in_3,
  input  in_4,
  input  in_5,
  input  clk
);

  wire abstractauto_wen, abstractcs_busy, abstractcs_wen, ack_drop, alu_bsel, alu_mod, and_5_out, and_8_out,
       and_11_out, and_12_out, and_13_out, and_14_out, and_15_out, and_16_out, and_17_out, and_18_out,
       and_19_out, and_20_out, and_21_out, and_22_out, and_23_out, and_25_out, and_26_out, and_29_out,
       and_34_out, and_39_out, and_42_out, and_44_out, autoexec, br_cond, branch_sel, clk_t, command_exec,
       command_reg_aarpostincrement, command_reg_arg0wen, command_reg_exec, command_reg_jumpprogbuf,
       command_reg_postexec, command_reg_regnoinvalid, command_reg_regwen, command_reg_sel,
       command_reg_transfer, command_reg_validtransferex, command_reg_write, command_unsuported_sel,
       command_wen, comparator_2_eq, comparator_3_eq, comparator_4_eq, comparator_5_eq, comparator_6_eq,
       comparator_7_eq, comparator_8_eq, comparator_9_eq, comparator_10_eq, comparator_11_eq,
       comparator_12_gt, comparator_14_lt, comparator_15_gt, comparator_16_eq, comparator_17_eq,
       comparator_18_eq, comparator_19_eq, comparator_20_eq, comparator_21_eq, comparator_22_eq,
       comparator_23_eq, comparator_25_gt, comparator_26_lt, csr_opclear, csr_opset, csr_useimm, csr_wen,
       d_ff_2_q, d_ff_3_q, d_ff_4_q, d_ff_5_q, d_ff_7_nq, d_ff_8_q, d_ff_9_q, dm_ack, dm_done, dm_start,
       dm_wen, dmcontrol_ackhavereset, dmcontrol_clrresethaltreq, dmcontrol_dmactive, dmcontrol_haltreq,
       dmcontrol_hartreset, dmcontrol_hasel, dmcontrol_ndmreset, dmcontrol_wen, dmi_access, dmi_ren, dmi_req,
       dmi_req_last_low, dmi_wen, dmstatus_allhalted, dmstatus_allnonexistent, dmstatus_allresumeack,
       dmstatus_allrunning, DPC194, dret_sel, ebreak_sel, ecall_sel, EX_MEM_ld_signext, EX_MEM_ram_b,
       EX_MEM_ram_h, EX_MEM_ram_ren, EX_MEM_ram_wen, gdbserver_1_p2, gdbserver_1_p4, gdbserver_1_p5,
       gdbserver_1_p6, haltreq, I_imm_sel, ID_EX_S_imm_sel, ID_EX_U_imm_sel, ID_IF_jalr_sel, ID_IF_mret_sel,
       jal_sel, multiplexer_23_out, multiplexer_25_out, nor_1_out, nor_2_out, not_1_out, not_2_out,
       not_3_out, not_5_out, not_6_out, not_8_out, not_9_out, not_11_out, not_12_out, not_13_out, not_14_out,
       not_15_out, not_16_out, or_1_out, or_2_out, or_3_out, or_5_out, or_7_out, or_8_out, or_9_out,
       or_10_out, or_11_out, or_13_out, or_15_out, or_16_out, or_18_out, or_19_out, or_20_out, reg_wen,
       register_3_q, rising_edge_1_o, rising_edge_4_o, rising_edge_6_o, rs_ff_as_1_q, rv5_tap_1_dmi_req,
       rv5_tap_1_dmi_write, SB_imm_sel, sbcs_wen, stopcond, UJ_imm_sel;
  wire [1:0] alu_asel, alu_opclass, EX_MEM_wb_sel;
  wire [2:0] abstractcs_cmderr, alu_op, and_24_out, command_reg_aarsize, dmi_rdata_lut_out, dmi_wen_lut_out,
       imm_sel, multiplexer_2_out, multiplexer_5_out, not_7_out;
  wire [4:0] command_reg_gprno, multiplexer_20_out, multiplexer_24_out;
  wire [6:0] rv5_tap_1_dmi_addr;
  wire [7:0] command_cmdtype;
  wire [11:0] abstractauto_autoexecdata;
  wire [15:0] abstractauto_autoexecprogbuf, command_reg_regno;
  wire [15:5] sub_1_s;
  wire [15:12] abstractauto_persistent;
  wire [19:0] dmcontrol_hartsel;
  wire [23:23] multiplexer_11_out;
  wire [29:0] EX_IF_pc_jumprel, multiplexer_7_out, multiplexer_8_out, multiplexer_9_out, multiplexer_10_out,
       multiplexer_12_out, multiplexer_13_out, multiplexer_14_out, multiplexer_15_out, multiplexer_16_out,
       multiplexer_17_out, PC_Incr_s;
  wire [30:2] dmcontrol_persistent;
  wire [30:3] dmcontrol_rdata;
  wire [31:0] addr_dm, alu_out, and_35_out, command_persistent_q, csr_out, dcsr, dm_wdata, dmi_memaddr,
       dmi_rdata, dmi_wdata, dpc, EX_MEM_rb, ID_EX_imm, ID_EX_ra, ID_IF_mepc, ID_IF_mtvec, IF_ID_inst,
       mem_out, multiplexer_1_out, multiplexer_18_out, multiplexer_19_out, multiplexer_21_out,
       multiplexer_22_out, multiplexer_26_out, multiplexer_27_out, not_10_out, or_14_out, out_dm, wb;
  wire [31:2] EX_MEM_pc, nextpc;

  Register #(.Bits(32)) u_dmcontrol_persistent (
    .D(dmi_wdata), .C(clk_t), .en(dmcontrol_wen),
    .Q({dmcontrol_haltreq, dmcontrol_persistent[30], dmcontrol_hartreset, dmcontrol_persistent[28:27], dmcontrol_hasel, dmcontrol_hartsel[9:0], dmcontrol_hartsel[19:10], dmcontrol_persistent[5:2], dmcontrol_ndmreset, dmcontrol_dmactive}));
  and and_1 (dmcontrol_clrresethaltreq, dmcontrol_wen, dmi_wdata[2]);
  and and_2 (dmcontrol_rdata[3], dmcontrol_wen, dmi_wdata[3]);
  and and_3 (dmcontrol_ackhavereset, dmcontrol_wen, dmi_wdata[28]);
  and and_4 (dmcontrol_rdata[30], dmcontrol_wen, dmi_wdata[30]);
  D_FF d_ff_1 (.D(dmi_req), .C(clk_t), .nQ(dmi_req_last_low));  // open: Q
  and and_5 (and_5_out, dmcontrol_rdata[30], dcsr[2]);
  RISING_EDGE rising_edge_1 (.clk(clk_t), .d(dmi_req), .o(rising_edge_1_o));
  D_FF d_ff_2 (.D(and_5_out), .C(clk_t), .Q(d_ff_2_q));  // open: nQ
  D_FF d_ff_3 (.D(d_ff_2_q), .C(clk_t), .Q(d_ff_3_q));  // open: nQ
  nor nor_1 (nor_1_out, rising_edge_1_o, abstractcs_busy);
  D_FF d_ff_4 (.D(d_ff_3_q), .C(clk_t), .Q(d_ff_4_q));  // open: nQ
  RISING_EDGE rising_edge_2 (.clk(clk_t), .d(nor_1_out), .o(dm_done));
  or or_1 (or_1_out, dm_done, ack_drop);
  or or_2 (or_2_out, dmcontrol_haltreq, d_ff_4_q);
  and and_6 (dm_start, dmi_req, not_1_out);
  not not_1 (not_1_out, dm_ack);
  and and_7 (ack_drop, not_2_out, dm_ack);
  not not_2 (not_2_out, dmi_req);
  and and_8 (and_8_out, or_2_out, not_3_out);
  not not_3 (not_3_out, dmstatus_allhalted);
  Register register_1 (.D(dm_done), .C(clk_t), .en(or_1_out), .Q(dm_ack));
  RISING_EDGE rising_edge_3 (.clk(clk_t), .d(and_8_out), .o(haltreq));
  not not_4 (dmstatus_allrunning, dmstatus_allhalted);
  Comparator #(.Bits(20)) comparator_1 (
    .a(dmcontrol_hartsel), .b({20{1'b0}}), .gt(dmstatus_allnonexistent));  // open: eq, lt
  RS_FF rs_ff_1 (.S(dmcontrol_rdata[30]), .C(clk_t), .R(dmcontrol_haltreq), .Q(dmstatus_allresumeack));  // open: nQ
  // GdbServer gdbserver_1: pin names not known; wires that end beside it: clk, gdbserver_1_p2, clk_t, gdbserver_1_p4, gdbserver_1_p5, gdbserver_1_p6
  RV5_TAP rv5_tap_1 (
    .TCK(gdbserver_1_p4), .TMS(gdbserver_1_p5), .TDI(gdbserver_1_p6), .DMI_ACK(dm_ack),
    .DMI_RDATA(dmi_rdata), .DMI_STATUS({2{abstractcs_busy}}), .TDO(gdbserver_1_p2),
    .DMI_REQ(rv5_tap_1_dmi_req), .DMI_WDATA(dmi_wdata), .DMI_ADDR(rv5_tap_1_dmi_addr),
    .DMI_WRITE(rv5_tap_1_dmi_write));
  RISING_EDGE rising_edge_4 (.clk(clk_t), .d(dmi_req), .o(rising_edge_4_o));
  Comparator #(.Bits(32)) comparator_2 (.a(dmi_memaddr), .b(32'hffc), .eq(comparator_2_eq));  // open: gt, lt
  Comparator #(.Bits(32)) comparator_3 (.a(dmi_memaddr), .b(32'h1004), .eq(comparator_3_eq));  // open: gt, lt
  Comparator #(.Bits(32)) comparator_4 (.a(dmi_memaddr), .b(32'h1008), .eq(comparator_4_eq));  // open: gt, lt
  Comparator #(.Bits(32)) comparator_5 (.a(dmi_memaddr), .b(32'h100c), .eq(comparator_5_eq));  // open: gt, lt
  Comparator #(.Bits(32)) comparator_6 (.a(dmi_memaddr), .b(32'h1010), .eq(comparator_6_eq));  // open: gt, lt
  Comparator #(.Bits(32)) comparator_7 (.a(dmi_memaddr), .b(32'h1014), .eq(comparator_7_eq));  // open: gt, lt
  Comparator #(.Bits(32)) comparator_8 (.a(dmi_memaddr), .b(32'h1018), .eq(comparator_8_eq));  // open: gt, lt
  Comparator #(.Bits(32)) comparator_9 (.a(dmi_memaddr), .b(32'h101c), .eq(comparator_9_eq));  // open: gt, lt
  Comparator #(.Bits(32)) comparator_10 (.a(dmi_memaddr), .b(32'h1020), .eq(comparator_10_eq));  // open: gt, lt
  D_FF d_ff_5 (.D(rv5_tap_1_dmi_req), .C(clk_t), .Q(d_ff_5_q));  // open: nQ
  and and_9 (dmi_wen, rv5_tap_1_dmi_write, rising_edge_4_o);
  and and_10 (dmi_ren, not_5_out, rising_edge_4_o);
  not not_5 (not_5_out, rv5_tap_1_dmi_write);
  and and_11 (and_11_out, comparator_2_eq, dmi_access, abstractauto_autoexecdata[0]);
  and and_12 (and_12_out, comparator_3_eq, dmi_access, abstractauto_autoexecprogbuf[0]);
  and and_13 (and_13_out, comparator_4_eq, dmi_access, abstractauto_autoexecprogbuf[1]);
  and and_14 (and_14_out, comparator_5_eq, dmi_access, abstractauto_autoexecprogbuf[2]);
  and and_15 (and_15_out, comparator_6_eq, dmi_access, abstractauto_autoexecprogbuf[3]);
  and and_16 (and_16_out, comparator_7_eq, dmi_access, abstractauto_autoexecprogbuf[4]);
  and and_17 (and_17_out, comparator_8_eq, dmi_access, abstractauto_autoexecprogbuf[5]);
  and and_18 (and_18_out, comparator_9_eq, dmi_access, abstractauto_autoexecprogbuf[6]);
  and and_19 (and_19_out, comparator_10_eq, dmi_access, abstractauto_autoexecprogbuf[7]);
  D_FF d_ff_6 (.D(d_ff_5_q), .C(clk_t), .Q(dmi_req));  // open: nQ
  or or_3 (or_3_out, dmi_ren, dmi_wen);
  and and_20 (and_20_out, or_3_out, dmi_req);
  or or_4 (autoexec, and_11_out, and_12_out, and_13_out, and_14_out, and_15_out, and_16_out, and_17_out, and_18_out, and_19_out);
  RISING_EDGE rising_edge_5 (.clk(clk_t), .d(and_20_out), .o(dmi_access));
  LookUpTable #(.Bits(3)) dmi_rdata_lut (
    .in0(rv5_tap_1_dmi_addr[0]), .in1(rv5_tap_1_dmi_addr[1]), .in2(rv5_tap_1_dmi_addr[2]),
    .in3(rv5_tap_1_dmi_addr[3]), .in4(rv5_tap_1_dmi_addr[4]), .in5(rv5_tap_1_dmi_addr[5]),
    .in6(rv5_tap_1_dmi_addr[6]), .out(dmi_rdata_lut_out));
  LookUpTable #(.Bits(3)) dmi_wen_lut (
    .in0(rv5_tap_1_dmi_addr[0]), .in1(rv5_tap_1_dmi_addr[1]), .in2(rv5_tap_1_dmi_addr[2]),
    .in3(rv5_tap_1_dmi_addr[3]), .in4(rv5_tap_1_dmi_addr[4]), .in5(rv5_tap_1_dmi_addr[5]),
    .in6(rv5_tap_1_dmi_addr[6]), .out(dmi_wen_lut_out));
  LookUpTable #(.Bits(32)) dmi_memaddr_lut (
    .in0(rv5_tap_1_dmi_addr[0]), .in1(rv5_tap_1_dmi_addr[1]), .in2(rv5_tap_1_dmi_addr[2]),
    .in3(rv5_tap_1_dmi_addr[3]), .in4(rv5_tap_1_dmi_addr[4]), .in5(rv5_tap_1_dmi_addr[5]),
    .in6(rv5_tap_1_dmi_addr[6]), .out(dmi_memaddr));
  and and_21 (and_21_out, command_reg_regnoinvalid, command_reg_transfer);
  Multiplexer #(.Selector_Bits(3), .Bits(32)) multiplexer_1 (
    .sel(dmi_rdata_lut_out), .in_0({32{1'b0}}), .in_1(out_dm),
    .in_2({dmcontrol_haltreq, dmcontrol_rdata[30], dmcontrol_hartreset, dmcontrol_ackhavereset, 1'b0, dmcontrol_hasel, dmcontrol_hartsel[9:0], dmcontrol_hartsel[19:10], 2'b00, dmcontrol_rdata[3], dmcontrol_clrresethaltreq, dmcontrol_ndmreset, dmcontrol_dmactive}),
    .in_3({{14{1'b0}}, {2{dmstatus_allresumeack}}, {2{dmstatus_allnonexistent}}, 2'b00, {2{dmstatus_allrunning}}, {2{dmstatus_allhalted}}, 8'h82}),
    .in_4(32'h111ffc), .in_5({19'h4000, abstractcs_busy, 1'b0, abstractcs_cmderr, 8'h1}),
    .in_6(32'h20000000), .in_7({abstractauto_autoexecprogbuf, 4'b0000, abstractauto_autoexecdata}),
    .out(multiplexer_1_out));
  Demultiplexer #(.Selector_Bits(3)) demultiplexer_1 (
    .sel(dmi_wen_lut_out), .in(dmi_wen), .out_1(dmcontrol_wen), .out_2(abstractcs_wen), .out_3(command_wen),
    .out_4(sbcs_wen), .out_5(abstractauto_wen));  // open: out_0, out_6, out_7
  Comparator #(.Bits(32)) comparator_11 (.a(dmi_memaddr), .b({32{1'b0}}), .eq(comparator_11_eq));  // open: gt, lt
  and and_22 (and_22_out, dmi_ren, dmi_req, dmi_req_last_low);
  not not_6 (not_6_out, comparator_11_eq);
  Comparator #(.Bits(3)) comparator_12 (.a(command_reg_aarsize), .b(3'b010), .gt(comparator_12_gt));  // open: eq, lt
  Register #(.Bits(32)) register_2 (.D(multiplexer_1_out), .C(clk_t), .en(and_22_out), .Q(dmi_rdata));
  and and_23 (and_23_out, dmi_wen, not_6_out);
  or or_5 (or_5_out, command_unsuported_sel, comparator_12_gt, and_21_out, command_reg_aarpostincrement);
  Multiplexer #(.Bits(3)) multiplexer_2 (.sel(or_5_out), .in_0(3'b000), .in_1(3'b010), .out(multiplexer_2_out));
  Multiplexer #(.Bits(32)) multiplexer_3 (.sel(command_reg_arg0wen), .in_0(dmi_wdata), .in_1(ID_EX_ra), .out(dm_wdata));
  or or_6 (dm_wen, and_23_out, command_reg_arg0wen);
  Multiplexer #(.Bits(32)) multiplexer_4 (
    .sel(command_reg_validtransferex), .in_0(dmi_memaddr), .in_1(32'hffc), .out(addr_dm));
  assign and_24_out = not_7_out & abstractcs_cmderr;  // And and_24, 3 bits wide
  assign not_7_out = ~dmi_wdata[10:8];  // Not not_7, 3 bits wide
  Multiplexer #(.Bits(3)) multiplexer_5 (
    .sel(command_reg_exec), .in_0(and_24_out), .in_1(multiplexer_2_out), .out(multiplexer_5_out));
  or or_7 (or_7_out, abstractcs_wen, command_exec);
  Register #(.Bits(3)) u_abstractcs_cmderr (.D(multiplexer_5_out), .C(clk_t), .en(or_7_out), .Q(abstractcs_cmderr));
  Multiplexer multiplexer_6 (.sel(or_8_out), .in_0(clock), .in_1(in_2), .out(clk_t));
  or or_8 (or_8_out, in_3, stopcond);
  and and_25 (and_25_out, branch_sel, br_cond);
  or or_9 (or_9_out, jal_sel, and_25_out);
  Multiplexer #(.Bits(30)) multiplexer_7 (
    .sel(or_9_out), .in_0(PC_Incr_s), .in_1(EX_IF_pc_jumprel), .out(multiplexer_7_out));
  Multiplexer #(.Bits(30)) multiplexer_8 (
    .sel(ID_IF_jalr_sel), .in_0(multiplexer_7_out), .in_1(alu_out[31:2]), .out(multiplexer_8_out));
  Multiplexer #(.Bits(30)) multiplexer_9 (
    .sel(ecall_sel), .in_0(multiplexer_8_out), .in_1(ID_IF_mtvec[31:2]), .out(multiplexer_9_out));
  Register #(.Bits(32)) command_persistent (.D(dmi_wdata), .C(clk_t), .en(command_wen), .Q(command_persistent_q));
  D_FF d_ff_7 (.D(command_wen), .C(clk_t), .nQ(d_ff_7_nq));  // open: Q
  Multiplexer #(.Bits(30)) multiplexer_10 (
    .sel(ID_IF_mret_sel), .in_0(multiplexer_9_out), .in_1(ID_IF_mepc[31:2]), .out(multiplexer_10_out));
  and and_26 (and_26_out, d_ff_7_nq, command_wen);
  nor nor_2 (nor_2_out, abstractcs_cmderr[0], abstractcs_cmderr[1], abstractcs_cmderr[2]);
  Comparator #(.Bits(8)) comparator_13 (
    .a(command_cmdtype), .b({8{1'b0}}), .gt(command_unsuported_sel), .eq(command_reg_sel));  // open: lt
  and and_27 (command_reg_exec, command_exec, command_reg_sel);
  Comparator #(.Bits(16)) comparator_14 (.a(command_reg_regno), .b(16'h1000), .lt(comparator_14_lt));  // open: gt, eq
  Comparator #(.Bits(16)) comparator_15 (.a(command_reg_regno), .b(16'h101f), .gt(comparator_15_gt));  // open: eq, lt
  Multiplexer #(.Bits(32)) multiplexer_11 (
    .sel(and_26_out), .in_0(command_persistent_q), .in_1(dmi_wdata),
    .out({command_cmdtype, multiplexer_11_out[23], command_reg_aarsize, command_reg_aarpostincrement, command_reg_postexec, command_reg_transfer, command_reg_write, command_reg_regno}));
  or or_10 (or_10_out, command_wen, autoexec);
  or or_11 (or_11_out, dmstatus_allhalted, dcsr[15]);
  or or_12 (command_reg_regnoinvalid, comparator_14_lt, comparator_15_gt);
  Multiplexer #(.Bits(30)) multiplexer_12 (
    .sel(or_11_out), .in_0(ID_IF_mtvec[31:2]), .in_1(30'h64), .out(multiplexer_12_out));
  and and_28 (command_exec, or_10_out, nor_2_out);
  Multiplexer #(.Bits(30)) multiplexer_13 (
    .sel(ebreak_sel), .in_0(multiplexer_10_out), .in_1(multiplexer_12_out), .out(multiplexer_13_out));
  and and_29 (and_29_out, dret_sel, dmstatus_allhalted);
  Multiplexer #(.Bits(30)) multiplexer_14 (
    .sel(and_29_out), .in_0(multiplexer_13_out), .in_1(dpc[31:2]), .out(multiplexer_14_out));
  Multiplexer #(.Bits(30)) multiplexer_15 (
    .sel(haltreq), .in_0(multiplexer_14_out), .in_1(30'h64), .out(multiplexer_15_out));
  not not_8 (not_8_out, command_reg_regnoinvalid);
  and and_30 (command_reg_arg0wen, not_9_out, command_reg_validtransferex);
  not not_9 (not_9_out, command_reg_write);
  and and_31 (command_reg_regwen, command_reg_write, command_reg_validtransferex);
  Sub #(.Bits(16)) sub_1 (
    .a(command_reg_regno), .b(16'h1000), .c_i(1'b0), .s({sub_1_s, command_reg_gprno}));  // open: c_o
  and and_32 (command_reg_jumpprogbuf, command_reg_postexec, command_reg_exec);
  and and_33 (command_reg_validtransferex, command_reg_exec, command_reg_transfer, not_8_out);
  Multiplexer #(.Bits(30)) multiplexer_16 (
    .sel(command_reg_jumpprogbuf), .in_0(multiplexer_15_out), .in_1(30'h401), .out(multiplexer_16_out));
  RISING_EDGE rising_edge_6 (.clk(clk_t), .d(dmcontrol_rdata[30]), .o(rising_edge_6_o));
  Multiplexer #(.Bits(30)) multiplexer_17 (
    .sel(rising_edge_6_o), .in_0(multiplexer_16_out), .in_1(30'h65), .out(multiplexer_17_out));
  D_FF #(.Bits(30)) PC_w (.D(multiplexer_17_out), .C(clk_t), .Q(EX_MEM_pc));  // open: nQ
  Add #(.Bits(30)) PC_Incr (.a(EX_MEM_pc), .b(30'h1), .c_i(1'b0), .s(PC_Incr_s));  // open: c_o
  Register #(.Bits(32)) u_abstractauto_persistent (
    .D(dmi_wdata), .C(clk_t), .en(abstractauto_wen),
    .Q({abstractauto_autoexecprogbuf, abstractauto_persistent, abstractauto_autoexecdata}));
  D_FF d_ff_8 (.D(command_exec), .C(clk_t), .Q(d_ff_8_q));  // open: nQ
  and and_34 (and_34_out, command_exec, command_reg_transfer);
  or or_13 (or_13_out, command_exec, d_ff_8_q);
  RV5_INSTR_DECODE rv5_instr_decode_1 (
    .instr(IF_ID_inst), .UJ_imm_sel(UJ_imm_sel), .U_imm_sel(ID_EX_U_imm_sel), .S_imm_sel(ID_EX_S_imm_sel),
    .SB_imm_sel(SB_imm_sel), .I_imm_sel(I_imm_sel), .alu_mod(alu_mod), .ram_wen(EX_MEM_ram_wen),
    .wb_sel(EX_MEM_wb_sel), .ram_ren(EX_MEM_ram_ren), .ecall_sel(ecall_sel), .alu_op(alu_op),
    .ram_b(EX_MEM_ram_b), .ram_h(EX_MEM_ram_h), .reg_wen(reg_wen), .branch_sel(branch_sel),
    .jal_sel(jal_sel), .jalr_sel(ID_IF_jalr_sel), .alu_a_sel(alu_asel), .ld_signext(EX_MEM_ld_signext),
    .csr_wen(csr_wen), .mret_sel(ID_IF_mret_sel), .ebreak_sel(ebreak_sel), .dret_sel(dret_sel),
    .csr_opset(csr_opset), .csr_opclear(csr_opclear), .csr_useimm(csr_useimm));  // open: rs2, rs1, rd, opcode, system_imm
  Multiplexer #(.Bits(32)) multiplexer_18 (
    .sel(csr_useimm), .in_0(ID_EX_ra), .in_1({{27{1'b0}}, IF_ID_inst[19:15]}), .out(multiplexer_18_out));
  Comparator #(.Bits(32)) comparator_16 (.a(dm_wdata), .b({32{1'b0}}), .eq(comparator_16_eq));  // open: gt, lt
  assign not_10_out = ~multiplexer_18_out;  // Not not_10, 32 bits wide
  not not_11 (not_11_out, comparator_16_eq);
  not not_12 (not_12_out, and_34_out);
  Comparator #(.Bits(32)) comparator_17 (.a(dmi_memaddr), .b(32'hffc), .eq(comparator_17_eq));  // open: gt, lt
  Comparator #(.Bits(32)) comparator_18 (.a(out_dm), .b({32{1'b0}}), .eq(comparator_18_eq));  // open: gt, lt
  Comparator #(.Bits(16)) comparator_19 (.a(command_reg_regno), .b(16'h1008), .eq(comparator_19_eq));  // open: gt, lt
  Comparator #(.Bits(12)) comparator_20 (.a(12'h7b0), .b(IF_ID_inst[31:20]), .eq(comparator_20_eq));  // open: gt, lt
  Multiplexer #(.Bits(32)) multiplexer_19 (.sel(command_reg_exec), .in_0(wb), .in_1(out_dm), .out(multiplexer_19_out));
  assign and_35_out = not_10_out & csr_out;  // And and_35, 32 bits wide
  assign or_14_out = multiplexer_18_out | csr_out;  // Or or_14, 32 bits wide
  not not_13 (not_13_out, comparator_18_eq);
  Comparator #(.Bits(32)) comparator_21 (.a(addr_dm), .b(32'h1024), .eq(comparator_21_eq));  // open: gt, lt
  // And and_36 has open pins: In_1=not_11_out, In_2=dm_wen, In_3=not_12_out, In_4=comparator_17_eq, out=open
  // And and_37 has open pins: In_1=comparator_17_eq, In_2=not_13_out, out=open
  Comparator #(.Bits(32)) comparator_22 (
    .a({abstractauto_autoexecprogbuf, 4'b0000, abstractauto_autoexecdata}), .b({32{1'b0}}),
    .eq(comparator_22_eq));  // open: gt, lt
  // And and_38 has open pins: In_1=comparator_20_eq, In_2=csr_wen, out=open
  RV5_IMM rv5_imm_1 (
    .UJ_imm_sel(UJ_imm_sel), .I_imm_sel(I_imm_sel), .SB_imm_sel(SB_imm_sel), .S_imm_sel(ID_EX_S_imm_sel),
    .U_imm_sel(ID_EX_U_imm_sel), .INSTR_32(IF_ID_inst), .imm(ID_EX_imm));
  Multiplexer #(.Bits(5)) multiplexer_20 (
    .sel(command_reg_exec), .in_0(IF_ID_inst[19:15]), .in_1(command_reg_gprno), .out(multiplexer_20_out));
  Multiplexer #(.Bits(32)) multiplexer_21 (
    .sel(csr_opclear), .in_0(multiplexer_18_out), .in_1(and_35_out), .out(multiplexer_21_out));
  and and_39 (and_39_out, comparator_19_eq, command_reg_write, 1'b1, command_reg_transfer, or_13_out);
  not not_14 (not_14_out, comparator_22_eq);
  // And and_40 has open pins: In_1=comparator_21_eq, In_2=dm_wen, In_3=dmi_wdata[2], out=open
  or or_15 (or_15_out, reg_wen, command_reg_regwen);
  Multiplexer #(.Bits(32)) multiplexer_22 (
    .sel(csr_opset), .in_0(multiplexer_21_out), .in_1(or_14_out), .out(multiplexer_22_out));
  RV5_MAIN_CONTROL rv5_main_control_1 (
    .opcode(IF_ID_inst[6:0]), .wb_sel(EX_MEM_wb_sel), .ram_wen(EX_MEM_ram_wen), .ram_ren(EX_MEM_ram_ren),
    .reg_wen(reg_wen), .branch_sel(branch_sel), .jal_sel(jal_sel), .jalr_sel(ID_IF_jalr_sel),
    .alu_asel(alu_asel), .alu_bsel(alu_bsel), .imm_sel(imm_sel), .alu_opclass(alu_opclass));
  Multiplexer multiplexer_23 (.sel(haltreq), .in_0(or_15_out), .in_1(1'b0), .out(multiplexer_23_out));
  Comparator #(.Bits(32)) comparator_23 (.a({EX_MEM_pc, 2'b00}), .b(32'h190), .eq(comparator_23_eq));  // open: gt, lt
  Comparator #(.Bits(32)) comparator_24 (.a({EX_MEM_pc, 2'b00}), .b(32'h194), .eq(DPC194));  // open: gt, lt
  Comparator #(.Bits(32)) comparator_25 (.a({EX_MEM_pc, 2'b00}), .b(32'h1003), .gt(comparator_25_gt));  // open: eq, lt
  Comparator #(.Bits(32)) comparator_26 (.a({EX_MEM_pc, 2'b00}), .b(32'h1021), .lt(comparator_26_lt));  // open: gt, eq
  RS_FF_AS rs_ff_as_1 (.S(autoexec), .R(1'b0), .Q(rs_ff_as_1_q));  // open: nQ
  D_FF d_ff_9 (.D(in_4), .C(clk_t), .Q(d_ff_9_q));  // open: nQ
  Multiplexer #(.Bits(5)) multiplexer_24 (
    .sel(command_reg_regwen), .in_0(IF_ID_inst[11:7]), .in_1(command_reg_gprno), .out(multiplexer_24_out));
  RV5_CSR rv5_csr_1 (
    .clk(clk_t), .addr(IF_ID_inst[31:20]), .w_data(multiplexer_22_out), .wen(csr_wen),
    .pc_in({EX_MEM_pc, 2'b00}), .ecall_sel(ecall_sel), .mret_sel(ID_IF_mret_sel), .ebreak_sel(ebreak_sel),
    .is_debug(dmstatus_allhalted), .haltreq(haltreq), .R_DATA(csr_out), .MTVEC_OUT(ID_IF_mtvec),
    .MEPC_OUT(ID_IF_mepc), .DCSR_OUT(dcsr), .DPC_OUT(dpc));
  or or_16 (or_16_out, comparator_23_eq, DPC194);
  and and_41 (abstractcs_busy, comparator_25_gt, comparator_26_lt);
  Comparator #(.Bits(3)) comparator_27 (.a(abstractcs_cmderr), .b(3'b111));  // open: gt, eq, lt
  not not_15 (not_15_out, d_ff_9_q);
  RV5_GPR rv5_gpr_1 (
    .RS1(multiplexer_20_out), .RS2(IF_ID_inst[24:20]), .D_in(multiplexer_19_out), .clk(clk_t),
    .WEN(multiplexer_23_out), .RD(multiplexer_24_out), .RA(ID_EX_ra), .RB(EX_MEM_rb));  // open: RD0
  or or_17 (dmstatus_allhalted, or_16_out, abstractcs_busy);
  and and_42 (and_42_out, not_15_out, in_4);
  Multiplexer multiplexer_25 (.sel(in_4), .in_0(1'b0), .in_1(1'b0), .out(multiplexer_25_out));
  or or_18 (or_18_out, 1'b0, and_42_out);
  Register register_3 (.D(multiplexer_25_out), .C(clk_t), .en(or_18_out), .Q(register_3_q));
  or or_19 (or_19_out, 1'b0, register_3_q);
  and and_43 (stopcond, or_19_out, in_5);
  RV5_ALU_CONTROL rv5_alu_control_1 ();  // open: inst_30, alu_opclass, funct3, alu_op, alu_mod
  Multiplexer #(.Bits(32)) multiplexer_26 (
    .sel(or_20_out), .in_0(EX_MEM_rb), .in_1(ID_EX_imm), .out(multiplexer_26_out));
  or or_20 (or_20_out, I_imm_sel, ID_EX_S_imm_sel, ID_EX_U_imm_sel);
  Add #(.Bits(30)) PC_JumpRel (.a(EX_MEM_pc), .b(ID_EX_imm[31:2]), .c_i(1'b0), .s(EX_IF_pc_jumprel));  // open: c_o
  Multiplexer #(.Selector_Bits(2), .Bits(32)) multiplexer_27 (
    .sel(alu_asel), .in_0(ID_EX_ra), .in_1({EX_MEM_pc, 2'b00}), .in_2({32{1'b0}}), .in_3({32{1'b0}}),
    .out(multiplexer_27_out));
  RV5_ALU rv5_alu_1 (
    .OP(alu_op), .Y(alu_out), .A(multiplexer_27_out), .B(multiplexer_26_out), .BR(br_cond), .MOD(alu_mod));
  not not_16 (not_16_out, haltreq);
  and and_44 (and_44_out, EX_MEM_ram_wen, not_16_out);
  // RV5_MEMORY rv5_memory_1: pin names not known; wires that end beside it: alu_out, EX_MEM_rb, and_44_out, EX_MEM_ram_ren, clk_t, EX_MEM_ram_b, EX_MEM_ram_h, EX_MEM_ld_signext, {EX_MEM_pc, 2'b00}, addr_dm, dm_wen, dm_wdata, mem_out, IF_ID_inst, out_dm
  Add #(.Bits(30)) add_1 (.a(EX_MEM_pc), .b({30{1'b0}}), .c_i(1'b1), .s(nextpc));  // open: c_o
  Multiplexer #(.Selector_Bits(2), .Bits(32)) multiplexer_28 (
    .sel(EX_MEM_wb_sel), .in_0(alu_out), .in_1({nextpc, 2'b00}), .in_2(mem_out), .in_3(csr_out), .out(wb));

  // Other names for the same wires on the sheet: ID_EX_pc[31:2] = EX_MEM_pc; IF_ID_pc[31:2] = EX_MEM_pc;
  //   MEM_WB_pc[31:2] = EX_MEM_pc; pc[31:2] = EX_MEM_pc;
  //   abstractauto_persistent (some bits) = {abstractauto_autoexecprogbuf, abstractauto_autoexecdata};
  //   abstractauto_rdata (some bits) = {abstractauto_autoexecprogbuf, abstractauto_autoexecdata};
  //   abstractcs_rdata (some bits) = {abstractcs_busy, abstractcs_cmderr}; ID_EX_alu_asel[1:0] = alu_asel;
  //   ID_EX_alu_mod = alu_mod; ID_EX_alu_op[2:0] = alu_op; EX_IF_alu_out[31:0] = alu_out;
  //   EX_MEM_alu_out[31:0] = alu_out; MEM_WB_alu_out[31:0] = alu_out; EX_MEM_csr_out[31:0] = csr_out;
  //   ID_EX_csr_out[31:0] = csr_out; MEM_WB_csr_out[31:0] = csr_out; ID_IF_dcsr[31:0] = dcsr;
  //   dmcontrol_rdata (some bits) = {dmcontrol_haltreq, dmcontrol_hartreset, dmcontrol_ackhavereset, dmcontrol_hasel, dmcontrol_hartsel[9:0], dmcontrol_hartsel[19:10], dmcontrol_clrresethaltreq, dmcontrol_ndmreset, dmcontrol_dmactive};
  //   dmcontrol_persistent (some bits) = {dmcontrol_haltreq, dmcontrol_hartreset, dmcontrol_hasel, dmcontrol_hartsel[9:0], dmcontrol_hartsel[19:10], dmcontrol_ndmreset, dmcontrol_dmactive};
  //   dmcontrol_hartselhi[9:0] = dmcontrol_hartsel[19:10]; dmcontrol_hartsello[9:0] = dmcontrol_hartsel[9:0];
  //   dmcontrol_resumereq = dmcontrol_rdata[30]; dmcontrol_setresethaltreq = dmcontrol_rdata[3];
  //   dmstatus_anynonexistent = dmstatus_allnonexistent;
  //   dmstatus_rdata (some bits) = {{2{dmstatus_allresumeack}}, {2{dmstatus_allnonexistent}}, {2{dmstatus_allrunning}}, {2{dmstatus_allhalted}}};
  //   dmstatus_anyresumeack = dmstatus_allresumeack; dmstatus_anyrunning = dmstatus_allrunning; ID_IF_dpc[31:0] = dpc;
  //   ID_IF_dret_sel = dret_sel; ID_IF_ebreak_sel = ebreak_sel; ID_IF_ecall_sel = ecall_sel;
  //   ID_EX_I_imm_sel = I_imm_sel; imm[31:0] = ID_EX_imm; in_progbuf = abstractcs_busy; inst_out[31:0] = IF_ID_inst;
  //   opcode[6:0] = IF_ID_inst[6:0]; rd[4:0] = IF_ID_inst[11:7]; rs1[4:0] = IF_ID_inst[19:15];
  //   rs2[4:0] = IF_ID_inst[24:20]; system_imm[11:0] = IF_ID_inst[31:20]; dmstatus_anyhalted = dmstatus_allhalted;
  //   is_debug = dmstatus_allhalted; jalr_sel = ID_IF_jalr_sel; ID_EX_ld_signext = EX_MEM_ld_signext;
  //   ld_signext = EX_MEM_ld_signext; MEM_WB_mem_out[31:0] = mem_out; mepc[31:0] = ID_IF_mepc;
  //   mret_sel = ID_IF_mret_sel; mtvec[31:0] = ID_IF_mtvec; pc_jumprel[29:0] = EX_IF_pc_jumprel; ra[31:0] = ID_EX_ra;
  //   ID_EX_ram_b = EX_MEM_ram_b; ram_b = EX_MEM_ram_b; ID_EX_ram_h = EX_MEM_ram_h; ram_h = EX_MEM_ram_h;
  //   ID_EX_ram_ren = EX_MEM_ram_ren; ram_ren = EX_MEM_ram_ren; ID_EX_ram_wen = EX_MEM_ram_wen;
  //   ram_wen = EX_MEM_ram_wen; ID_EX_rb[31:0] = EX_MEM_rb; rb[31:0] = EX_MEM_rb; S_imm_sel = ID_EX_S_imm_sel;
  //   U_imm_sel = ID_EX_U_imm_sel; WB_ID_wb[31:0] = wb; ID_EX_wb_sel[1:0] = EX_MEM_wb_sel;
  //   MEM_WB_wb_sel[1:0] = EX_MEM_wb_sel; wb_sel[1:0] = EX_MEM_wb_sel

  // Notes on the sheet:
  //   clock: Hz: 2147483647
  //   in_5: default 1
  //   clk: Hz: 50000
  //   Debug module registers:
  //   dmcontrol
  //   We store any fields that need to be
  //   persistent in a register:
  //   Every RW field can be directly
  //   extracted for use from the
  //   persistent register:
  //   W1 fields should only be high
  //   for the clock cycle that they're written:
  //   temp stuff
  //   It's useful to have each field separate
  //   for implementing their functionality,
  //   but let's also pack them up
  //   so that the debugger can read them:
  //   (And for convenience, let's 
  //   also expose this:)
  //   Additional debug module logic:
  //   halting
  //   We should halt if we're being asked to via dmcontrol or if we've just completed
  //   a single-step:
  //   Debug park loop > dret
  //   sbcs
  //   We don't support system bus
  //   access, so we can treat this entire
  //   register as effectively read-only:
  //   (We can get away with a hardcoded
  //   number of clock cycles for single-step.)
  //   dret > curr. instr
  //   curr. instr > next instr
  //   dmstatus
  //   Every field in mstatus is read-only.
  //   We know our CPU handles halts in a
  //   single clock cycle, so to avoid complication
  //   we won't hold this signal high.
  //   Determine each field's value:
  //   autoexec
  //   We just check if we're accessing any data/progbuf words
  //   that we're supposed to autoexec on access of:
  //   Pack them up so the debugger
  //   can read them:
  //   TODO: Simplify
  //   Are we reading or writing to dmi
  //   on this clock cycle?
  //   abstractcs
  //   contents of dmi_rdata_lut (hex, n*v repeats v):
  //   4*0,1,11*0,2,3,4,0,0,0,5,0,7,7*0,8*1,16*0,6
  //   contents of dmi_wen_lut (hex, n*v repeats v):
  //   16*0,1,5*0,2,3,5,31*0,4
  //   contents of dmi_memaddr_lut (hex, n*v repeats v):
  //   4*0,ffc,27*0,1004,1008,100c,1010,1014,1018,101c,1020
  //   Determine each field's value:
  //   (especially cmderr...)
  //   memory access
  //   If the debug module is accessing RAM,
  //   it is either because one of the dmi
  //   registers is memory-mapped, or 
  //   we are executing a command that
  //   requires us to do so.
  //   hartinfo
  //   IF: Instruction fetch
  //   command
  //   This is a write-only register. 
  //   We choose to process it entirely on the same cycle it is written.
  //   I should mention that we only implement the access register
  //   command. This is because it contains functionality for arbitrary
  //   code execution, which allows us to do everything else.
  //   Handle persistence and extract all fields:
  //   Figure out if we should be executing
  //   the command:
  //   Split out cmdtype to selectors:
  //   Determine if we need to execute a register access
  //   command:
  //   Figure out if regno is invalid:
  //   Determine if a valid transfer is to be executed:
  //   Will we end up reading a register?
  //   Let's see:
  //   What about writing?
  //   If we end up reading or writing a
  //   register, we'll need its number in
  //   the standard format:
  //   And finally figure out if we need to
  //   jump to the progbuf:
  //   abstractauto
  //   This is an optional register, but OpenOCD
  //   is bugged and requires it. (riscv-collab/riscv-openocd/issues/587)
  //   Store for persistence:
  //   Extract the fields:
  //   Debug stuff
  //   Pack up:
  //   ID: Instruction decode/register file read
  //   For now, address range check is
  //   the most robust way to know if
  //   we're in debug mode.
  //   Might change so debug ROM length
  //   is variable, but for now I KNOW this
  //   works.
  //   EX: Execute/address calculation
  //   MEM: Memory access
  //   WB: Write back
  //   Here we are trying to make this circuit hierarchical
  //       RV5-REGS contains register bank related hw.
  //       RV5-ALU contains ALU related hw
  //       RV5-INSTR-DECODE contains Instruction Reg, and all needed decodes
  //             decoder for immediate sel
  //       RV5-IMM is a combinatorial that extracts the needed immediates, 
  //              and provides the sign-extended 32-bit value thru a MUX.
  //       RV5-PCU needs some fixes.
  //              increments the PC and allows Jumps, and provides next PC for JAL save of PC.
  //   See examples in Digital in particular processors as to how 
  //   to do this.  
  //   TODO: 
  //   1st. Add a test to each element in the hierarchy.
  //   2nd Resize boxes with appropriate SVG for readable packages w. appropriate signals.
  //   We need to:
  //       RV5-INSTR-DECODE: Decodes the instruction set and provides control signals, and FMT
  //            decode for immediate select has been completed.
  //       Implement:
  //            RV5-LOAD-STORE: Provides Load and Store
  //            RV5-MEMORY: Include ROM and RAM.
  //            RV5-IO: Provides a mean to read a program, communicate with a terminal (keyboard/display)
  //            Create a ROM/RAM  bootstrap
  //                 that loads a program.
  //   Note: Assembler test programs can be found at:   
  //      https://github.com/riscv-software-src/riscv-tests
  //   PCU (Program Control Unit, 
  //   PC = PC + 4, or PC = PC += SBimm32
  //   or PC = ALU out or PC += sgn_ext-imm32
  //   for FMT U, and UJ
  //   Need to figure out a way to load memory
  //   with instructions, ideally from RARS.
  //   Check out how MARS does it for MIPS.
  //   NEXT, NEED LOAD AND STORE,
  //   Address comes from ALU output
  //   which goes to memory via see-thru latch
  //    latch,which goes out to memory for 
  //   loading and storing.  reads 32-word
  //   and stores in rd.   Need to figure out a good
  //   approach to read and write to memory 
  //   with Digital and load it at start up.
  //   We need to arbitrate use of memory 
  //   between load/store and fetching instruction.
endmodule
