// Digital circuit RV5-SLL.dig as structural Verilog
module RV5_SLL (
  input  [31:0] in,
  input  [4:0] shift,
  output [31:0] out
);

  wire [23:0] multiplexer_3_out;
  wire [27:0] multiplexer_2_out;
  wire [29:0] multiplexer_1_out;
  wire [31:0] multiplexer_4_out;
  wire [31:24] multiplexer_3_out_2;
  wire [31:28] multiplexer_2_out_2;
  wire [31:30] multiplexer_1_out_2;

  Multiplexer #(.Bits(32)) multiplexer_1 (
    .sel(shift[0]), .in_0(in), .in_1({in[30:0], 1'b0}), .out({multiplexer_1_out_2, multiplexer_1_out}));
  Multiplexer #(.Bits(32)) multiplexer_2 (
    .sel(shift[1]), .in_0({multiplexer_1_out_2, multiplexer_1_out}), .in_1({multiplexer_1_out, 2'b00}),
    .out({multiplexer_2_out_2, multiplexer_2_out}));
  Multiplexer #(.Bits(32)) multiplexer_3 (
    .sel(shift[2]), .in_0({multiplexer_2_out_2, multiplexer_2_out}), .in_1({multiplexer_2_out, 4'b0000}),
    .out({multiplexer_3_out_2, multiplexer_3_out}));
  Multiplexer #(.Bits(32)) multiplexer_4 (
    .sel(shift[3]), .in_0({multiplexer_3_out_2, multiplexer_3_out}), .in_1({multiplexer_3_out, {8{1'b0}}}),
    .out(multiplexer_4_out));
  Multiplexer #(.Bits(32)) multiplexer_5 (
    .sel(shift[4]), .in_0(multiplexer_4_out), .in_1({multiplexer_4_out[15:0], {16{1'b0}}}), .out(out));

  // Notes on the sheet:
  //   RV5-SLL
endmodule
