// Digital circuit RV5-SYSTEM-CONTROL.dig as structural Verilog
module RV5_SYSTEM_CONTROL (
  input  [6:0] opcode,
  input  [2:0] funct3,
  input  [11:0] inst_20_31,
  output csr_wen,
  output csr_opset,
  output csr_opclear,
  output csr_useimm,
  output ecall_sel,
  output ebreak_sel,
  output mret_sel,
  output dret_sel
);

  wire and_1_out, funct3_000, not_1_out, not_2_out, not_3_out, not_4_out, opcode_system,
       otherfromtruth2_1_p13, otherfromtruth2_1_p14, otherfromtruth2_1_p15, otherfromtruth2_1_p16;

  nor nor_1 (funct3_000, funct3[0], funct3[1], funct3[2]);
  and and_1 (and_1_out, funct3_000, opcode_system);
  // OTHERFROMTRUTH2 otherfromtruth2_1: pin names not known; wires that end beside it: inst_20_31[11], inst_20_31[10], inst_20_31[9], inst_20_31[8], inst_20_31[7], inst_20_31[6], inst_20_31[5], inst_20_31[4], inst_20_31[3], inst_20_31[2], inst_20_31[1], inst_20_31[0], otherfromtruth2_1_p13, otherfromtruth2_1_p14, otherfromtruth2_1_p15, otherfromtruth2_1_p16
  not not_1 (not_1_out, funct3[0]);
  and and_2 (csr_opset, not_1_out, funct3[1]);
  and and_3 (csr_opclear, funct3[0], funct3[1]);
  and and_4 (csr_wen, not_2_out, opcode_system);
  not not_2 (not_2_out, funct3_000);
  not not_3 (not_3_out, opcode[2]);
  not not_4 (not_4_out, opcode[3]);
  and and_5 (opcode_system, opcode[0], opcode[1], not_3_out, not_4_out, opcode[4], opcode[5], opcode[6]);
  and and_6 (ecall_sel, and_1_out, otherfromtruth2_1_p13);
  and and_7 (ebreak_sel, and_1_out, otherfromtruth2_1_p14);
  and and_8 (mret_sel, and_1_out, otherfromtruth2_1_p15);
  and and_9 (dret_sel, and_1_out, otherfromtruth2_1_p16);

  assign csr_useimm = funct3[2];

  // Notes on the sheet:
  //   RV5-SYSTEM-CONTROL
endmodule
