// Digital circuit RV5-SYSTEM-CONTROL2.dig as structural Verilog
module RV5_SYSTEM_CONTROL2 (
  input  is_system,
  input  [11:0] inst_20_31,
  input  [2:0] funct3,
  output reg_wen,
  output [1:0] wb_sel,
  output csr_wen,
  output csr_opset,
  output csr_opclear,
  output csr_useimm,
  output is_ecall,
  output is_ebreak,
  output is_mret,
  output is_dret
);

  wire is_priv, nor_1_out, not_1_out, or_1_out, otherfromtruth2_1_p13, otherfromtruth2_1_p14,
       otherfromtruth2_1_p15, otherfromtruth2_1_p16;

  or or_1 (or_1_out, funct3[0], funct3[1], funct3[2]);
  nor nor_1 (nor_1_out, funct3[0], funct3[1], funct3[2]);
  and and_1 (csr_wen, is_system, or_1_out);
  and and_2 (is_priv, nor_1_out, is_system);
  // OTHERFROMTRUTH2 otherfromtruth2_1: pin names not known; wires that end beside it: inst_20_31[11], inst_20_31[10], inst_20_31[9], inst_20_31[8], inst_20_31[7], inst_20_31[6], inst_20_31[5], inst_20_31[4], inst_20_31[3], inst_20_31[2], inst_20_31[1], inst_20_31[0], otherfromtruth2_1_p13, otherfromtruth2_1_p14, otherfromtruth2_1_p15, otherfromtruth2_1_p16
  and and_3 (csr_opset, csr_wen, not_1_out, funct3[1]);
  not not_1 (not_1_out, funct3[0]);
  and and_4 (csr_opclear, csr_wen, funct3[0], funct3[1]);
  and and_5 (csr_useimm, csr_wen, funct3[2]);
  and and_6 (is_ecall, is_priv, otherfromtruth2_1_p13);
  and and_7 (is_ebreak, is_priv, otherfromtruth2_1_p14);
  and and_8 (is_mret, is_priv, otherfromtruth2_1_p15);
  and and_9 (is_dret, is_priv, otherfromtruth2_1_p16);

  assign reg_wen = csr_wen;
  assign wb_sel = {2{csr_wen}};

  // Other names for the same wires on the sheet: is_csr = csr_wen

  // Notes on the sheet:
  //   RV5-SYSTEM-CONTROL
  //   TODO: DOC
endmodule
