// Digital circuit RV5-TAP.dig as structural Verilog
module RV5_TAP (
  input  TCK,
  input  RESET,
  input  TDI,
  input  TMS,
  input  DMI_ACK,
  input  [31:0] DMI_RDATA,
  input  [1:0] DMI_STATUS,
  output TDO,
  output DMI_REQ,
  output [6:0] DMI_ADDR,
  output [31:0] DMI_WDATA,
  output [1:0] DMI_OP,
  output [1:0] E_DMISTAT,
  output E_DMI_BUSY,
  output [1:0] E_STICKY_ERR
);

  wire and_1_out, and_2_out, and_3_out, and_4_out, and_5_out, bypass, bypass_wen, capture_dr, capture_ir,
       decoder_2_out_0, decoder_2_out_2, decoder_2_out_3, decoder_2_out_4, decoder_2_out_5, decoder_2_out_6,
       decoder_2_out_7, decoder_2_out_8, decoder_2_out_9, decoder_2_out_10, decoder_2_out_11,
       decoder_2_out_12, decoder_2_out_14, decoder_2_out_15, decoder_2_out_18, decoder_2_out_19,
       decoder_2_out_20, decoder_2_out_21, decoder_2_out_22, decoder_2_out_23, decoder_2_out_24,
       decoder_2_out_25, decoder_2_out_26, decoder_2_out_27, decoder_2_out_28, decoder_2_out_29,
       decoder_2_out_30, decoder_2_out_31, dmi_wen, dtcms_wen, exit1_dr, exit1_ir, exit2_dr, exit2_ir,
       idcode_wen, ir_bypass, ir_dmi, ir_dtmcs, ir_idcode, ir_wen, multiplexer_3_out, multiplexer_4_out,
       multiplexer_7_out, nor_1_out, not_1_out, not_2_out, not_3_out, or_1_out, or_2_out, or_3_out, or_4_out,
       or_7_out, pause_dr, pause_ir, run_test_idle, select_dr_scan, select_ir_scan, shift_dr, shift_ir,
       tdo_t, test_logic_reset, update_dr, update_ir;
  wire [0:0] multiplexer_5_out;
  wire [1:0] multiplexer_2_out, multiplexer_6_out, multiplexer_9_out_3, priorityencoder_1_num,
       priorityencoder_2_num;
  wire [2:0] multiplexer_9_out_4;
  wire [3:0] multiplexer_5_out_4, multiplexer_9_out, state_lut_out, state_q;
  wire [4:0] ir, multiplexer_1_out;
  wire [5:0] multiplexer_9_out_2;
  wire [6:0] multiplexer_6_out_3;
  wire [10:0] multiplexer_5_out_2;
  wire [13:0] multiplexer_9_out_6;
  wire [15:0] multiplexer_5_out_3;
  wire [17:15] multiplexer_9_out_5;
  wire [31:0] dtmcs, idcode, multiplexer_6_out_2;

  nor nor_1 (nor_1_out, E_STICKY_ERR[0], E_STICKY_ERR[1]);
  or or_1 (or_1_out, DMI_OP[0], DMI_OP[1]);
  or or_2 (or_2_out, dtmcs[16], dtmcs[17]);
  not not_1 (not_1_out, DMI_REQ);
  not not_2 (not_2_out, DMI_STATUS[0]);
  Multiplexer #(.Bits(5)) multiplexer_1 (
    .sel(shift_ir), .in_0(5'b00001), .in_1({TDI, ir[4:1]}), .out(multiplexer_1_out));
  and and_1 (and_1_out, update_dr, ir_dmi, nor_1_out, not_1_out);
  and and_2 (and_2_out, not_2_out, DMI_STATUS[1], DMI_ACK);
  and and_3 (and_3_out, or_1_out, update_dr, DMI_REQ, ir_dmi);
  and and_4 (and_4_out, update_dr, ir_dtmcs, or_2_out);
  and and_5 (and_5_out, update_dr, ir_dtmcs, dtmcs[17]);
  Register #(.Bits(5)) u_ir (.D(multiplexer_1_out), .C(TCK), .en(ir_wen), .Q(ir));
  PriorityEncoder #(.Selector_Bits(2)) priorityencoder_1 (
    .in0(1'b0), .in1(and_4_out), .in2(and_3_out), .in3(and_2_out), .num(priorityencoder_1_num));  // open: any
  or or_3 (or_3_out, and_2_out, and_3_out, and_4_out);
  PriorityEncoder #(.Selector_Bits(2)) priorityencoder_2 (
    .in0(1'b0), .in1(and_1_out), .in2(DMI_ACK), .in3(and_5_out), .num(priorityencoder_2_num));  // open: any
  or or_4 (or_4_out, and_1_out, DMI_ACK, and_5_out);
  Multiplexer #(.Selector_Bits(2), .Bits(2)) multiplexer_2 (
    .sel(priorityencoder_1_num), .in_0(2'b00), .in_1(2'b00), .in_2(2'b11), .in_3(2'b10),
    .out(multiplexer_2_out));
  Multiplexer #(.Selector_Bits(2)) multiplexer_3 (
    .sel(priorityencoder_2_num), .in_0(1'b0), .in_1(1'b1), .in_2(1'b0), .in_3(1'b0), .out(multiplexer_3_out));
  Multiplexer multiplexer_4 (.sel(shift_dr), .in_0(1'b0), .in_1(TDI), .out(multiplexer_4_out));
  Register dmi_busy (.D(multiplexer_3_out), .C(TCK), .en(or_4_out), .Q(DMI_REQ));
  Register #(.Bits(2)) sticky_error (.D(multiplexer_2_out), .C(TCK), .en(or_3_out), .Q(E_STICKY_ERR));
  Register u_bypass (.D(multiplexer_4_out), .C(TCK), .en(bypass_wen), .Q(bypass));
  Multiplexer #(.Bits(32)) multiplexer_5 (
    .sel(shift_dr), .in_0(32'h1), .in_1({TDI, idcode[31:1]}),
    .out({multiplexer_5_out_4, multiplexer_5_out_3, multiplexer_5_out_2, multiplexer_5_out[0]}));
  not not_3 (not_3_out, TCK);
  Register tdo_latch (.D(tdo_t), .C(not_3_out), .en(1'b1), .Q(TDO));
  Register idcode_reserved0 (.D(multiplexer_5_out[0]), .C(TCK), .en(idcode_wen), .Q(idcode[0]));
  Register #(.Bits(11)) idcode_manufid (.D(multiplexer_5_out_2), .C(TCK), .en(idcode_wen), .Q(idcode[11:1]));
  Register #(.Bits(16)) idcode_partnumber (.D(multiplexer_5_out_3), .C(TCK), .en(idcode_wen), .Q(idcode[27:12]));
  Register #(.Bits(4)) idcode_version (.D(multiplexer_5_out_4), .C(TCK), .en(idcode_wen), .Q(idcode[31:28]));
  Register #(.Bits(4)) state (.D(state_lut_out), .C(TCK), .en(1'b1), .Q(state_q));
  Decoder #(.Selector_Bits(4)) decoder_1 (
    .sel(state_q), .out_0(test_logic_reset), .out_1(run_test_idle), .out_2(select_dr_scan),
    .out_3(select_ir_scan), .out_4(capture_ir), .out_5(shift_ir), .out_6(exit1_ir), .out_7(pause_ir),
    .out_8(exit2_ir), .out_9(update_ir), .out_10(capture_dr), .out_11(shift_dr), .out_12(exit1_dr),
    .out_13(pause_dr), .out_14(exit2_dr), .out_15(update_dr));
  LookUpTable #(.Bits(4)) state_lut (
    .in0(TMS), .in1(state_q[0]), .in2(state_q[1]), .in3(state_q[2]), .in4(state_q[3]), .out(state_lut_out));
  Multiplexer #(.Bits(41)) multiplexer_6 (
    .sel(shift_dr), .in_0({{7{1'b0}}, DMI_RDATA, DMI_STATUS}), .in_1({TDI, DMI_ADDR, DMI_WDATA, DMI_OP[1]}),
    .out({multiplexer_6_out_3, multiplexer_6_out_2, multiplexer_6_out}));
  Multiplexer #(.Selector_Bits(5)) multiplexer_7 (
    .sel(ir), .in_0(bypass), .in_1(idcode[0]), .in_2(bypass), .in_3(bypass), .in_4(bypass), .in_5(bypass),
    .in_6(bypass), .in_7(bypass), .in_8(bypass), .in_9(bypass), .in_10(bypass), .in_11(bypass),
    .in_12(bypass), .in_13(bypass), .in_14(bypass), .in_15(bypass), .in_16(dtmcs[0]), .in_17(DMI_OP[0]),
    .in_18(bypass), .in_19(bypass), .in_20(bypass), .in_21(bypass), .in_22(bypass), .in_23(bypass),
    .in_24(bypass), .in_25(bypass), .in_26(bypass), .in_27(bypass), .in_28(bypass), .in_29(bypass),
    .in_30(bypass), .in_31(bypass), .out(multiplexer_7_out));
  Multiplexer multiplexer_8 (.sel(shift_ir), .in_0(multiplexer_7_out), .in_1(ir[0]), .out(tdo_t));
  Register #(.Bits(2)) u_dmi_op (.D(multiplexer_6_out), .C(TCK), .en(dmi_wen), .Q(DMI_OP));
  Register #(.Bits(32)) dmi_data (.D(multiplexer_6_out_2), .C(TCK), .en(dmi_wen), .Q(DMI_WDATA));
  Register #(.Bits(7)) u_dmi_addr (.D(multiplexer_6_out_3), .C(TCK), .en(dmi_wen), .Q(DMI_ADDR));
  Decoder #(.Selector_Bits(5)) decoder_2 (
    .sel(ir), .out_0(decoder_2_out_0), .out_1(ir_idcode), .out_2(decoder_2_out_2), .out_3(decoder_2_out_3),
    .out_4(decoder_2_out_4), .out_5(decoder_2_out_5), .out_6(decoder_2_out_6), .out_7(decoder_2_out_7),
    .out_8(decoder_2_out_8), .out_9(decoder_2_out_9), .out_10(decoder_2_out_10), .out_11(decoder_2_out_11),
    .out_12(decoder_2_out_12), .out_13(decoder_2_out_12), .out_14(decoder_2_out_14),
    .out_15(decoder_2_out_15), .out_16(ir_dtmcs), .out_17(ir_dmi), .out_18(decoder_2_out_18),
    .out_19(decoder_2_out_19), .out_20(decoder_2_out_20), .out_21(decoder_2_out_21),
    .out_22(decoder_2_out_22), .out_23(decoder_2_out_23), .out_24(decoder_2_out_24),
    .out_25(decoder_2_out_25), .out_26(decoder_2_out_26), .out_27(decoder_2_out_27),
    .out_28(decoder_2_out_28), .out_29(decoder_2_out_29), .out_30(decoder_2_out_30), .out_31(decoder_2_out_31));
  or or_5 (ir_wen, capture_ir, shift_ir, test_logic_reset);
  or or_6 (ir_bypass, decoder_2_out_0, decoder_2_out_2, decoder_2_out_3, decoder_2_out_4, decoder_2_out_5, decoder_2_out_6, decoder_2_out_7, decoder_2_out_8, decoder_2_out_9, decoder_2_out_10, decoder_2_out_11, decoder_2_out_12, decoder_2_out_12, decoder_2_out_14, decoder_2_out_15, decoder_2_out_18, decoder_2_out_19, decoder_2_out_20, decoder_2_out_21, decoder_2_out_22, decoder_2_out_23, decoder_2_out_24, decoder_2_out_25, decoder_2_out_26, decoder_2_out_27, decoder_2_out_28, decoder_2_out_29, decoder_2_out_30, decoder_2_out_31);
  or or_7 (or_7_out, capture_dr, shift_dr);
  Multiplexer #(.Bits(32)) multiplexer_9 (
    .sel(shift_dr), .in_0({20'h1, E_STICKY_ERR, 10'h71}), .in_1({TDI, dtmcs[31:12], E_DMISTAT, dtmcs[9:1]}),
    .out({multiplexer_9_out_6, multiplexer_9_out_5, multiplexer_9_out_4, multiplexer_9_out_3, multiplexer_9_out_2, multiplexer_9_out}));
  and and_6 (bypass_wen, or_7_out, ir_bypass);
  and and_7 (idcode_wen, or_7_out, ir_idcode);
  and and_8 (dtcms_wen, or_7_out, ir_dtmcs);
  and and_9 (dmi_wen, or_7_out, ir_dmi);
  Register #(.Bits(4)) dtmcs_version (.D(multiplexer_9_out), .C(TCK), .en(dtcms_wen), .Q(dtmcs[3:0]));
  Register #(.Bits(6)) dtmcs_abits (.D(multiplexer_9_out_2), .C(TCK), .en(dtcms_wen), .Q(dtmcs[9:4]));
  Register #(.Bits(2)) dtmcs_dmistat (.D(multiplexer_9_out_3), .C(TCK), .en(dtcms_wen), .Q(E_DMISTAT));
  Register #(.Bits(3)) dtmcs_idle (.D(multiplexer_9_out_4), .C(TCK), .en(dtcms_wen), .Q(dtmcs[14:12]));
  Register dtmcs_reserved0 (.D(multiplexer_9_out_5[15]), .C(TCK), .en(dtcms_wen), .Q(dtmcs[15]));
  Register dtmcs_dmireset (.D(multiplexer_9_out_5[16]), .C(TCK), .en(dtcms_wen), .Q(dtmcs[16]));
  Register dtmcs_dmihardreset (.D(multiplexer_9_out_5[17]), .C(TCK), .en(dtcms_wen), .Q(dtmcs[17]));
  Register #(.Bits(14)) dtmcs_reserved1 (.D(multiplexer_9_out_6), .C(TCK), .en(dtcms_wen), .Q(dtmcs[31:18]));

  assign E_DMI_BUSY = DMI_REQ;

  // Other names for the same wires on the sheet: dmi[40:0] = {DMI_ADDR, DMI_WDATA, DMI_OP}; dmi_busy = DMI_REQ;
  //   dmi_data[31:0] = DMI_WDATA; dmi_data_d[31:0] = DMI_RDATA; dmi_op_d[1:0] = DMI_STATUS;
  //   dtmcs_abits[5:0] = dtmcs[9:4]; dtmcs_dmihardreset = dtmcs[17]; dtmcs_dmireset = dtmcs[16];
  //   dtmcs[11:10] = E_DMISTAT; dtmcs_dmistat[1:0] = E_DMISTAT; dtmcs_idle[2:0] = dtmcs[14:12];
  //   dtmcs_reserved0 = dtmcs[15]; dtmcs_reserved1[13:0] = dtmcs[31:18]; dtmcs_version[3:0] = dtmcs[3:0];
  //   idcode_manufid[10:0] = idcode[11:1]; idcode_partnumber[15:0] = idcode[27:12]; idcode_reserved0 = idcode[0];
  //   idcode_version[3:0] = idcode[31:28]; dtmcs_dmistat_d[1:0] = E_STICKY_ERR; sticky_error[1:0] = E_STICKY_ERR

  // Notes on the sheet:
  //   ir register
  //   bypass register
  //   idcode register
  //   contents of state_lut (hex, n*v repeats v):
  //   1,0,1,2,a,3,4,0,5,6,5,6,7,9,7,8,5,9,1,2,b,c,b,c,d,f,d,e,b,f,1,2
  //   dmi register
  //   WHEN IN SHIFT-DR:
  //   TDI is shifted in from top every
  //   TCK when *_wen is high.
  //   WHEN NOT IN SHIFT-DR:
  //   Registers can be written
  //   independently when *_wen
  //   is high.
  //   dtcms register
  //   Todo:
  //   If dr-shift bit 17 is high and
  //   active IR is 0x10 and we're
  //   in Update DR,
  //   do a hard reset of the DMI.
  //   Here we are trying to make this circuit hierarchical
  //       RV5-REGS contains register bank related hw.
  //       RV5-ALU contains ALU related hw
  //       RV5-INSTR-DECODE contains Instruction Reg, and all needed decodes
  //             decoder for immediate sel
  //       RV5-IMM is a combinatorial that extracts the needed immediates, 
  //              and provides the sign-extended 32-bit value thru a MUX.
  //       RV5-PCU needs some fixes.
  //              increments the PC and allows Jumps, and provides next PC for JAL save of PC.
  //   See examples in Digital in particular processors as to how 
  //   to do this.  
  //   TODO: 
  //   1st. Add a test to each element in the hierarchy.
  //   2nd Resize boxes with appropriate SVG for readable packages w. appropriate signals.
  //   We need to:
  //       RV5-INSTR-DECODE: Decodes the instruction set and provides control signals, and FMT
  //            decode for immediate select has been completed.
  //       Implement:
  //            RV5-LOAD-STORE: Provides Load and Store
  //            RV5-MEMORY: Include ROM and RAM.
  //            RV5-IO: Provides a mean to read a program, communicate with a terminal (keyboard/display)
  //            Create a ROM/RAM  bootstrap
  //                 that loads a program.
  //   Note: Assembler test programs can be found at:   
  //      https://github.com/riscv-software-src/riscv-tests
  //   PCU (Program Control Unit, 
  //   PC = PC + 4, or PC = PC += SBimm32
  //   or PC = ALU out or PC += sgn_ext-imm32
  //   for FMT U, and UJ
  //   Need to figure out a way to load memory
  //   with instructions, ideally from RARS.
  //   Check out how MARS does it for MIPS.
  //   NEXT, NEED LOAD AND STORE,
  //   Address comes from ALU output
  //   which goes to memory via see-thru latch
  //    latch,which goes out to memory for 
  //   loading and storing.  reads 32-word
  //   and stores in rd.   Need to figure out a good
  //   approach to read and write to memory 
  //   with Digital and load it at start up.
  //   We need to arbitrate use of memory 
  //   between load/store and fetching instruction.
  //   RV5-DECODER:
  //      decodes: opcode, funct3, funct7
  //      generates: 
  //           # FMT - DO I NEED IT HERE?
  //           # imm_sel,  DONE ALREADY
  //           wen, 
  //           sub/add, 
  //           func_sel
endmodule
