// Digital circuit detrs.dig as structural Verilog
module detrs (
  input  set,
  input  reset,
  output O
);

  wire and_1_out, not_1_out;

  and and_1 (and_1_out, not_1_out, reset);
  not not_1 (not_1_out, set);
  RS_FF_AS rs_ff_as_1 (.S(set), .R(and_1_out), .Q(O));  // open: nQ
endmodule
